// Digital circuit 32regs.dig as structural Verilog
module _32regs (
  input  cl,
  input  [31:0] select,
  input  save_yn,
  input  [31:0] value,
  output [31:0] reg0,
  output [31:0] reg1,
  output [31:0] reg2,
  output [31:0] reg3,
  output [31:0] reg4,
  output [31:0] reg5,
  output [31:0] reg6,
  output [31:0] reg7,
  output [31:0] reg8,
  output [31:0] reg9,
  output [31:0] reg10,
  output [31:0] reg11,
  output [31:0] reg12,
  output [31:0] reg13,
  output [31:0] reg14,
  output [31:0] reg15,
  output [31:0] reg16,
  output [31:0] reg17,
  output [31:0] reg18,
  output [31:0] reg19,
  output [31:0] reg20,
  output [31:0] reg21,
  output [31:0] reg22,
  output [31:0] reg23,
  output [31:0] reg24,
  output [31:0] reg25,
  output [31:0] reg26,
  output [31:0] reg27,
  output [31:0] reg28,
  output [31:0] reg29,
  output [31:0] reg30,
  output [31:0] reg31
);

  wire and_1_out, decoder_1_out_0, decoder_1_out_1, decoder_1_out_2, decoder_1_out_3, decoder_1_out_4,
       decoder_1_out_5, decoder_1_out_6, decoder_1_out_7, decoder_1_out_8, decoder_1_out_9, decoder_1_out_10,
       decoder_1_out_11, decoder_1_out_12, decoder_1_out_13, decoder_1_out_14, decoder_1_out_15,
       decoder_1_out_16, decoder_1_out_17, decoder_1_out_18, decoder_1_out_19, decoder_1_out_20,
       decoder_1_out_21, decoder_1_out_22, decoder_1_out_23, decoder_1_out_24, decoder_1_out_25,
       decoder_1_out_26, decoder_1_out_27, decoder_1_out_28, decoder_1_out_29, decoder_1_out_30,
       decoder_1_out_31;
  wire [4:0] driver_1_out;

  assign driver_1_out = save_yn ? select[4:0] : 5'bz;  // Driver driver_1
  PullDown #(.Bits(5)) pulldown_1 (.out(driver_1_out));
  Decoder #(.Selector_Bits(5)) decoder_1 (
    .sel(driver_1_out), .out_0(decoder_1_out_0), .out_1(decoder_1_out_1), .out_2(decoder_1_out_2),
    .out_3(decoder_1_out_3), .out_4(decoder_1_out_4), .out_5(decoder_1_out_5), .out_6(decoder_1_out_6),
    .out_7(decoder_1_out_7), .out_8(decoder_1_out_8), .out_9(decoder_1_out_9), .out_10(decoder_1_out_10),
    .out_11(decoder_1_out_11), .out_12(decoder_1_out_12), .out_13(decoder_1_out_13),
    .out_14(decoder_1_out_14), .out_15(decoder_1_out_15), .out_16(decoder_1_out_16),
    .out_17(decoder_1_out_17), .out_18(decoder_1_out_18), .out_19(decoder_1_out_19),
    .out_20(decoder_1_out_20), .out_21(decoder_1_out_21), .out_22(decoder_1_out_22),
    .out_23(decoder_1_out_23), .out_24(decoder_1_out_24), .out_25(decoder_1_out_25),
    .out_26(decoder_1_out_26), .out_27(decoder_1_out_27), .out_28(decoder_1_out_28),
    .out_29(decoder_1_out_29), .out_30(decoder_1_out_30), .out_31(decoder_1_out_31));
  and and_1 (and_1_out, save_yn, decoder_1_out_0);
  Register #(.Bits(32)) register_1 (.D(value), .C(cl), .en(and_1_out), .Q(reg0));
  Register #(.Bits(32)) register_2 (.D(value), .C(cl), .en(decoder_1_out_1), .Q(reg1));
  Register #(.Bits(32)) register_3 (.D(value), .C(cl), .en(decoder_1_out_2), .Q(reg2));
  Register #(.Bits(32)) register_4 (.D(value), .C(cl), .en(decoder_1_out_3), .Q(reg3));
  Register #(.Bits(32)) register_5 (.D(value), .C(cl), .en(decoder_1_out_4), .Q(reg4));
  Register #(.Bits(32)) register_6 (.D(value), .C(cl), .en(decoder_1_out_5), .Q(reg5));
  Register #(.Bits(32)) register_7 (.D(value), .C(cl), .en(decoder_1_out_6), .Q(reg6));
  Register #(.Bits(32)) register_8 (.D(value), .C(cl), .en(decoder_1_out_7), .Q(reg7));
  Register #(.Bits(32)) register_9 (.D(value), .C(cl), .en(decoder_1_out_8), .Q(reg8));
  Register #(.Bits(32)) register_10 (.D(value), .C(cl), .en(decoder_1_out_9), .Q(reg9));
  Register #(.Bits(32)) register_11 (.D(value), .C(cl), .en(decoder_1_out_10), .Q(reg10));
  Register #(.Bits(32)) register_12 (.D(value), .C(cl), .en(decoder_1_out_11), .Q(reg11));
  Register #(.Bits(32)) register_13 (.D(value), .C(cl), .en(decoder_1_out_12), .Q(reg12));
  Register #(.Bits(32)) register_14 (.D(value), .C(cl), .en(decoder_1_out_13), .Q(reg13));
  Register #(.Bits(32)) register_15 (.D(value), .C(cl), .en(decoder_1_out_14), .Q(reg14));
  Register #(.Bits(32)) register_16 (.D(value), .C(cl), .en(decoder_1_out_15), .Q(reg15));
  Register #(.Bits(32)) register_17 (.D(value), .C(cl), .en(decoder_1_out_16), .Q(reg16));
  Register #(.Bits(32)) register_18 (.D(value), .C(cl), .en(decoder_1_out_17), .Q(reg17));
  Register #(.Bits(32)) register_19 (.D(value), .C(cl), .en(decoder_1_out_18), .Q(reg18));
  Register #(.Bits(32)) register_20 (.D(value), .C(cl), .en(decoder_1_out_19), .Q(reg19));
  Register #(.Bits(32)) register_21 (.D(value), .C(cl), .en(decoder_1_out_20), .Q(reg20));
  Register #(.Bits(32)) register_22 (.D(value), .C(cl), .en(decoder_1_out_21), .Q(reg21));
  Register #(.Bits(32)) register_23 (.D(value), .C(cl), .en(decoder_1_out_22), .Q(reg22));
  Register #(.Bits(32)) register_24 (.D(value), .C(cl), .en(decoder_1_out_23), .Q(reg23));
  Register #(.Bits(32)) register_25 (.D(value), .C(cl), .en(decoder_1_out_24), .Q(reg24));
  Register #(.Bits(32)) register_26 (.D(value), .C(cl), .en(decoder_1_out_25), .Q(reg25));
  Register #(.Bits(32)) register_27 (.D(value), .C(cl), .en(decoder_1_out_26), .Q(reg26));
  Register #(.Bits(32)) register_28 (.D(value), .C(cl), .en(decoder_1_out_27), .Q(reg27));
  Register #(.Bits(32)) register_29 (.D(value), .C(cl), .en(decoder_1_out_28), .Q(reg28));
  Register #(.Bits(32)) register_30 (.D(value), .C(cl), .en(decoder_1_out_29), .Q(reg29));
  Register #(.Bits(32)) register_31 (.D(value), .C(cl), .en(decoder_1_out_30), .Q(reg30));
  Register #(.Bits(32)) register_32 (.D(value), .C(cl), .en(decoder_1_out_31), .Q(reg31));
endmodule
