// Digital circuit ALU.dig as structural Verilog
module ALU (
  input  cl,
  input  [31:0] in0,
  input  [31:0] in1,
  input  [31:0] carryin,
  input  [7:0] instr0_7,
  input  instrbit9,
  input  pushoverwrite,
  input  popoverwrite,
  output [31:0] \output ,
  output [31:0] carry,
  output [31:0] stackeeh
);

  wire [31:0] arithmaticenginewithfloatt_1_carry, arithmaticenginewithfloatt_1_out, logicengine_1_y,
       shift_1_carry, shift_1_out;

  arithmaticenginewithfloatt arithmaticenginewithfloatt_1 (
    .in0(in0), .in1(in1), .carryin(carryin), .instr0_7(instr0_7), .instr9(instrbit9),
    .out(arithmaticenginewithfloatt_1_out), .carry(arithmaticenginewithfloatt_1_carry));
  logicengine logicengine_1 (.in0(in0), .in1(in1), .instr0_7(instr0_7), .Y(logicengine_1_y));
  shift shift_1 (
    .in0(in0), .in1(in1), .carryin(carryin), .instr0_7(instr0_7), .out(shift_1_out), .carry(shift_1_carry));
  Multiplexer #(.Bits(32)) multiplexer_1 (
    .sel(instr0_7[3]), .in_0(arithmaticenginewithfloatt_1_carry), .in_1(shift_1_carry), .out(carry));
  Multiplexer #(.Selector_Bits(2), .Bits(32)) multiplexer_2 (
    .sel(instr0_7[4:3]), .in_0({32{1'b0}}), .in_1(logicengine_1_y), .in_2(arithmaticenginewithfloatt_1_out),
    .in_3(shift_1_out), .out(\output ));

  assign stackeeh = {32{1'b0}};
endmodule
