// Digital circuit RAM.dig as structural Verilog
module RAM (
  input  cl,
  input  [31:0] dst,
  input  save_yn,
  input  [31:0] value,
  input  save_carry,
  input  [31:0] carry,
  input  [31:0] in_49,
  input  cl_doublespeed,
  output [31:0] reg0,
  output [31:0] reg1,
  output [31:0] reg2,
  output [31:0] reg3,
  output [31:0] reg4,
  output [31:0] reg5,
  output [31:0] reg6,
  output [31:0] reg7,
  output [31:0] reg8,
  output [31:0] reg9,
  output [31:0] reg10,
  output [31:0] reg11,
  output [31:0] reg12,
  output [31:0] reg13,
  output [31:0] reg14,
  output [31:0] reg15,
  output [31:0] reg16,
  output [31:0] reg17,
  output [31:0] reg18,
  output [31:0] reg19,
  output [31:0] reg20,
  output [31:0] reg21,
  output [31:0] reg22,
  output [31:0] reg23,
  output [31:0] reg24,
  output [31:0] reg25,
  output [31:0] reg26,
  output [31:0] reg27,
  output [31:0] reg28,
  output [31:0] reg29,
  output [31:0] reg30,
  output [31:0] reg31,
  output [31:0] carryo,
  output outputflag0,
  output [31:0] output0,
  output outputflag1,
  output [31:0] output1,
  output outputflag2,
  output [31:0] output2,
  output outputflag3,
  output [31:0] output3,
  output [31:0] counter,
  output [31:0] ram
);

  wire and_1_out, and_2_out, and_3_out, and_4_out, comparator_1_lt, comparator_2_eq, comparator_2_gt,
       comparator_2_lt, not_1_out, reset_1_out;
  wire [31:0] multiplexer_1_out;

  Comparator #(.Bits(32)) comparator_1 (.a(dst), .b(32'h20), .lt(comparator_1_lt));  // open: gt, eq
  Comparator #(.Bits(32)) comparator_2 (
    .a(dst), .b(32'h24), .gt(comparator_2_gt), .eq(comparator_2_eq), .lt(comparator_2_lt));
  and and_1 (and_1_out, ~comparator_1_lt, save_yn, comparator_2_lt, cl);  // And
  and and_2 (and_2_out, comparator_1_lt, save_yn);
  Multiplexer #(.Bits(32)) multiplexer_1 (.sel(not_1_out), .in_0(dst), .in_1(in_49), .out(multiplexer_1_out));
  not not_1 (not_1_out, cl);
  _32regs _32regs_1 (
    .cl(cl), .select(dst), .save_yn(and_2_out), .value(value), .reg0(reg0), .reg1(reg1), .reg2(reg2),
    .reg3(reg3), .reg4(reg4), .reg5(reg5), .reg6(reg6), .reg7(reg7), .reg8(reg8), .reg9(reg9), .reg10(reg10),
    .reg11(reg11), .reg12(reg12), .reg13(reg13), .reg14(reg14), .reg15(reg15), .reg16(reg16), .reg17(reg17),
    .reg18(reg18), .reg19(reg19), .reg20(reg20), .reg21(reg21), .reg22(reg22), .reg23(reg23), .reg24(reg24),
    .reg25(reg25), .reg26(reg26), .reg27(reg27), .reg28(reg28), .reg29(reg29), .reg30(reg30), .reg31(reg31));
  and and_3 (and_3_out, comparator_2_eq, save_yn);
  and and_4 (and_4_out, cl, save_yn, comparator_2_gt);
  Register #(.Bits(32)) register_1 (.D(carry), .C(cl), .en(save_carry), .Q(carryo));
  Demultiplexer #(.Selector_Bits(2), .Bits(32)) demultiplexer_1 (
    .sel(dst[1:0]), .in(value), .out_0(output0), .out_1(output1), .out_2(output2), .out_3(output3));
  Demultiplexer #(.Selector_Bits(2)) demultiplexer_2 (
    .sel(dst[1:0]), .in(and_1_out), .out_0(outputflag0), .out_1(outputflag1), .out_2(outputflag2),
    .out_3(outputflag3));
  CounterPreset #(.Bits(32)) counterpreset_1 (
    .en(1'b1), .C(~cl), .dir(1'b0), .in(value), .ld(and_3_out), .clr(reset_1_out), .out(counter));  // open: ovf
  Reset #(.invertOutput("false")) reset_1 (.out(reset_1_out));
  RAMDualAccess #(.AddrBits(24), .Bits(32)) ramdualaccess_1 (
    .str(and_4_out), .C(cl_doublespeed), .ld(1'b1), .A1(multiplexer_1_out[23:0]), .Din1(value),
    .A2({24{1'b0}}), .D1(ram));  // open: D2

  // Notes on the sheet:
  //   cl_doublespeed: default 1
endmodule
