// Digital circuit arithmaticengine.dig as structural Verilog
module arithmaticengine (
  input  [31:0] in0,
  input  [31:0] in1,
  input  [31:0] carryin,
  input  [7:0] instr0_7,
  input  instr9,
  output [31:0] out,
  output [31:0] carry
);

  wire and_1_out;
  wire [0:0] add_1_c_o, add_2_c_o, sub_1_c_o, sub_2_c_o;
  wire [31:0] add_1_s, add_2_s, div_1_q, div_1_r, multiplexer_1_out, multiplexer_2_out, sub_1_s, sub_2_s;
  wire [63:0] mul_1_mul;

  and and_1 (and_1_out, carryin[0], instr0_7[0]);
  Add #(.Bits(32)) add_1 (.a(in0), .b(in1), .c_i(and_1_out), .s(add_1_s), .c_o(add_1_c_o[0]));
  Sub #(.Bits(32)) sub_1 (.a(in0), .b(in1), .c_i(and_1_out), .s(sub_1_s), .c_o(sub_1_c_o[0]));
  Mul #(.Signed("true"), .Bits(32)) mul_1 (.a(in0), .b(in1), .mul(mul_1_mul));
  Div #(.remainderPositive("false"), .Signed("true"), .Bits(32)) div_1 (.a(in0), .b(in1), .q(div_1_q), .r(div_1_r));
  Add #(.Bits(32)) add_2 (.a(in0), .b(32'h1), .c_i(1'b0), .s(add_2_s), .c_o(add_2_c_o[0]));
  Sub #(.Bits(32)) sub_2 (.a(in0), .b(32'h1), .c_i(1'b0), .s(sub_2_s), .c_o(sub_2_c_o[0]));
  Multiplexer #(.Selector_Bits(3), .Bits(32)) multiplexer_1 (
    .sel(instr0_7[2:0]), .in_0(add_1_s), .in_1(add_1_s), .in_2(sub_1_s), .in_3(sub_1_s),
    .in_4(mul_1_mul[31:0]), .in_5(div_1_q), .in_6(add_2_s), .in_7(sub_2_s), .out(multiplexer_1_out));
  Multiplexer #(.Selector_Bits(3), .Bits(32)) multiplexer_2 (
    .sel(instr0_7[2:0]), .in_0({{31{1'b0}}, add_1_c_o[0]}), .in_1({{31{1'b0}}, add_1_c_o[0]}),
    .in_2({{31{1'b0}}, sub_1_c_o[0]}), .in_3({{31{1'b0}}, sub_1_c_o[0]}), .in_4(mul_1_mul[63:32]),
    .in_5(div_1_r), .in_6({{31{1'b0}}, add_2_c_o[0]}), .in_7({{31{1'b0}}, sub_2_c_o[0]}),
    .out(multiplexer_2_out));
  Multiplexer #(.Bits(32)) multiplexer_3 (.sel(instr9), .in_0(multiplexer_2_out), .in_1({32{1'b0}}), .out(carry));
  Multiplexer #(.Bits(32)) multiplexer_4 (.sel(instr9), .in_0(multiplexer_1_out), .in_1(in0), .out(out));
endmodule
