// Digital circuit arithmaticenginewithfloatt.dig as structural Verilog
module arithmaticenginewithfloatt (
  input  [31:0] in0,
  input  [31:0] in1,
  input  [31:0] carryin,
  input  [7:0] instr0_7,
  input  instr9,
  output [31:0] out,
  output [31:0] carry
);

  wire and_1_out, demultiplexer_1_out_0, demultiplexer_1_out_1, demultiplexer_1_out_2, demultiplexer_1_out_3,
       demultiplexer_1_out_4, demultiplexer_1_out_5;
  wire [0:0] add_1_c_o, add_2_c_o, sub_1_c_o, sub_2_c_o;
  wire [31:0] add_1_s, add_2_s, div_1_q, div_1_r, driver_1_out, driver_2_out, driver_3_out, driver_4_out,
       driver_5_out, driver_6_out, driver_7_out, driver_8_out, driver_9_out, driver_10_out,
       floataddermetedgecases_1_out, floataddermetedgecases_2_out, floatdivwithedgecases_1_out,
       floatmultwithedgecases_1_out, ftoint_1_o, inttoff_1_o, multiplexer_1_out, multiplexer_2_out,
       multiplexer_3_out, sub_1_s, sub_2_s;
  wire [31:31] not_1_out;
  wire [63:0] mul_1_mul;

  and and_1 (and_1_out, carryin[0], instr0_7[0]);
  Demultiplexer #(.Selector_Bits(3)) demultiplexer_1 (
    .sel(instr0_7[2:0]), .in(instr9), .out_0(demultiplexer_1_out_0), .out_1(demultiplexer_1_out_1),
    .out_2(demultiplexer_1_out_2), .out_3(demultiplexer_1_out_3), .out_4(demultiplexer_1_out_4),
    .out_5(demultiplexer_1_out_5));  // open: out_6, out_7
  Add #(.Bits(32)) add_1 (.a(in0), .b(in1), .c_i(and_1_out), .s(add_1_s), .c_o(add_1_c_o[0]));
  Sub #(.Bits(32)) sub_1 (.a(in0), .b(in1), .c_i(and_1_out), .s(sub_1_s), .c_o(sub_1_c_o[0]));
  Mul #(.Signed("true"), .Bits(32)) mul_1 (.a(in0), .b(in1), .mul(mul_1_mul));
  Div #(.remainderPositive("false"), .Signed("true"), .Bits(32)) div_1 (.a(in0), .b(in1), .q(div_1_q), .r(div_1_r));
  Add #(.Bits(32)) add_2 (.a(in0), .b(32'h1), .c_i(1'b0), .s(add_2_s), .c_o(add_2_c_o[0]));
  Sub #(.Bits(32)) sub_2 (.a(in0), .b(32'h1), .c_i(1'b0), .s(sub_2_s), .c_o(sub_2_c_o[0]));
  assign driver_1_out = demultiplexer_1_out_0 ? in0 : 32'bz;  // Driver driver_1
  assign driver_2_out = demultiplexer_1_out_1 ? in0 : 32'bz;  // Driver driver_2
  assign driver_3_out = demultiplexer_1_out_1 ? in1 : 32'bz;  // Driver driver_3
  assign driver_4_out = demultiplexer_1_out_2 ? in0 : 32'bz;  // Driver driver_4
  assign driver_5_out = demultiplexer_1_out_2 ? in1 : 32'bz;  // Driver driver_5
  assign driver_6_out = demultiplexer_1_out_3 ? in0 : 32'bz;  // Driver driver_6
  assign driver_7_out = demultiplexer_1_out_3 ? in1 : 32'bz;  // Driver driver_7
  assign driver_8_out = demultiplexer_1_out_4 ? in0 : 32'bz;  // Driver driver_8
  assign driver_9_out = demultiplexer_1_out_5 ? in0 : 32'bz;  // Driver driver_9
  assign driver_10_out = demultiplexer_1_out_0 ? in1 : 32'bz;  // Driver driver_10
  not not_1 (not_1_out[31], driver_3_out[31]);
  PullDown #(.Bits(32)) pulldown_1 (.out(driver_4_out));
  PullDown #(.Bits(32)) pulldown_2 (.out(driver_5_out));
  PullDown #(.Bits(32)) pulldown_3 (.out(driver_6_out));
  PullDown #(.Bits(32)) pulldown_4 (.out(driver_7_out));
  PullDown #(.Bits(32)) pulldown_5 (.out(driver_8_out));
  PullDown #(.Bits(32)) pulldown_6 (.out(driver_9_out));
  PullDown #(.Bits(32)) pulldown_7 (.out(driver_1_out));
  PullDown #(.Bits(32)) pulldown_8 (.out(driver_10_out));
  PullDown #(.Bits(32)) pulldown_9 (.out(driver_2_out));
  PullDown #(.Bits(32)) pulldown_10 (.out(driver_3_out));
  floataddermetedgecases floataddermetedgecases_1 (
    .in0(driver_1_out), .in1(driver_10_out), .out(floataddermetedgecases_1_out));
  floataddermetedgecases floataddermetedgecases_2 (
    .in0(driver_2_out), .in1({not_1_out[31], driver_3_out[30:0]}), .out(floataddermetedgecases_2_out));
  floatmultwithedgecases floatmultwithedgecases_1 (
    .in0(driver_4_out), .in1(driver_5_out), .out(floatmultwithedgecases_1_out));
  floatdivwithedgecases floatdivwithedgecases_1 (
    .in0(driver_6_out), .in1(driver_7_out), .out(floatdivwithedgecases_1_out));
  ftoint ftoint_1 (.m(driver_8_out[22:0]), .e(driver_8_out[30:23]), .s(driver_8_out[31]), .o(ftoint_1_o));
  inttoff inttoff_1 (.i(driver_9_out), .o(inttoff_1_o));
  Multiplexer #(.Selector_Bits(3), .Bits(32)) multiplexer_1 (
    .sel(instr0_7[2:0]), .in_0(add_1_s), .in_1(add_1_s), .in_2(sub_1_s), .in_3(sub_1_s),
    .in_4(mul_1_mul[31:0]), .in_5(div_1_q), .in_6(add_2_s), .in_7(sub_2_s), .out(multiplexer_1_out));
  Multiplexer #(.Selector_Bits(3), .Bits(32)) multiplexer_2 (
    .sel(instr0_7[2:0]), .in_0({{31{1'b0}}, add_1_c_o[0]}), .in_1({{31{1'b0}}, add_1_c_o[0]}),
    .in_2({{31{1'b0}}, sub_1_c_o[0]}), .in_3({{31{1'b0}}, sub_1_c_o[0]}), .in_4(mul_1_mul[63:32]),
    .in_5(div_1_r), .in_6({{31{1'b0}}, add_2_c_o[0]}), .in_7({{31{1'b0}}, sub_2_c_o[0]}),
    .out(multiplexer_2_out));
  Multiplexer #(.Selector_Bits(3), .Bits(32)) multiplexer_3 (
    .sel(instr0_7[2:0]), .in_0(floataddermetedgecases_1_out), .in_1(floataddermetedgecases_2_out),
    .in_2(floatmultwithedgecases_1_out), .in_3(floatdivwithedgecases_1_out), .in_4(ftoint_1_o),
    .in_5(inttoff_1_o), .in_6({32{1'b0}}), .in_7({32{1'b0}}), .out(multiplexer_3_out));
  Multiplexer #(.Bits(32)) multiplexer_4 (.sel(instr9), .in_0(multiplexer_2_out), .in_1({32{1'b0}}), .out(carry));
  Multiplexer #(.Bits(32)) multiplexer_5 (.sel(instr9), .in_0(multiplexer_1_out), .in_1(multiplexer_3_out), .out(out));
endmodule
