// Digital circuit comparison.dig as structural Verilog
module comparison (
  input  [31:0] in0,
  input  [31:0] in1,
  input  [7:0] instr0_7,
  input  instr8,
  input  instr9,
  input  instr11,
  input  interrupt,
  output out
);

  wire and_1_out, and_2_out, and_3_out, and_4_out, and_5_out, and_6_out, and_7_out, comparator_1_eq,
       comparator_1_gt, comparator_1_lt, comparator_2_eq, comparator_2_gt, comparator_2_lt,
       multiplexer_1_out, multiplexer_2_out, or_1_out, or_2_out;

  Comparator #(.Signed("true"), .Bits(32)) comparator_1 (
    .a(in0), .b(in1), .gt(comparator_1_gt), .eq(comparator_1_eq), .lt(comparator_1_lt));
  Comparator #(.Bits(32)) comparator_2 (
    .a(in0), .b(in1), .gt(comparator_2_gt), .eq(comparator_2_eq), .lt(comparator_2_lt));
  and and_1 (and_1_out, instr0_7[0], comparator_1_gt);
  and and_2 (and_2_out, instr0_7[1], comparator_1_eq);
  and and_3 (and_3_out, instr0_7[2], comparator_1_lt);
  and and_4 (and_4_out, comparator_2_gt, instr0_7[0]);
  and and_5 (and_5_out, comparator_2_eq, instr0_7[1]);
  and and_6 (and_6_out, comparator_2_lt, instr0_7[2]);
  or or_1 (or_1_out, and_1_out, and_2_out, and_3_out);
  or or_2 (or_2_out, and_4_out, and_5_out, and_6_out);
  Multiplexer multiplexer_1 (.sel(instr8), .in_0(or_1_out), .in_1(or_2_out), .out(multiplexer_1_out));
  Multiplexer multiplexer_2 (.sel(instr9), .in_0(multiplexer_1_out), .in_1(1'b0), .out(multiplexer_2_out));
  and and_7 (and_7_out, multiplexer_2_out, interrupt);
  Multiplexer multiplexer_3 (.sel(instr11), .in_0(multiplexer_2_out), .in_1(and_7_out), .out(out));
endmodule
