// Digital circuit div.dig as structural Verilog
module div (
  input  [23:0] in0,
  input  [23:0] in1,
  output [47:0] out
);

  wire sub_1_c_o, sub_2_c_o, sub_3_c_o, sub_4_c_o, sub_5_c_o, sub_6_c_o, sub_7_c_o, sub_8_c_o, sub_9_c_o,
       sub_10_c_o, sub_11_c_o, sub_12_c_o, sub_13_c_o, sub_14_c_o, sub_15_c_o, sub_16_c_o, sub_17_c_o,
       sub_18_c_o, sub_19_c_o, sub_20_c_o, sub_21_c_o, sub_22_c_o, sub_23_c_o, sub_24_c_o;
  wire [23:0] div_1_r;
  wire [24:0] sub_1_s;
  wire [25:0] sub_2_s;
  wire [25:1] multiplexer_1_out;
  wire [26:0] sub_3_s;
  wire [26:1] multiplexer_2_out;
  wire [27:0] sub_4_s;
  wire [27:1] multiplexer_3_out;
  wire [28:0] sub_5_s;
  wire [28:1] multiplexer_4_out;
  wire [29:0] sub_6_s;
  wire [29:1] multiplexer_5_out;
  wire [30:0] sub_7_s;
  wire [30:1] multiplexer_6_out;
  wire [31:0] sub_8_s;
  wire [31:1] multiplexer_7_out;
  wire [32:0] sub_9_s;
  wire [32:1] multiplexer_8_out;
  wire [33:0] sub_10_s;
  wire [33:1] multiplexer_9_out;
  wire [34:0] sub_11_s;
  wire [34:1] multiplexer_10_out;
  wire [35:0] sub_12_s;
  wire [35:1] multiplexer_11_out;
  wire [36:0] sub_13_s;
  wire [36:1] multiplexer_12_out;
  wire [37:0] sub_14_s;
  wire [37:1] multiplexer_13_out;
  wire [38:0] sub_15_s;
  wire [38:1] multiplexer_14_out;
  wire [39:0] sub_16_s;
  wire [39:1] multiplexer_15_out;
  wire [40:0] sub_17_s;
  wire [40:1] multiplexer_16_out;
  wire [41:0] sub_18_s;
  wire [41:1] multiplexer_17_out;
  wire [42:0] sub_19_s;
  wire [42:1] multiplexer_18_out;
  wire [43:0] sub_20_s;
  wire [43:1] multiplexer_19_out;
  wire [44:0] sub_21_s;
  wire [44:1] multiplexer_20_out;
  wire [45:0] sub_22_s;
  wire [45:1] multiplexer_21_out;
  wire [46:0] sub_23_s;
  wire [46:1] multiplexer_22_out;
  wire [47:1] multiplexer_23_out;

  Div #(.Bits(24)) div_1 (.a(in0), .b(in1), .q(out[47:24]), .r(div_1_r));
  Sub #(.Bits(25)) sub_1 (.a({div_1_r, 1'b0}), .b({1'b0, in1}), .c_i(1'b0), .s(sub_1_s), .c_o(sub_1_c_o));
  Multiplexer #(.Bits(25)) multiplexer_1 (
    .sel(sub_1_c_o), .in_0(sub_1_s), .in_1({div_1_r, 1'b0}), .out(multiplexer_1_out));
  Sub #(.Bits(26)) sub_2 (.a({multiplexer_1_out, 1'b0}), .b({2'b00, in1}), .c_i(1'b0), .s(sub_2_s), .c_o(sub_2_c_o));
  Multiplexer #(.Bits(26)) multiplexer_2 (
    .sel(sub_2_c_o), .in_0(sub_2_s), .in_1({multiplexer_1_out, 1'b0}), .out(multiplexer_2_out));
  Sub #(.Bits(27)) sub_3 (.a({multiplexer_2_out, 1'b0}), .b({3'b000, in1}), .c_i(1'b0), .s(sub_3_s), .c_o(sub_3_c_o));
  Multiplexer #(.Bits(27)) multiplexer_3 (
    .sel(sub_3_c_o), .in_0(sub_3_s), .in_1({multiplexer_2_out, 1'b0}), .out(multiplexer_3_out));
  Sub #(.Bits(28)) sub_4 (.a({multiplexer_3_out, 1'b0}), .b({4'b0000, in1}), .c_i(1'b0), .s(sub_4_s), .c_o(sub_4_c_o));
  Multiplexer #(.Bits(28)) multiplexer_4 (
    .sel(sub_4_c_o), .in_0(sub_4_s), .in_1({multiplexer_3_out, 1'b0}), .out(multiplexer_4_out));
  Sub #(.Bits(29)) sub_5 (
    .a({multiplexer_4_out, 1'b0}), .b({{5{1'b0}}, in1}), .c_i(1'b0), .s(sub_5_s), .c_o(sub_5_c_o));
  Multiplexer #(.Bits(29)) multiplexer_5 (
    .sel(sub_5_c_o), .in_0(sub_5_s), .in_1({multiplexer_4_out, 1'b0}), .out(multiplexer_5_out));
  Sub #(.Bits(30)) sub_6 (
    .a({multiplexer_5_out, 1'b0}), .b({{6{1'b0}}, in1}), .c_i(1'b0), .s(sub_6_s), .c_o(sub_6_c_o));
  Multiplexer #(.Bits(30)) multiplexer_6 (
    .sel(sub_6_c_o), .in_0(sub_6_s), .in_1({multiplexer_5_out, 1'b0}), .out(multiplexer_6_out));
  Sub #(.Bits(31)) sub_7 (
    .a({multiplexer_6_out, 1'b0}), .b({{7{1'b0}}, in1}), .c_i(1'b0), .s(sub_7_s), .c_o(sub_7_c_o));
  Multiplexer #(.Bits(31)) multiplexer_7 (
    .sel(sub_7_c_o), .in_0(sub_7_s), .in_1({multiplexer_6_out, 1'b0}), .out(multiplexer_7_out));
  Sub #(.Bits(32)) sub_8 (
    .a({multiplexer_7_out, 1'b0}), .b({{8{1'b0}}, in1}), .c_i(1'b0), .s(sub_8_s), .c_o(sub_8_c_o));
  Multiplexer #(.Bits(32)) multiplexer_8 (
    .sel(sub_8_c_o), .in_0(sub_8_s), .in_1({multiplexer_7_out, 1'b0}), .out(multiplexer_8_out));
  Sub #(.Bits(33)) sub_9 (
    .a({multiplexer_8_out, 1'b0}), .b({{9{1'b0}}, in1}), .c_i(1'b0), .s(sub_9_s), .c_o(sub_9_c_o));
  Multiplexer #(.Bits(33)) multiplexer_9 (
    .sel(sub_9_c_o), .in_0(sub_9_s), .in_1({multiplexer_8_out, 1'b0}), .out(multiplexer_9_out));
  Sub #(.Bits(34)) sub_10 (
    .a({multiplexer_9_out, 1'b0}), .b({{10{1'b0}}, in1}), .c_i(1'b0), .s(sub_10_s), .c_o(sub_10_c_o));
  Multiplexer #(.Bits(34)) multiplexer_10 (
    .sel(sub_10_c_o), .in_0(sub_10_s), .in_1({multiplexer_9_out, 1'b0}), .out(multiplexer_10_out));
  Sub #(.Bits(35)) sub_11 (
    .a({multiplexer_10_out, 1'b0}), .b({{11{1'b0}}, in1}), .c_i(1'b0), .s(sub_11_s), .c_o(sub_11_c_o));
  Multiplexer #(.Bits(35)) multiplexer_11 (
    .sel(sub_11_c_o), .in_0(sub_11_s), .in_1({multiplexer_10_out, 1'b0}), .out(multiplexer_11_out));
  Sub #(.Bits(36)) sub_12 (
    .a({multiplexer_11_out, 1'b0}), .b({{12{1'b0}}, in1}), .c_i(1'b0), .s(sub_12_s), .c_o(sub_12_c_o));
  Multiplexer #(.Bits(36)) multiplexer_12 (
    .sel(sub_12_c_o), .in_0(sub_12_s), .in_1({multiplexer_11_out, 1'b0}), .out(multiplexer_12_out));
  Sub #(.Bits(37)) sub_13 (
    .a({multiplexer_12_out, 1'b0}), .b({{13{1'b0}}, in1}), .c_i(1'b0), .s(sub_13_s), .c_o(sub_13_c_o));
  Multiplexer #(.Bits(37)) multiplexer_13 (
    .sel(sub_13_c_o), .in_0(sub_13_s), .in_1({multiplexer_12_out, 1'b0}), .out(multiplexer_13_out));
  Sub #(.Bits(38)) sub_14 (
    .a({multiplexer_13_out, 1'b0}), .b({{14{1'b0}}, in1}), .c_i(1'b0), .s(sub_14_s), .c_o(sub_14_c_o));
  Multiplexer #(.Bits(38)) multiplexer_14 (
    .sel(sub_14_c_o), .in_0(sub_14_s), .in_1({multiplexer_13_out, 1'b0}), .out(multiplexer_14_out));
  Sub #(.Bits(39)) sub_15 (
    .a({multiplexer_14_out, 1'b0}), .b({{15{1'b0}}, in1}), .c_i(1'b0), .s(sub_15_s), .c_o(sub_15_c_o));
  Multiplexer #(.Bits(39)) multiplexer_15 (
    .sel(sub_15_c_o), .in_0(sub_15_s), .in_1({multiplexer_14_out, 1'b0}), .out(multiplexer_15_out));
  Sub #(.Bits(40)) sub_16 (
    .a({multiplexer_15_out, 1'b0}), .b({{16{1'b0}}, in1}), .c_i(1'b0), .s(sub_16_s), .c_o(sub_16_c_o));
  Multiplexer #(.Bits(40)) multiplexer_16 (
    .sel(sub_16_c_o), .in_0(sub_16_s), .in_1({multiplexer_15_out, 1'b0}), .out(multiplexer_16_out));
  Sub #(.Bits(41)) sub_17 (
    .a({multiplexer_16_out, 1'b0}), .b({{17{1'b0}}, in1}), .c_i(1'b0), .s(sub_17_s), .c_o(sub_17_c_o));
  Multiplexer #(.Bits(41)) multiplexer_17 (
    .sel(sub_17_c_o), .in_0(sub_17_s), .in_1({multiplexer_16_out, 1'b0}), .out(multiplexer_17_out));
  Sub #(.Bits(42)) sub_18 (
    .a({multiplexer_17_out, 1'b0}), .b({{18{1'b0}}, in1}), .c_i(1'b0), .s(sub_18_s), .c_o(sub_18_c_o));
  Multiplexer #(.Bits(42)) multiplexer_18 (
    .sel(sub_18_c_o), .in_0(sub_18_s), .in_1({multiplexer_17_out, 1'b0}), .out(multiplexer_18_out));
  Sub #(.Bits(43)) sub_19 (
    .a({multiplexer_18_out, 1'b0}), .b({{19{1'b0}}, in1}), .c_i(1'b0), .s(sub_19_s), .c_o(sub_19_c_o));
  Multiplexer #(.Bits(43)) multiplexer_19 (
    .sel(sub_19_c_o), .in_0(sub_19_s), .in_1({multiplexer_18_out, 1'b0}), .out(multiplexer_19_out));
  Sub #(.Bits(44)) sub_20 (
    .a({multiplexer_19_out, 1'b0}), .b({{20{1'b0}}, in1}), .c_i(1'b0), .s(sub_20_s), .c_o(sub_20_c_o));
  Multiplexer #(.Bits(44)) multiplexer_20 (
    .sel(sub_20_c_o), .in_0(sub_20_s), .in_1({multiplexer_19_out, 1'b0}), .out(multiplexer_20_out));
  Sub #(.Bits(45)) sub_21 (
    .a({multiplexer_20_out, 1'b0}), .b({{21{1'b0}}, in1}), .c_i(1'b0), .s(sub_21_s), .c_o(sub_21_c_o));
  Multiplexer #(.Bits(45)) multiplexer_21 (
    .sel(sub_21_c_o), .in_0(sub_21_s), .in_1({multiplexer_20_out, 1'b0}), .out(multiplexer_21_out));
  Sub #(.Bits(46)) sub_22 (
    .a({multiplexer_21_out, 1'b0}), .b({{22{1'b0}}, in1}), .c_i(1'b0), .s(sub_22_s), .c_o(sub_22_c_o));
  Multiplexer #(.Bits(46)) multiplexer_22 (
    .sel(sub_22_c_o), .in_0(sub_22_s), .in_1({multiplexer_21_out, 1'b0}), .out(multiplexer_22_out));
  Sub #(.Bits(47)) sub_23 (
    .a({multiplexer_22_out, 1'b0}), .b({{23{1'b0}}, in1}), .c_i(1'b0), .s(sub_23_s), .c_o(sub_23_c_o));
  Multiplexer #(.Bits(47)) multiplexer_23 (
    .sel(sub_23_c_o), .in_0(sub_23_s), .in_1({multiplexer_22_out, 1'b0}), .out(multiplexer_23_out));
  Sub #(.Bits(48)) sub_24 (
    .a({multiplexer_23_out, 1'b0}), .b({{24{1'b0}}, in1}), .c_i(1'b0), .c_o(sub_24_c_o));  // open: s
  not not_1 (out[23], sub_1_c_o);
  not not_2 (out[22], sub_2_c_o);
  not not_3 (out[21], sub_3_c_o);
  not not_4 (out[20], sub_4_c_o);
  not not_5 (out[19], sub_5_c_o);
  not not_6 (out[18], sub_6_c_o);
  not not_7 (out[17], sub_7_c_o);
  not not_8 (out[16], sub_8_c_o);
  not not_9 (out[15], sub_9_c_o);
  not not_10 (out[14], sub_10_c_o);
  not not_11 (out[13], sub_11_c_o);
  not not_12 (out[12], sub_12_c_o);
  not not_13 (out[11], sub_13_c_o);
  not not_14 (out[10], sub_14_c_o);
  not not_15 (out[9], sub_15_c_o);
  not not_16 (out[8], sub_16_c_o);
  not not_17 (out[7], sub_17_c_o);
  not not_18 (out[6], sub_18_c_o);
  not not_19 (out[5], sub_19_c_o);
  not not_20 (out[4], sub_20_c_o);
  not not_21 (out[3], sub_21_c_o);
  not not_22 (out[2], sub_22_c_o);
  not not_23 (out[1], sub_23_c_o);
  not not_24 (out[0], sub_24_c_o);
endmodule
