// Digital circuit floatadder.dig as structural Verilog
module floatadder (
  input  [22:0] m0,
  input  [22:0] m1,
  input  [7:0] e0,
  input  [7:0] e1,
  input  s0,
  input  s1,
  output [22:0] m,
  output [7:0] e,
  output s
);

  wire and_1_out, comparator_1_gt, comparator_1_lt, comparator_2_gt, comparator_2_lt, comparator_3_lt,
       comparator_4_eq, comparator_5_eq, multiplexer_3_out, multiplexer_4_out, nor_1_out, or_3_out, or_4_out,
       sub_1_c_o, sub_4_c_o, xor_1_out;
  wire [4:0] priorityencoder_1_num, sub_3_s;
  wire [5:5] sub_3_c_o;
  wire [7:0] add_1_s, add_3_s, bitextender_1_out, multiplexer_1_out, multiplexer_7_out, not_1_out, sub_1_s,
       sub_4_s;
  wire [23:0] add_2_s, barrelshifter_1_out, multiplexer_2_out, multiplexer_5_out, multiplexer_6_out,
       multiplexer_8_out, multiplexer_9_out, sub_2_s;
  wire [23:23] or_1_out, or_2_out;
  wire [24:0] barrelshifter_2_out, barrelshifter_3_out, multiplexer_11_out, multiplexer_12_out;
  wire [24:23] multiplexer_14_out;
  wire [24:24] add_2_c_o, sub_2_c_o;

  nor nor_1 (nor_1_out, or_2_out[23], or_1_out[23]);
  Comparator #(.Bits(8)) comparator_1 (.a({8{1'b0}}), .b(e0), .gt(comparator_1_gt), .lt(comparator_1_lt));  // open: eq
  Comparator #(.Bits(8)) comparator_2 (.a(e1), .b({8{1'b0}}), .gt(comparator_2_gt), .lt(comparator_2_lt));  // open: eq
  or or_1 (or_1_out[23], comparator_1_gt, comparator_1_lt);
  or or_2 (or_2_out[23], comparator_2_gt, comparator_2_lt);
  xor xor_1 (xor_1_out, s0, s1);
  Multiplexer #(.Bits(8)) multiplexer_1 (.sel(sub_1_c_o), .in_0(e0), .in_1(e1), .out(multiplexer_1_out));
  Sub #(.Bits(8)) sub_1 (.a(e0), .b(e1), .c_i(1'b0), .s(sub_1_s), .c_o(sub_1_c_o));
  Multiplexer #(.Bits(24)) multiplexer_2 (
    .sel(sub_1_c_o), .in_0({or_2_out[23], m1}), .in_1({or_1_out[23], m0}), .out(multiplexer_2_out));
  Multiplexer multiplexer_3 (.sel(sub_1_c_o), .in_0(s0), .in_1(s1), .out(multiplexer_3_out));
  Multiplexer multiplexer_4 (.sel(sub_1_c_o), .in_0(s1), .in_1(s0), .out(multiplexer_4_out));
  Multiplexer #(.Bits(24)) multiplexer_5 (
    .sel(sub_1_c_o), .in_0({or_1_out[23], m0}), .in_1({or_2_out[23], m1}), .out(multiplexer_5_out));
  assign not_1_out = ~sub_1_s;  // Not not_1, 8 bits wide
  Add #(.Bits(8)) add_1 (.a(not_1_out), .b({8{1'b0}}), .c_i(1'b1), .s(add_1_s));  // open: c_o
  Multiplexer #(.Bits(24)) multiplexer_6 (
    .sel(or_3_out), .in_0(multiplexer_2_out), .in_1({24{1'b0}}), .out(multiplexer_6_out));
  Multiplexer #(.Bits(8)) multiplexer_7 (.sel(sub_1_c_o), .in_0(sub_1_s), .in_1(add_1_s), .out(multiplexer_7_out));
  BarrelShifter #(.Bits(24), .direction("right")) barrelshifter_1 (
    .in(multiplexer_6_out), .shift(multiplexer_7_out[4:0]), .out(barrelshifter_1_out));
  or or_3 (or_3_out, multiplexer_7_out[5], multiplexer_7_out[6], multiplexer_7_out[7]);
  Comparator #(.Bits(24)) comparator_3 (
    .a(multiplexer_5_out), .b(barrelshifter_1_out), .lt(comparator_3_lt));  // open: gt, eq
  Multiplexer #(.Bits(24)) multiplexer_8 (
    .sel(comparator_3_lt), .in_0(multiplexer_5_out), .in_1(barrelshifter_1_out), .out(multiplexer_8_out));
  Multiplexer #(.Bits(24)) multiplexer_9 (
    .sel(comparator_3_lt), .in_0(barrelshifter_1_out), .in_1(multiplexer_5_out), .out(multiplexer_9_out));
  Multiplexer multiplexer_10 (.sel(comparator_3_lt), .in_0(multiplexer_3_out), .in_1(multiplexer_4_out), .out(s));
  Add #(.Bits(24)) add_2 (.a(multiplexer_5_out), .b(barrelshifter_1_out), .c_i(1'b0), .s(add_2_s), .c_o(add_2_c_o[24]));
  Sub #(.Bits(24)) sub_2 (.a(multiplexer_8_out), .b(multiplexer_9_out), .c_i(1'b0), .s(sub_2_s), .c_o(sub_2_c_o[24]));
  Multiplexer #(.Bits(25)) multiplexer_11 (
    .sel(xor_1_out), .in_0({add_2_c_o[24], add_2_s}), .in_1({sub_2_c_o[24], sub_2_s}),
    .out(multiplexer_11_out));
  PriorityEncoder #(.Selector_Bits(5)) priorityencoder_1 (
    .in0(multiplexer_11_out[0]), .in1(multiplexer_11_out[1]), .in2(multiplexer_11_out[2]),
    .in3(multiplexer_11_out[3]), .in4(multiplexer_11_out[4]), .in5(multiplexer_11_out[5]),
    .in6(multiplexer_11_out[6]), .in7(multiplexer_11_out[7]), .in8(multiplexer_11_out[8]),
    .in9(multiplexer_11_out[9]), .in10(multiplexer_11_out[10]), .in11(multiplexer_11_out[11]),
    .in12(multiplexer_11_out[12]), .in13(multiplexer_11_out[13]), .in14(multiplexer_11_out[14]),
    .in15(multiplexer_11_out[15]), .in16(multiplexer_11_out[16]), .in17(multiplexer_11_out[17]),
    .in18(multiplexer_11_out[18]), .in19(multiplexer_11_out[19]), .in20(multiplexer_11_out[20]),
    .in21(multiplexer_11_out[21]), .in22(multiplexer_11_out[22]), .in23(multiplexer_11_out[23]),
    .in24(multiplexer_11_out[24]), .in25(1'b0), .in26(1'b0), .in27(1'b0), .in28(1'b0), .in29(1'b0),
    .in30(1'b0), .in31(1'b0), .num(priorityencoder_1_num));  // open: any
  Sub #(.Bits(5)) sub_3 (.a(5'b10111), .b(priorityencoder_1_num), .c_i(1'b0), .s(sub_3_s), .c_o(sub_3_c_o[5]));
  BarrelShifter #(.Bits(25), .barrelSigned("true")) barrelshifter_2 (
    .in(multiplexer_11_out), .shift({sub_3_c_o[5], sub_3_s}), .out(barrelshifter_2_out));
  BitExtender #(.inputBits(6), .outputBits(8)) bitextender_1 (.in({sub_3_c_o[5], sub_3_s}), .out(bitextender_1_out));
  Multiplexer #(.Bits(25)) multiplexer_12 (
    .sel(sub_4_c_o), .in_0(barrelshifter_2_out), .in_1(multiplexer_11_out), .out(multiplexer_12_out));
  Sub #(.Bits(8)) sub_4 (.a(multiplexer_1_out), .b(bitextender_1_out), .c_i(1'b0), .s(sub_4_s), .c_o(sub_4_c_o));
  Comparator #(.Bits(8)) comparator_4 (.a(bitextender_1_out), .b({8{1'b1}}), .eq(comparator_4_eq));  // open: gt, lt
  Comparator #(.Bits(8)) comparator_5 (.a({8{1'b0}}), .b(sub_4_s), .eq(comparator_5_eq));  // open: gt, lt
  or or_4 (or_4_out, comparator_5_eq, sub_4_c_o);
  Add #(.Bits(8)) add_3 (.a({8{1'b0}}), .b({8{1'b0}}), .c_i(multiplexer_11_out[23]), .s(add_3_s));  // open: c_o
  BarrelShifter #(.Bits(25), .direction("right")) barrelshifter_3 (
    .in(multiplexer_12_out), .shift(5'b00001), .out(barrelshifter_3_out));
  Multiplexer #(.Bits(8)) multiplexer_13 (.sel(and_1_out), .in_0(sub_4_s), .in_1(add_3_s), .out(e));
  and and_1 (and_1_out, or_4_out, nor_1_out);
  Multiplexer #(.Bits(25)) multiplexer_14 (
    .sel(comparator_4_eq), .in_0(multiplexer_12_out), .in_1(barrelshifter_3_out),
    .out({multiplexer_14_out, m}));
endmodule
