// Digital circuit floataddermetedgecases.dig as structural Verilog
module floataddermetedgecases (
  input  [31:0] in0,
  input  [31:0] in1,
  output [31:0] out
);

  wire and_1_out, and_2_out, and_3_out, comparator_1_eq, comparator_2_eq, comparator_3_gt, comparator_4_gt,
       comparator_5_gt, or_1_out, or_2_out, xor_1_out;
  wire [7:0] floatadder_1_e;
  wire [22:0] floatadder_1_m;
  wire [31:0] multiplexer_1_out, multiplexer_2_out, multiplexer_3_out;
  wire [31:31] floatadder_1_s;

  floatadder floatadder_1 (
    .m0(in1[22:0]), .m1(in0[22:0]), .e0(in1[30:23]), .e1(in0[30:23]), .s0(in1[31]), .s1(in0[31]),
    .m(floatadder_1_m), .e(floatadder_1_e), .s(floatadder_1_s[31]));
  Comparator #(.Bits(31)) comparator_1 (.a(in1[30:0]), .b(in0[30:0]), .eq(comparator_1_eq));  // open: gt, lt
  xor xor_1 (xor_1_out, in0[31], in1[31]);
  Comparator #(.Bits(8)) comparator_2 (.a({8{1'b1}}), .b(in1[30:23]), .eq(comparator_2_eq));  // open: gt, lt
  Comparator #(.Bits(31)) comparator_3 (.a(in0[30:0]), .b(31'h7f800000), .gt(comparator_3_gt));  // open: eq, lt
  Comparator #(.Bits(31)) comparator_4 (.a(in1[30:0]), .b(31'h7f800000), .gt(comparator_4_gt));  // open: eq, lt
  or or_1 (or_1_out, comparator_3_gt, comparator_4_gt);
  and and_1 (and_1_out, comparator_1_eq, xor_1_out);
  and and_2 (and_2_out, comparator_1_eq, comparator_2_eq);
  Multiplexer #(.Bits(32)) multiplexer_1 (
    .sel(and_1_out), .in_0({floatadder_1_s[31], floatadder_1_e, floatadder_1_m}), .in_1({32{1'b0}}),
    .out(multiplexer_1_out));
  Multiplexer #(.Bits(32)) multiplexer_2 (
    .sel(and_2_out), .in_0(multiplexer_1_out), .in_1(in0), .out(multiplexer_2_out));
  and and_3 (and_3_out, and_2_out, xor_1_out);
  or or_2 (or_2_out, and_3_out, or_1_out);
  Comparator #(.Bits(31)) comparator_5 (
    .a(multiplexer_2_out[30:0]), .b(31'h7f800000), .gt(comparator_5_gt));  // open: eq, lt
  Multiplexer #(.Bits(32)) multiplexer_3 (
    .sel(comparator_5_gt), .in_0(multiplexer_2_out), .in_1({multiplexer_2_out[31], 31'h7f800000}),
    .out(multiplexer_3_out));
  Multiplexer #(.Bits(32)) multiplexer_4 (.sel(or_2_out), .in_0(multiplexer_3_out), .in_1({32{1'b1}}), .out(out));
endmodule
