// Digital circuit floatdiv.dig as structural Verilog
module floatdiv (
  input  [22:0] m0,
  input  [22:0] m1,
  input  [7:0] e0,
  input  [7:0] e1,
  input  s0,
  input  s1,
  output [22:0] m,
  output [7:0] e,
  output s,
  output overflow
);

  wire add_1_c_o, and_1_out, comparator_1_eq, comparator_2_eq, comparator_3_gt, comparator_4_gt,
       comparator_5_gt, sub_3_c_o;
  wire [5:0] multiplexer_1_out, priorityencoder_1_num;
  wire [7:0] add_1_s, sub_1_s, sub_2_s, sub_3_s;
  wire [23:23] not_1_out, not_2_out;
  wire [47:0] barrelshifter_1_out, barrelshifter_2_out, div_1_out;

  Comparator #(.Bits(8)) comparator_1 (.a({8{1'b0}}), .b(e0), .eq(comparator_1_eq));  // open: gt, lt
  Comparator #(.Bits(8)) comparator_2 (.a(e1), .b({8{1'b0}}), .eq(comparator_2_eq));  // open: gt, lt
  not not_1 (not_1_out[23], comparator_1_eq);
  not not_2 (not_2_out[23], comparator_2_eq);
  xor xor_1 (s, s0, s1);
  div div_1 (.in0({not_1_out[23], m0}), .in1({not_2_out[23], m1}), .out(div_1_out));
  Sub #(.Bits(8)) sub_1 (.a(e0), .b(e1), .c_i(1'b0), .s(sub_1_s));  // open: c_o
  Comparator #(.Bits(8)) comparator_3 (.a(e0), .b(e1), .gt(comparator_3_gt));  // open: eq, lt
  PriorityEncoder #(.Selector_Bits(6)) priorityencoder_1 (
    .in0(div_1_out[0]), .in1(div_1_out[1]), .in2(div_1_out[2]), .in3(div_1_out[3]), .in4(div_1_out[4]),
    .in5(div_1_out[5]), .in6(div_1_out[6]), .in7(div_1_out[7]), .in8(div_1_out[8]), .in9(div_1_out[9]),
    .in10(div_1_out[10]), .in11(div_1_out[11]), .in12(div_1_out[12]), .in13(div_1_out[13]),
    .in14(div_1_out[14]), .in15(div_1_out[15]), .in16(div_1_out[16]), .in17(div_1_out[17]),
    .in18(div_1_out[18]), .in19(div_1_out[19]), .in20(div_1_out[20]), .in21(div_1_out[21]),
    .in22(div_1_out[22]), .in23(div_1_out[23]), .in24(div_1_out[24]), .in25(div_1_out[25]),
    .in26(div_1_out[26]), .in27(div_1_out[27]), .in28(div_1_out[28]), .in29(div_1_out[29]),
    .in30(div_1_out[30]), .in31(div_1_out[31]), .in32(div_1_out[32]), .in33(div_1_out[33]),
    .in34(div_1_out[34]), .in35(div_1_out[35]), .in36(div_1_out[36]), .in37(div_1_out[37]),
    .in38(div_1_out[38]), .in39(div_1_out[39]), .in40(div_1_out[40]), .in41(div_1_out[41]),
    .in42(div_1_out[42]), .in43(div_1_out[43]), .in44(div_1_out[44]), .in45(div_1_out[45]),
    .in46(div_1_out[46]), .in47(div_1_out[47]), .in48(1'b0), .in49(1'b0), .in50(1'b0), .in51(1'b0),
    .in52(1'b0), .in53(1'b0), .in54(1'b0), .in55(1'b0), .in56(1'b0), .in57(1'b0), .in58(1'b0), .in59(1'b0),
    .in60(1'b0), .in61(1'b0), .in62(1'b0), .in63(1'b0), .num(priorityencoder_1_num));  // open: any
  Sub #(.Bits(6)) sub_2 (
    .a(6'b011000), .b(priorityencoder_1_num), .c_i(1'b0), .s({sub_2_s[7], sub_2_s[4:0]}));  // open: c_o
  Sub #(.Bits(8)) sub_3 (.a(sub_1_s), .b({{3{sub_2_s[7]}}, sub_2_s[4:0]}), .c_i(1'b0), .s(sub_3_s), .c_o(sub_3_c_o));
  Comparator #(.Signed("true"), .Bits(8)) comparator_4 (
    .a({2'b00, sub_2_s[7], sub_2_s[4:0]}), .b(sub_1_s), .gt(comparator_4_gt));  // open: eq, lt
  Comparator #(.Signed("true"), .Bits(6)) comparator_5 (
    .a({sub_2_s[7], sub_2_s[4:0]}), .b({6{1'b0}}), .gt(comparator_5_gt));  // open: eq, lt
  Add #(.Bits(8)) add_1 (.a(sub_3_s), .b(8'h7f), .c_i(1'b0), .s(add_1_s), .c_o(add_1_c_o));
  and and_1 (and_1_out, comparator_5_gt, sub_3_c_o);
  Multiplexer #(.Bits(6)) multiplexer_1 (
    .sel(comparator_4_gt), .in_0({sub_2_s[7], sub_2_s[4:0]}), .in_1(sub_1_s[5:0]), .out(multiplexer_1_out));
  Multiplexer #(.Bits(8)) multiplexer_2 (.sel(and_1_out), .in_0(add_1_s), .in_1({8{1'b0}}), .out(e));
  BarrelShifter #(.Bits(48), .barrelSigned("true")) barrelshifter_1 (
    .in(div_1_out), .shift({{2{multiplexer_1_out[5]}}, multiplexer_1_out[4:0]}), .out(barrelshifter_1_out));
  BarrelShifter #(.Bits(48)) barrelshifter_2 (
    .in(barrelshifter_1_out), .shift({{5{1'b0}}, multiplexer_1_out[5]}),
    .out({barrelshifter_2_out[47:24], m, barrelshifter_2_out[0]}));
  and and_2 (overflow, add_1_c_o, comparator_3_gt);

  // Notes on the sheet:
  //   e0: default 128
  //   e1: default 129
endmodule
