// Digital circuit floatdivwithedgecases.dig as structural Verilog
module floatdivwithedgecases (
  input  [31:0] in0,
  input  [31:0] in1,
  output [31:0] out
);

  wire and_1_out, and_2_out, and_3_out, and_4_out, and_5_out, and_6_out, and_7_out, and_8_out,
       comparator_1_eq, comparator_2_eq, comparator_2_gt, comparator_3_eq, comparator_4_eq, comparator_4_gt,
       comparator_5_eq, floatdiv_1_overflow, nor_1_out, nor_2_out, or_1_out, or_2_out, or_3_out;
  wire [7:0] floatdiv_1_e;
  wire [22:0] floatdiv_1_m;
  wire [31:0] multiplexer_1_out, multiplexer_2_out, multiplexer_3_out;
  wire [31:31] floatdiv_1_s;

  Comparator #(.Bits(31)) comparator_1 (.a(in0[30:0]), .b(in1[30:0]), .eq(comparator_1_eq));  // open: gt, lt
  floatdiv floatdiv_1 (
    .m0(in0[22:0]), .m1(in1[22:0]), .e0(in0[30:23]), .e1(in1[30:23]), .s0(in0[31]), .s1(in1[31]),
    .m(floatdiv_1_m), .e(floatdiv_1_e), .s(floatdiv_1_s[31]), .overflow(floatdiv_1_overflow));
  Comparator #(.Bits(31)) comparator_2 (
    .a(in0[30:0]), .b(31'h7f800000), .gt(comparator_2_gt), .eq(comparator_2_eq));  // open: lt
  Comparator #(.Bits(31)) comparator_3 (.a(in0[30:0]), .b({31{1'b0}}), .eq(comparator_3_eq));  // open: gt, lt
  Comparator #(.Bits(31)) comparator_4 (
    .a(in1[30:0]), .b(31'h7f800000), .gt(comparator_4_gt), .eq(comparator_4_eq));  // open: lt
  Comparator #(.Bits(31)) comparator_5 (.a(in1[30:0]), .b({31{1'b0}}), .eq(comparator_5_eq));  // open: gt, lt
  nor nor_1 (nor_1_out, comparator_3_eq, comparator_2_eq, comparator_2_gt);
  nor nor_2 (nor_2_out, comparator_5_eq, comparator_4_eq, comparator_4_gt);
  and and_1 (and_1_out, comparator_2_eq, comparator_4_eq);
  and and_2 (and_2_out, comparator_3_eq, comparator_5_eq);
  and and_3 (and_3_out, nor_1_out, comparator_5_eq);
  and and_4 (and_4_out, comparator_2_eq, comparator_5_eq);
  and and_5 (and_5_out, comparator_2_eq, nor_2_out);
  and and_6 (and_6_out, nor_1_out, comparator_4_eq);
  and and_7 (and_7_out, comparator_3_eq, nor_2_out);
  and and_8 (and_8_out, comparator_3_eq, comparator_4_eq);
  or or_1 (or_1_out, comparator_2_gt, comparator_4_gt, and_1_out, and_2_out);
  or or_2 (or_2_out, and_3_out, floatdiv_1_overflow, and_4_out, and_5_out);
  or or_3 (or_3_out, and_6_out, and_7_out, and_8_out);
  Multiplexer #(.Bits(32)) multiplexer_1 (
    .sel(comparator_1_eq), .in_0({floatdiv_1_s[31], floatdiv_1_e, floatdiv_1_m}),
    .in_1({floatdiv_1_s[31], 31'h3f800000}), .out(multiplexer_1_out));
  Multiplexer #(.Bits(32)) multiplexer_2 (
    .sel(or_2_out), .in_0(multiplexer_1_out), .in_1({floatdiv_1_s[31], 31'h7f800000}), .out(multiplexer_2_out));
  Multiplexer #(.Bits(32)) multiplexer_3 (
    .sel(or_3_out), .in_0(multiplexer_2_out), .in_1({floatdiv_1_s[31], {31{1'b0}}}), .out(multiplexer_3_out));
  Multiplexer #(.Bits(32)) multiplexer_4 (.sel(or_1_out), .in_0(multiplexer_3_out), .in_1({32{1'b1}}), .out(out));

  // Notes on the sheet:
  //   in0: default 1077936128
  //   in1: default 1084227584
endmodule
