// Digital circuit floatmult.dig as structural Verilog
module floatmult (
  input  [22:0] m0,
  input  [22:0] m1,
  input  [7:0] e0,
  input  [7:0] e1,
  input  s0,
  input  s1,
  output [22:0] m,
  output [7:0] e,
  output s
);

  wire and_1_out, comparator_1_eq, comparator_2_eq, sub_1_c_o, sub_3_c_o, xor_1_out;
  wire [0:0] mul_1_mul_2;
  wire [4:0] priorityencoder_1_num;
  wire [5:0] sub_1_s;
  wire [7:0] add_1_s, add_2_s, multiplexer_2_out, multiplexer_3_out, multiplexer_6_out, sub_2_s, sub_3_s;
  wire [8:6] sub_1_s_2;
  wire [8:8] add_1_c_o;
  wire [22:0] multiplexer_1_out, multiplexer_4_out, multiplexer_5_out;
  wire [23:23] not_1_out, not_2_out;
  wire [46:0] mul_1_mul;
  wire [47:0] barrelshifter_1_out, barrelshifter_2_out, barrelshifter_3_out;

  Comparator #(.Bits(8)) comparator_1 (.a({8{1'b0}}), .b(e0), .eq(comparator_1_eq));  // open: gt, lt
  Comparator #(.Bits(8)) comparator_2 (.a(e1), .b({8{1'b0}}), .eq(comparator_2_eq));  // open: gt, lt
  not not_1 (not_1_out[23], comparator_1_eq);
  not not_2 (not_2_out[23], comparator_2_eq);
  Multiplexer #(.Bits(23)) multiplexer_1 (.sel(not_1_out[23]), .in_0(m0), .in_1(m1), .out(multiplexer_1_out));
  xor xor_1 (xor_1_out, not_1_out[23], not_2_out[23]);
  Add #(.Bits(8)) add_1 (.a(e0), .b(e1), .c_i(mul_1_mul_2[0]), .s(add_1_s), .c_o(add_1_c_o[8]));
  xor xor_2 (s, s0, s1);
  PriorityEncoder #(.Selector_Bits(5)) priorityencoder_1 (
    .in0(multiplexer_1_out[0]), .in1(multiplexer_1_out[1]), .in2(multiplexer_1_out[2]),
    .in3(multiplexer_1_out[3]), .in4(multiplexer_1_out[4]), .in5(multiplexer_1_out[5]),
    .in6(multiplexer_1_out[6]), .in7(multiplexer_1_out[7]), .in8(multiplexer_1_out[8]),
    .in9(multiplexer_1_out[9]), .in10(multiplexer_1_out[10]), .in11(multiplexer_1_out[11]),
    .in12(multiplexer_1_out[12]), .in13(multiplexer_1_out[13]), .in14(multiplexer_1_out[14]),
    .in15(multiplexer_1_out[15]), .in16(multiplexer_1_out[16]), .in17(multiplexer_1_out[17]),
    .in18(multiplexer_1_out[18]), .in19(multiplexer_1_out[19]), .in20(multiplexer_1_out[20]),
    .in21(multiplexer_1_out[21]), .in22(multiplexer_1_out[22]), .in23(1'b0), .in24(1'b0), .in25(1'b0),
    .in26(1'b0), .in27(1'b0), .in28(1'b0), .in29(1'b0), .in30(1'b0), .in31(1'b0), .num(priorityencoder_1_num));  // open: any
  Mul #(.Bits(24)) mul_1 (.a({not_1_out[23], m0}), .b({not_2_out[23], m1}), .mul({mul_1_mul_2[0], mul_1_mul}));
  Sub #(.Bits(9)) sub_1 (.a({add_1_c_o[8], add_1_s}), .b(9'h7f), .c_i(1'b0), .s({sub_1_s_2, sub_1_s}), .c_o(sub_1_c_o));
  BarrelShifter #(.Bits(48), .direction("right")) barrelshifter_1 (
    .in({mul_1_mul_2[0], mul_1_mul}), .shift({{5{1'b0}}, mul_1_mul_2[0]}), .out(barrelshifter_1_out));
  BarrelShifter #(.Bits(48)) barrelshifter_2 (.in(barrelshifter_1_out), .shift(sub_1_s), .out(barrelshifter_2_out));
  Multiplexer #(.Bits(8)) multiplexer_2 (
    .sel(sub_1_s_2[8]), .in_0({sub_1_s_2[7:6], sub_1_s}), .in_1({8{1'b1}}), .out(multiplexer_2_out));
  Multiplexer #(.Bits(8)) multiplexer_3 (
    .sel(sub_1_c_o), .in_0(multiplexer_2_out), .in_1({8{1'b0}}), .out(multiplexer_3_out));
  Sub #(.Bits(8)) sub_2 (.a(8'h17), .b({3'b000, priorityencoder_1_num}), .c_i(1'b0), .s(sub_2_s));  // open: c_o
  BarrelShifter #(.Bits(48)) barrelshifter_3 (
    .in(barrelshifter_1_out), .shift(sub_2_s[5:0]), .out(barrelshifter_3_out));
  Multiplexer #(.Bits(23)) multiplexer_4 (
    .sel(xor_1_out), .in_0(barrelshifter_1_out[45:23]), .in_1(barrelshifter_3_out[45:23]),
    .out(multiplexer_4_out));
  Sub #(.Bits(8)) sub_3 (.a(multiplexer_3_out), .b(sub_2_s), .c_i(1'b0), .s(sub_3_s), .c_o(sub_3_c_o));
  and and_1 (and_1_out, xor_1_out, sub_3_c_o);
  Add #(.Bits(8)) add_2 (.a(sub_3_s), .b({8{1'b0}}), .c_i(1'b1), .s(add_2_s));  // open: c_o
  Multiplexer #(.Bits(23)) multiplexer_5 (
    .sel(and_1_out), .in_0(multiplexer_4_out), .in_1(barrelshifter_2_out[45:23]), .out(multiplexer_5_out));
  Multiplexer #(.Bits(8)) multiplexer_6 (.sel(sub_3_c_o), .in_0(add_2_s), .in_1({8{1'b0}}), .out(multiplexer_6_out));
  Multiplexer #(.Bits(23)) multiplexer_7 (.sel(sub_1_c_o), .in_0(multiplexer_5_out), .in_1({23{1'b0}}), .out(m));
  Multiplexer #(.Bits(8)) multiplexer_8 (.sel(xor_1_out), .in_0(multiplexer_3_out), .in_1(multiplexer_6_out), .out(e));
endmodule
