// Digital circuit floatmultwithedgecases.dig as structural Verilog
module floatmultwithedgecases (
  input  [31:0] in0,
  input  [31:0] in1,
  output [31:0] out
);

  wire and_1_out, comparator_1_eq, comparator_2_eq, comparator_3_eq, comparator_4_eq, comparator_5_gt,
       comparator_6_gt, or_1_out, or_2_out, or_3_out, or_4_out;
  wire [7:0] floatmult_1_e;
  wire [22:0] floatmult_1_m;
  wire [31:0] multiplexer_1_out, multiplexer_2_out;
  wire [31:31] floatmult_1_s;

  floatmult floatmult_1 (
    .m0(in0[22:0]), .m1(in1[22:0]), .e0(in0[30:23]), .e1(in1[30:23]), .s0(in0[31]), .s1(in1[31]),
    .m(floatmult_1_m), .e(floatmult_1_e), .s(floatmult_1_s[31]));
  Comparator #(.Bits(8)) comparator_1 (.a({8{1'b1}}), .b(in1[30:23]), .eq(comparator_1_eq));  // open: gt, lt
  Comparator #(.Bits(8)) comparator_2 (.a({8{1'b1}}), .b(in0[30:23]), .eq(comparator_2_eq));  // open: gt, lt
  Comparator #(.Bits(31)) comparator_3 (.a(in1[30:0]), .b({31{1'b0}}), .eq(comparator_3_eq));  // open: gt, lt
  Comparator #(.Bits(31)) comparator_4 (.a(in0[30:0]), .b({31{1'b0}}), .eq(comparator_4_eq));  // open: gt, lt
  Comparator #(.Bits(31)) comparator_5 (.a(in1[30:0]), .b(31'h7f800000), .gt(comparator_5_gt));  // open: eq, lt
  Comparator #(.Bits(31)) comparator_6 (.a(in0[30:0]), .b(31'h7f800000), .gt(comparator_6_gt));  // open: eq, lt
  or or_1 (or_1_out, comparator_1_eq, comparator_2_eq);
  or or_2 (or_2_out, comparator_3_eq, comparator_4_eq);
  or or_3 (or_3_out, comparator_5_gt, comparator_6_gt);
  Multiplexer #(.Bits(32)) multiplexer_1 (
    .sel(or_1_out), .in_0({floatmult_1_s[31], floatmult_1_e, floatmult_1_m}),
    .in_1({floatmult_1_s[31], 31'h7f800000}), .out(multiplexer_1_out));
  Multiplexer #(.Bits(32)) multiplexer_2 (
    .sel(or_2_out), .in_0(multiplexer_1_out), .in_1({32{1'b0}}), .out(multiplexer_2_out));
  and and_1 (and_1_out, or_1_out, or_2_out);
  or or_4 (or_4_out, and_1_out, or_3_out);
  Multiplexer #(.Bits(32)) multiplexer_3 (.sel(or_4_out), .in_0(multiplexer_2_out), .in_1({32{1'b1}}), .out(out));
endmodule
