// Digital circuit ftoint.dig as structural Verilog
module ftoint (
  input  [22:0] m,
  input  [7:0] e,
  input  s,
  output [31:0] o
);

  wire multiplexer_3_out, nand_1_out, or_1_out;
  wire [6:6] sub_1_c_o;
  wire [7:0] sub_1_s;
  wire [30:0] add_1_s, multiplexer_1_out, not_1_out;
  wire [31:0] barrelshifter_1_out;

  Sub #(.Bits(8)) sub_1 (.a(e), .b(8'h96), .c_i(1'b0), .s(sub_1_s), .c_o(sub_1_c_o[6]));
  BarrelShifter #(.Bits(32), .barrelSigned("true")) barrelshifter_1 (
    .in({9'h1, m}), .shift({sub_1_c_o[6], sub_1_s[5:0]}), .out(barrelshifter_1_out));
  assign not_1_out = ~barrelshifter_1_out[30:0];  // Not not_1, 31 bits wide
  Add #(.Bits(31)) add_1 (.a(not_1_out), .b(31'h1), .c_i(1'b0), .s(add_1_s));  // open: c_o
  Multiplexer #(.Bits(31)) multiplexer_1 (
    .sel(s), .in_0(barrelshifter_1_out[30:0]), .in_1(add_1_s), .out(multiplexer_1_out));
  Multiplexer #(.Bits(32)) multiplexer_2 (
    .sel(multiplexer_3_out), .in_0({s, multiplexer_1_out}), .in_1({32{1'b0}}), .out(o));
  nand nand_1 (nand_1_out, sub_1_s[6], sub_1_s[7]);
  or or_1 (or_1_out, sub_1_s[6], sub_1_s[7]);
  Multiplexer multiplexer_3 (.sel(sub_1_c_o[6]), .in_0(or_1_out), .in_1(nand_1_out), .out(multiplexer_3_out));
endmodule
