// Digital circuit graphicsramtest.dig as structural Verilog
module graphicsramtest (
  input  in_1,
  input  clk,
  input  [4:0] in_3,
  input  [6:0] in_4
);

  GraphicCard #(.graphicHeight(4), .Bits(7), .graphicWidth(4)) graphiccard_1 (
    .A(in_3), .str(1'b1), .C(clk), .ld(1'b0), .B(in_1), .D(in_4));
endmodule
