// Digital circuit inttoff.dig as structural Verilog
module inttoff (
  input  [31:0] i,
  output [31:0] o
);

  wire not_2_out, priorityencoder_1_any;
  wire [4:0] priorityencoder_1_num, sub_1_s;
  wire [7:0] add_2_s, barrelshifter_1_out;
  wire [30:0] add_1_s, multiplexer_1_out, not_1_out;

  assign not_1_out = ~i[30:0];  // Not not_1, 31 bits wide
  Add #(.Bits(31)) add_1 (.a(not_1_out), .b(31'h1), .c_i(1'b0), .s(add_1_s));  // open: c_o
  Multiplexer #(.Bits(31)) multiplexer_1 (.sel(i[31]), .in_0(i[30:0]), .in_1(add_1_s), .out(multiplexer_1_out));
  PriorityEncoder #(.Selector_Bits(5)) priorityencoder_1 (
    .in0(multiplexer_1_out[0]), .in1(multiplexer_1_out[1]), .in2(multiplexer_1_out[2]),
    .in3(multiplexer_1_out[3]), .in4(multiplexer_1_out[4]), .in5(multiplexer_1_out[5]),
    .in6(multiplexer_1_out[6]), .in7(multiplexer_1_out[7]), .in8(multiplexer_1_out[8]),
    .in9(multiplexer_1_out[9]), .in10(multiplexer_1_out[10]), .in11(multiplexer_1_out[11]),
    .in12(multiplexer_1_out[12]), .in13(multiplexer_1_out[13]), .in14(multiplexer_1_out[14]),
    .in15(multiplexer_1_out[15]), .in16(multiplexer_1_out[16]), .in17(multiplexer_1_out[17]),
    .in18(multiplexer_1_out[18]), .in19(multiplexer_1_out[19]), .in20(multiplexer_1_out[20]),
    .in21(multiplexer_1_out[21]), .in22(multiplexer_1_out[22]), .in23(multiplexer_1_out[23]),
    .in24(multiplexer_1_out[24]), .in25(multiplexer_1_out[25]), .in26(multiplexer_1_out[26]),
    .in27(multiplexer_1_out[27]), .in28(multiplexer_1_out[28]), .in29(multiplexer_1_out[29]),
    .in30(multiplexer_1_out[30]), .in31(1'b0), .num(priorityencoder_1_num), .any(priorityencoder_1_any));
  Sub #(.Bits(5)) sub_1 (.a({5{1'b1}}), .b(priorityencoder_1_num), .c_i(1'b0), .s(sub_1_s));  // open: c_o
  not not_2 (not_2_out, priorityencoder_1_any);
  BarrelShifter #(.Bits(31)) barrelshifter_1 (
    .in(multiplexer_1_out), .shift(sub_1_s), .out({o[22:0], barrelshifter_1_out}));
  Add #(.Bits(8)) add_2 (.a({3'b000, priorityencoder_1_num}), .b(8'h7f), .c_i(1'b0), .s(add_2_s));  // open: c_o
  Multiplexer #(.Bits(8)) multiplexer_2 (.sel(not_2_out), .in_0(add_2_s), .in_1({8{1'b0}}), .out(o[30:23]));

  assign o[31] = i[31];
endmodule
