// Digital circuit logicengine.dig as structural Verilog
module logicengine (
  input  [31:0] in0,
  input  [31:0] in1,
  input  [7:0] instr0_7,
  output [31:0] Y
);

  wire [0:0] bitselector_1_out;
  wire [4:0] priorityencoder_1_num;
  wire [31:0] and_1_out, multiplexer_1_out, not_1_out, not_2_out, not_3_out, not_4_out, or_1_out, xor_1_out;

  assign and_1_out = in0 & in1;  // And and_1, 32 bits wide
  assign or_1_out = in0 | in1;  // Or or_1, 32 bits wide
  assign xor_1_out = in0 ^ in1;  // XOr xor_1, 32 bits wide
  PriorityEncoder #(.Selector_Bits(5)) priorityencoder_1 (
    .in0(in0[0]), .in1(in0[1]), .in2(in0[2]), .in3(in0[3]), .in4(in0[4]), .in5(in0[5]), .in6(in0[6]),
    .in7(in0[7]), .in8(in0[8]), .in9(in0[9]), .in10(in0[10]), .in11(in0[11]), .in12(in0[12]), .in13(in0[13]),
    .in14(in0[14]), .in15(in0[15]), .in16(in0[16]), .in17(in0[17]), .in18(in0[18]), .in19(in0[19]),
    .in20(in0[20]), .in21(in0[21]), .in22(in0[22]), .in23(in0[23]), .in24(in0[24]), .in25(in0[25]),
    .in26(in0[26]), .in27(in0[27]), .in28(in0[28]), .in29(in0[29]), .in30(in0[30]), .in31(in0[31]),
    .num(priorityencoder_1_num));  // open: any
  assign not_1_out = ~and_1_out;  // Not not_1, 32 bits wide
  assign not_2_out = ~or_1_out;  // Not not_2, 32 bits wide
  assign not_3_out = ~xor_1_out;  // Not not_3, 32 bits wide
  BitSelector #(.Selector_Bits(5)) bitselector_1 (.in(in0), .sel(in1[4:0]), .out(bitselector_1_out[0]));
  assign not_4_out = ~in0;  // Not not_4, 32 bits wide
  Multiplexer #(.Bits(32)) multiplexer_1 (
    .sel(instr0_7[6]), .in_0(not_4_out), .in_1({{27{1'b0}}, priorityencoder_1_num}), .out(multiplexer_1_out));
  Multiplexer #(.Selector_Bits(3), .Bits(32)) multiplexer_2 (
    .sel(instr0_7[2:0]), .in_0(and_1_out), .in_1(or_1_out), .in_2(not_1_out), .in_3(not_2_out),
    .in_4(xor_1_out), .in_5(not_3_out), .in_6({{31{1'b0}}, bitselector_1_out[0]}), .in_7(multiplexer_1_out),
    .out(Y));
endmodule

/* Test case:
  instr0-7 in0 in1 Y
loop(i,100000)
  let a = random(1<<32);
  let b = random(1<<32);
  0 (a)  (b)  (a&b)
  1 (a)  (b)  (a|b)
  2 (a)  (b)  (~(a&b))
  3 (a)  (b)  (~(a|b))
  4 (a)  (b)  (a^b)
  5 (a)  (b)  (~(a^b))
  7 (a)  (b)  (~a)
  let b = random(16);
  6 (a)  (b)  ((a>>b)&1)

end loop
*/
