// Digital circuit mem block.dig as structural Verilog
module mem_block (
  input  cl_double,
  input  cl,
  input  [31:0] dst,
  input  save_yn,
  input  [31:0] value,
  input  save_carry,
  input  [31:0] carry,
  input  [7:0] instr0_7,
  input  doublepoint_y,
  input  [31:0] source0,
  input  [31:0] source1,
  input  [31:0] dstaddress,
  input  [31:0] input0,
  input  [31:0] input1,
  input  [31:0] input2,
  output [31:0] inputt0,
  output [31:0] inputt1,
  output [31:0] selected_dst,
  output [31:0] carryo,
  output outputflag0,
  output [31:0] output0,
  output outputflag1,
  output [31:0] output1,
  output outputflag2,
  output [31:0] output2,
  output outputflag3,
  output [31:0] output3,
  output [31:0] counter,
  output inputflag0,
  output inputflag1,
  output inputflag2
);

  wire comparator_1_eq, comparator_2_eq, comparator_3_eq, comparator_4_eq, comparator_5_eq, comparator_6_eq,
       comparator_7_eq, or_1_out, or_2_out, or_3_out;
  wire [31:0] ram_1_ram, ram_1_reg0, ram_1_reg1, ram_1_reg2, ram_1_reg3, ram_1_reg4, ram_1_reg5, ram_1_reg6,
       ram_1_reg7, ram_1_reg8, ram_1_reg9, ram_1_reg10, ram_1_reg11, ram_1_reg12, ram_1_reg13, ram_1_reg14,
       ram_1_reg15, ram_1_reg16, ram_1_reg17, ram_1_reg18, ram_1_reg19, ram_1_reg20, ram_1_reg21,
       ram_1_reg22, ram_1_reg23, ram_1_reg24, ram_1_reg25, ram_1_reg26, ram_1_reg27, ram_1_reg28,
       ram_1_reg29, ram_1_reg30, ram_1_reg31, selectdst_1_out_42, selectinput_2_input;

  Comparator #(.Bits(32)) comparator_1 (.a(source0), .b(32'h20), .eq(comparator_1_eq));  // open: gt, lt
  Comparator #(.Bits(32)) comparator_2 (.a(source1), .b(32'h20), .eq(comparator_2_eq));  // open: gt, lt
  Comparator #(.Bits(32)) comparator_3 (.a(source0), .b(32'h21), .eq(comparator_3_eq));  // open: gt, lt
  Comparator #(.Bits(32)) comparator_4 (.a(source1), .b(32'h21), .eq(comparator_4_eq));  // open: gt, lt
  Comparator #(.Bits(32)) comparator_5 (.a(source0), .b(32'h21), .eq(comparator_5_eq));  // open: gt, lt
  Comparator #(.Bits(32)) comparator_6 (.a(source1), .b(32'h21), .eq(comparator_6_eq));  // open: gt, lt
  or or_1 (or_1_out, comparator_1_eq, comparator_2_eq);
  or or_2 (or_2_out, comparator_3_eq, comparator_4_eq);
  or or_3 (or_3_out, comparator_5_eq, comparator_6_eq);
  and and_1 (inputflag0, or_1_out, ~instr0_7[7], cl);  // And
  and and_2 (inputflag1, or_2_out, ~instr0_7[7], cl);  // And
  and and_3 (inputflag2, or_3_out, ~instr0_7[7], cl);  // And
  RAM ram_1 (
    .cl(cl), .dst(dst), .save_yn(save_yn), .value(value), .save_carry(save_carry), .carry(carry),
    .in_49(selectdst_1_out_42), .cl_doublespeed(cl_double), .reg0(ram_1_reg0), .reg1(ram_1_reg1),
    .reg2(ram_1_reg2), .reg3(ram_1_reg3), .reg4(ram_1_reg4), .reg5(ram_1_reg5), .reg6(ram_1_reg6),
    .reg7(ram_1_reg7), .reg8(ram_1_reg8), .reg9(ram_1_reg9), .reg10(ram_1_reg10), .reg11(ram_1_reg11),
    .reg12(ram_1_reg12), .reg13(ram_1_reg13), .reg14(ram_1_reg14), .reg15(ram_1_reg15), .reg16(ram_1_reg16),
    .reg17(ram_1_reg17), .reg18(ram_1_reg18), .reg19(ram_1_reg19), .reg20(ram_1_reg20), .reg21(ram_1_reg21),
    .reg22(ram_1_reg22), .reg23(ram_1_reg23), .reg24(ram_1_reg24), .reg25(ram_1_reg25), .reg26(ram_1_reg26),
    .reg27(ram_1_reg27), .reg28(ram_1_reg28), .reg29(ram_1_reg29), .reg30(ram_1_reg30), .reg31(ram_1_reg31),
    .carryo(carryo), .outputflag0(outputflag0), .output0(output0), .outputflag1(outputflag1),
    .output1(output1), .outputflag2(outputflag2), .output2(output2), .outputflag3(outputflag3),
    .output3(output3), .counter(counter), .ram(ram_1_ram));
  selectdst selectdst_1 (
    .doublepointer(doublepoint_y), .immediate_y(instr0_7[7]), .immediate_select(source0), .reg0(ram_1_reg0),
    .reg1(ram_1_reg1), .reg2(ram_1_reg2), .reg3(ram_1_reg3), .reg4(ram_1_reg4), .reg5(ram_1_reg5),
    .reg6(ram_1_reg6), .reg7(ram_1_reg7), .reg8(ram_1_reg8), .reg9(ram_1_reg9), .reg10(ram_1_reg10),
    .reg11(ram_1_reg11), .reg12(ram_1_reg12), .reg13(ram_1_reg13), .reg14(ram_1_reg14), .reg15(ram_1_reg15),
    .reg16(ram_1_reg16), .reg17(ram_1_reg17), .reg18(ram_1_reg18), .reg19(ram_1_reg19), .reg20(ram_1_reg20),
    .reg21(ram_1_reg21), .reg22(ram_1_reg22), .reg23(ram_1_reg23), .reg24(ram_1_reg24), .reg25(ram_1_reg25),
    .reg26(ram_1_reg26), .reg27(ram_1_reg27), .reg28(ram_1_reg28), .reg29(ram_1_reg29), .reg30(ram_1_reg30),
    .reg31(ram_1_reg31), .input0(input0), .input1(input1), .input2(input2), .carry(carryo),
    .extraregs(ram_1_ram), .\input (inputt0), .out_42(selectdst_1_out_42));
  selectinput selectinput_1 (
    .immediate_y(instr0_7[6]), .immediate_select(source1), .reg0(ram_1_reg0), .reg1(ram_1_reg1),
    .reg2(ram_1_reg2), .reg3(ram_1_reg3), .reg4(ram_1_reg4), .reg5(ram_1_reg5), .reg6(ram_1_reg6),
    .reg7(ram_1_reg7), .reg8(ram_1_reg8), .reg9(ram_1_reg9), .reg10(ram_1_reg10), .reg11(ram_1_reg11),
    .reg12(ram_1_reg12), .reg13(ram_1_reg13), .reg14(ram_1_reg14), .reg15(ram_1_reg15), .reg16(ram_1_reg16),
    .reg17(ram_1_reg17), .reg18(ram_1_reg18), .reg19(ram_1_reg19), .reg20(ram_1_reg20), .reg21(ram_1_reg21),
    .reg22(ram_1_reg22), .reg23(ram_1_reg23), .reg24(ram_1_reg24), .reg25(ram_1_reg25), .reg26(ram_1_reg26),
    .reg27(ram_1_reg27), .reg28(ram_1_reg28), .reg29(ram_1_reg29), .reg30(ram_1_reg30), .reg31(ram_1_reg31),
    .input0(input0), .input1(input1), .input2(input2), .carry(carryo), .extraregs(ram_1_ram),
    .\input (inputt1));
  selectinput selectinput_2 (
    .immediate_y(instr0_7[5]), .immediate_select(dstaddress), .reg0(ram_1_reg0), .reg1(ram_1_reg1),
    .reg2(ram_1_reg2), .reg3(ram_1_reg3), .reg4(ram_1_reg4), .reg5(ram_1_reg5), .reg6(ram_1_reg6),
    .reg7(ram_1_reg7), .reg8(ram_1_reg8), .reg9(ram_1_reg9), .reg10(ram_1_reg10), .reg11(ram_1_reg11),
    .reg12(ram_1_reg12), .reg13(ram_1_reg13), .reg14(ram_1_reg14), .reg15(ram_1_reg15), .reg16(ram_1_reg16),
    .reg17(ram_1_reg17), .reg18(ram_1_reg18), .reg19(ram_1_reg19), .reg20(ram_1_reg20), .reg21(ram_1_reg21),
    .reg22(ram_1_reg22), .reg23(ram_1_reg23), .reg24(ram_1_reg24), .reg25(ram_1_reg25), .reg26(ram_1_reg26),
    .reg27(ram_1_reg27), .reg28(ram_1_reg28), .reg29(ram_1_reg29), .reg30(ram_1_reg30), .reg31(ram_1_reg31),
    .input0(input0), .input1(input1), .input2(input2), .carry(carryo), .extraregs(ram_1_ram),
    .\input (selectinput_2_input));
  Multiplexer #(.Bits(32)) multiplexer_1 (
    .sel(comparator_7_eq), .in_0(selectinput_2_input), .in_1(inputt0), .out(selected_dst));
  Comparator #(.Bits(7)) comparator_7 (.a(instr0_7[6:0]), .b(7'b0111111), .eq(comparator_7_eq));  // open: gt, lt
endmodule
