// Digital circuit selectdst.dig as structural Verilog
module selectdst (
  input  doublepointer,
  input  immediate_y,
  input  [31:0] immediate_select,
  input  [31:0] reg0,
  input  [31:0] reg1,
  input  [31:0] reg2,
  input  [31:0] reg3,
  input  [31:0] reg4,
  input  [31:0] reg5,
  input  [31:0] reg6,
  input  [31:0] reg7,
  input  [31:0] reg8,
  input  [31:0] reg9,
  input  [31:0] reg10,
  input  [31:0] reg11,
  input  [31:0] reg12,
  input  [31:0] reg13,
  input  [31:0] reg14,
  input  [31:0] reg15,
  input  [31:0] reg16,
  input  [31:0] reg17,
  input  [31:0] reg18,
  input  [31:0] reg19,
  input  [31:0] reg20,
  input  [31:0] reg21,
  input  [31:0] reg22,
  input  [31:0] reg23,
  input  [31:0] reg24,
  input  [31:0] reg25,
  input  [31:0] reg26,
  input  [31:0] reg27,
  input  [31:0] reg28,
  input  [31:0] reg29,
  input  [31:0] reg30,
  input  [31:0] reg31,
  input  [31:0] input0,
  input  [31:0] input1,
  input  [31:0] input2,
  input  [31:0] carry,
  input  [31:0] extraregs,
  output [31:0] \input ,
  output [31:0] out_42
);

  wire and_1_out, and_2_out, comparator_1_gt, comparator_2_gt;
  wire [1:1] multiplexer_6_out_2;
  wire [4:0] multiplexer_6_out;
  wire [31:0] multiplexer_1_out, multiplexer_2_out, multiplexer_3_out, multiplexer_4_out, multiplexer_5_out,
       multiplexer_7_out;
  wire [31:6] multiplexer_6_out_3;

  Multiplexer #(.Selector_Bits(5), .Bits(32)) multiplexer_1 (
    .sel(immediate_select[4:0]), .in_0(reg0), .in_1(reg1), .in_2(reg2), .in_3(reg3), .in_4(reg4),
    .in_5(reg5), .in_6(reg6), .in_7(reg7), .in_8(reg8), .in_9(reg9), .in_10(reg10), .in_11(reg11),
    .in_12(reg12), .in_13(reg13), .in_14(reg14), .in_15(reg15), .in_16(reg16), .in_17(reg17), .in_18(reg18),
    .in_19(reg19), .in_20(reg20), .in_21(reg21), .in_22(reg22), .in_23(reg23), .in_24(reg24), .in_25(reg25),
    .in_26(reg26), .in_27(reg27), .in_28(reg28), .in_29(reg29), .in_30(reg30), .in_31(reg31),
    .out(multiplexer_1_out));
  Multiplexer #(.Selector_Bits(5), .Bits(32)) multiplexer_2 (
    .sel(multiplexer_6_out), .in_0(reg0), .in_1(reg1), .in_2(reg2), .in_3(reg3), .in_4(reg4), .in_5(reg5),
    .in_6(reg6), .in_7(reg7), .in_8(reg8), .in_9(reg9), .in_10(reg10), .in_11(reg11), .in_12(reg12),
    .in_13(reg13), .in_14(reg14), .in_15(reg15), .in_16(reg16), .in_17(reg17), .in_18(reg18), .in_19(reg19),
    .in_20(reg20), .in_21(reg21), .in_22(reg22), .in_23(reg23), .in_24(reg24), .in_25(reg25), .in_26(reg26),
    .in_27(reg27), .in_28(reg28), .in_29(reg29), .in_30(reg30), .in_31(reg31), .out(multiplexer_2_out));
  Multiplexer #(.Selector_Bits(2), .Bits(32)) multiplexer_3 (
    .sel(immediate_select[1:0]), .in_0(input0), .in_1(input1), .in_2(input2), .in_3(carry),
    .out(multiplexer_3_out));
  Multiplexer #(.Selector_Bits(2), .Bits(32)) multiplexer_4 (
    .sel(multiplexer_6_out[1:0]), .in_0(input0), .in_1(input1), .in_2(input2), .in_3(carry),
    .out(multiplexer_4_out));
  Multiplexer #(.Selector_Bits(2), .Bits(32)) multiplexer_5 (
    .sel({immediate_select[5], immediate_y}), .in_0(multiplexer_1_out), .in_1(immediate_select),
    .in_2(multiplexer_3_out), .in_3(immediate_select), .out(multiplexer_5_out));
  Comparator #(.Bits(32)) comparator_1 (.a(immediate_select), .b(32'h24), .gt(comparator_1_gt));  // open: eq, lt
  and and_1 (and_1_out, ~immediate_y, comparator_1_gt);  // And
  Multiplexer #(.Bits(32)) multiplexer_6 (
    .sel(and_1_out), .in_0(multiplexer_5_out), .in_1(extraregs),
    .out({multiplexer_6_out_3, multiplexer_6_out_2[1], multiplexer_6_out}));
  Comparator #(.Bits(32)) comparator_2 (
    .a({multiplexer_6_out_3, multiplexer_6_out_2[1], multiplexer_6_out}), .b(32'h24), .gt(comparator_2_gt));  // open: eq, lt
  Multiplexer #(.Selector_Bits(2), .Bits(32)) multiplexer_7 (
    .sel({multiplexer_6_out_2[1], doublepointer}),
    .in_0({multiplexer_6_out_3, multiplexer_6_out_2[1], multiplexer_6_out}), .in_1(multiplexer_2_out),
    .in_2({multiplexer_6_out_3, multiplexer_6_out_2[1], multiplexer_6_out}), .in_3(multiplexer_4_out),
    .out(multiplexer_7_out));
  and and_2 (and_2_out, doublepointer, ~immediate_y, comparator_2_gt);  // And
  Multiplexer #(.Bits(32)) multiplexer_8 (.sel(and_2_out), .in_0(multiplexer_7_out), .in_1(extraregs), .out(\input ));
  Multiplexer #(.Bits(32)) multiplexer_9 (
    .sel(doublepointer), .in_0(immediate_select),
    .in_1({multiplexer_6_out_3, multiplexer_6_out_2[1], multiplexer_6_out}), .out(out_42));
endmodule
