// Digital circuit selectinput.dig as structural Verilog
module selectinput (
  input  immediate_y,
  input  [31:0] immediate_select,
  input  [31:0] reg0,
  input  [31:0] reg1,
  input  [31:0] reg2,
  input  [31:0] reg3,
  input  [31:0] reg4,
  input  [31:0] reg5,
  input  [31:0] reg6,
  input  [31:0] reg7,
  input  [31:0] reg8,
  input  [31:0] reg9,
  input  [31:0] reg10,
  input  [31:0] reg11,
  input  [31:0] reg12,
  input  [31:0] reg13,
  input  [31:0] reg14,
  input  [31:0] reg15,
  input  [31:0] reg16,
  input  [31:0] reg17,
  input  [31:0] reg18,
  input  [31:0] reg19,
  input  [31:0] reg20,
  input  [31:0] reg21,
  input  [31:0] reg22,
  input  [31:0] reg23,
  input  [31:0] reg24,
  input  [31:0] reg25,
  input  [31:0] reg26,
  input  [31:0] reg27,
  input  [31:0] reg28,
  input  [31:0] reg29,
  input  [31:0] reg30,
  input  [31:0] reg31,
  input  [31:0] input0,
  input  [31:0] input1,
  input  [31:0] input2,
  input  [31:0] carry,
  input  [31:0] extraregs,
  output [31:0] \input 
);

  wire comparator_1_gt;
  wire [31:0] multiplexer_1_out, multiplexer_2_out, multiplexer_3_out, multiplexer_4_out;

  Multiplexer #(.Selector_Bits(5), .Bits(32)) multiplexer_1 (
    .sel(immediate_select[4:0]), .in_0(reg0), .in_1(reg1), .in_2(reg2), .in_3(reg3), .in_4(reg4),
    .in_5(reg5), .in_6(reg6), .in_7(reg7), .in_8(reg8), .in_9(reg9), .in_10(reg10), .in_11(reg11),
    .in_12(reg12), .in_13(reg13), .in_14(reg14), .in_15(reg15), .in_16(reg16), .in_17(reg17), .in_18(reg18),
    .in_19(reg19), .in_20(reg20), .in_21(reg21), .in_22(reg22), .in_23(reg23), .in_24(reg24), .in_25(reg25),
    .in_26(reg26), .in_27(reg27), .in_28(reg28), .in_29(reg29), .in_30(reg30), .in_31(reg31),
    .out(multiplexer_1_out));
  Multiplexer #(.Selector_Bits(2), .Bits(32)) multiplexer_2 (
    .sel(immediate_select[1:0]), .in_0(input0), .in_1(input1), .in_2(input2), .in_3(carry),
    .out(multiplexer_2_out));
  Comparator #(.Bits(32)) comparator_1 (.a(immediate_select), .b(32'h24), .gt(comparator_1_gt));  // open: eq, lt
  Multiplexer #(.Bits(32)) multiplexer_3 (
    .sel(immediate_select[5]), .in_0(multiplexer_1_out), .in_1(multiplexer_2_out), .out(multiplexer_3_out));
  Multiplexer #(.Bits(32)) multiplexer_4 (
    .sel(comparator_1_gt), .in_0(multiplexer_3_out), .in_1(extraregs), .out(multiplexer_4_out));
  Multiplexer #(.Bits(32)) multiplexer_5 (
    .sel(immediate_y), .in_0(multiplexer_4_out), .in_1(immediate_select), .out(\input ));
endmodule
