// Digital circuit byte adder.dig as structural Verilog
module byte_adder (
  input  carryin,
  input  [7:0] a,
  input  [7:0] b,
  output carry,
  output [7:0] out
);

  wire full_adder_1_carry, full_adder_2_carry, full_adder_3_carry, full_adder_4_carry, full_adder_5_carry,
       full_adder_6_carry, full_adder_7_carry;

  full_adder full_adder_1 (.carryin(carryin), .b(b[0]), .a(a[0]), .out(out[0]), .carry(full_adder_1_carry));
  full_adder full_adder_2 (.carryin(full_adder_1_carry), .b(b[1]), .a(a[1]), .out(out[1]), .carry(full_adder_2_carry));
  full_adder full_adder_3 (.carryin(full_adder_2_carry), .b(b[2]), .a(a[2]), .out(out[2]), .carry(full_adder_3_carry));
  full_adder full_adder_4 (.carryin(full_adder_3_carry), .b(b[3]), .a(a[3]), .out(out[3]), .carry(full_adder_4_carry));
  full_adder full_adder_5 (.carryin(full_adder_4_carry), .b(b[4]), .a(a[4]), .out(out[4]), .carry(full_adder_5_carry));
  full_adder full_adder_6 (.carryin(full_adder_5_carry), .b(b[5]), .a(a[5]), .out(out[5]), .carry(full_adder_6_carry));
  full_adder full_adder_7 (.carryin(full_adder_6_carry), .b(b[6]), .a(a[6]), .out(out[6]), .carry(full_adder_7_carry));
  full_adder full_adder_8 (.carryin(full_adder_7_carry), .b(b[7]), .a(a[7]), .out(out[7]), .carry(carry));
endmodule
