// Digital circuit full adder.dig as structural Verilog
module full_adder (
  input  carryin,
  input  b,
  input  a,
  output out,
  output carry
);

  wire and_1_out, and_2_out, or_1_out, xor_1_out;

  or or_1 (or_1_out, b, carryin);
  xor xor_1 (xor_1_out, b, carryin);
  xor xor_2 (out, a, xor_1_out);
  and and_1 (and_1_out, a, or_1_out);
  and and_2 (and_2_out, b, carryin);
  or or_2 (carry, and_1_out, and_2_out);
endmodule
