// Digital circuit mmm.dig as structural Verilog
module mmm (
  input  in_1,
  input  cl,
  output out_2,
  output [7:0] out_3
);

  wire pulldown_1_out;
  wire [7:0] counter_1_out;

  Counter #(.Bits(8)) counter_1 (.en(cl), .C(cl), .clr(pulldown_1_out), .out(counter_1_out));  // open: ovf
  PullDown pulldown_1 (.out(pulldown_1_out));
  byte_adder byte_adder_1 (.carryin(in_1), .a(counter_1_out), .b(counter_1_out), .carry(out_2), .out(out_3));

  // Notes on the sheet:
  //   cl: Hz: 2147483647
endmodule
