// Logisim project OVERTURE.circ as structural Verilog: 29 circuits, main circuit bit_mem
module overture (
  output output_flag,
  output [7:0] o,
  output input_flag
);

  wire and_1_out, and_2_out, clock_1_out, comparator_2_eq, instruction_decoder_1_condition,
       instruction_decoder_1_copy, instruction_decoder_1_immediate, instruction_decoder_1_operation,
       or_1_out, overture_condition_1_out_3, overture_destination_1_save_n_y, overture_mem_1_counter_flag;
  wire [2:0] overture_destination_1_destination;
  wire [7:0] alu_1_out_4, count_1_out_4, counter_1_q, indtruction_value_1_out_8, multiplexer_1_out,
       overture_mem_1_reg0, overture_mem_1_reg1, overture_mem_1_reg2, overture_mem_1_reg3, rom_1_data,
       rom_2_data;

  Clock clock_1 (.out(clock_1_out));
  or or_1 (or_1_out, and_2_out, overture_mem_1_counter_flag, and_1_out);
  Multiplexer #(.width(8)) multiplexer_1 (.in0(o), .in1(overture_mem_1_reg0), .out(multiplexer_1_out), .sel(and_1_out));
  Comparator #(.width(3)) comparator_1 (.a(3'b111), .b(rom_1_data[5:3]), .eq(input_flag));  // open: gt, lt
  count count_1 (.clock(clock_1_out), .overwrite(or_1_out), .value(multiplexer_1_out), .out_4(count_1_out_4));
  Counter #(.trigger("falling")) counter_1 (
    .count(input_flag), .Q(counter_1_q), .up(1'b1), .clk(clock_1_out));  // open: load, D, carry, clr
  ROM rom_1 (.addr(count_1_out_4), .data(rom_1_data));
  ROM rom_2 (.addr(counter_1_q), .data(rom_2_data));
  and and_1 (and_1_out, overture_condition_1_out_3, instruction_decoder_1_condition);
  instruction_decoder instruction_decoder_1 (
    .in_1(rom_1_data[7:6]), .immediate(instruction_decoder_1_immediate), .copy(instruction_decoder_1_copy),
    .operation(instruction_decoder_1_operation), .condition(instruction_decoder_1_condition));
  Comparator #(.width(3)) comparator_2 (
    .a(3'b110), .b(overture_destination_1_destination), .eq(comparator_2_eq));  // open: gt, lt
  overture_destination overture_destination_1 (
    .immediate(instruction_decoder_1_immediate), .copy(instruction_decoder_1_copy),
    .operation(instruction_decoder_1_operation), .condition(instruction_decoder_1_condition),
    .arg1(rom_1_data[2:0]), .save_N_Y(overture_destination_1_save_n_y),
    .destination(overture_destination_1_destination));
  indtruction_value indtruction_value_1 (
    .ALU_value(alu_1_out_4), .immediate(instruction_decoder_1_immediate), .copy(instruction_decoder_1_copy),
    .operation(instruction_decoder_1_operation), .condition(instruction_decoder_1_condition),
    .immediate_value(rom_1_data), .register_value(o), .out_8(indtruction_value_1_out_8));
  and and_2 (and_2_out, instruction_decoder_1_copy, comparator_2_eq);
  overture_mem overture_mem_1 (
    .source(rom_1_data[5:3]), .destination(overture_destination_1_destination),
    .save_Y_N(overture_destination_1_save_n_y), .value(indtruction_value_1_out_8), .counter(count_1_out_4),
    .input_i(rom_2_data), .cl(clock_1_out), .reg0(overture_mem_1_reg0), .reg1(overture_mem_1_reg1),
    .reg2(overture_mem_1_reg2), .reg3(overture_mem_1_reg3), .counter_flag(overture_mem_1_counter_flag),
    .output_flag(output_flag), .selected_value(o));  // open: reg4, reg5
  overture_condition overture_condition_1 (
    .condition(rom_1_data[2:0]), .value_reg0(overture_mem_1_reg3), .out_3(overture_condition_1_out_3));
  ALU alu_1 (.op_code(rom_1_data[2:0]), .a(overture_mem_1_reg1), .b(overture_mem_1_reg2), .out_4(alu_1_out_4));

  // Notes on the sheet:
  //   contents of rom_1 (hex, n*v repeats v):
  //   78 41 1 42 85 18 c2 78 41 42 1 44 d 5d 84 62 4c 69 5d 85 61 54 6a c5 6f 49
  //   contents of rom_2 (hex, n*v repeats v):
  //   3 4
  //   00xxxxxx: immediate, x -> reg0
  //   01xxxyyy: copy, regX -> regY
  //   10xxxxxx: operation, 000: or, 001: nand, 010: nor, 011: and, 100: add, 101: sub
  //   11xxxxxx: condition (jump to reg0 if reg3), 000: False, 001: >0, 010: =0, 011: >=0, 100: <0, 101: !=0, 110: <=0, 111: True
endmodule

module ALU (
  input  [2:0] op_code,
  input  [7:0] a,
  input  [7:0] b,
  output [7:0] out_4
);

  wire and_1_out, and_2_out, and_3_out, and_4_out;
  wire [7:0] bit_extender_1_out, byte_adder_1_sum, logic_engine_1_o, xor_1_out;

  LED or_nand (.in(and_1_out));
  LED led_1 (.in(and_2_out));
  and and_1 (and_1_out, ~op_code[2], op_code[0]);  // AND_Gate
  and and_2 (and_2_out, ~op_code[2], op_code[1]);  // AND_Gate
  LED add (.in(and_3_out));
  LED sub (.in(and_4_out));
  and and_3 (and_3_out, ~op_code[1], op_code[1]);  // AND_Gate
  and and_4 (and_4_out, op_code[1], op_code[2]);
  assign bit_extender_1_out = {{7{op_code[0]}}, op_code[0]};  // Bit_Extender bit_extender_1
  assign xor_1_out = b ^ bit_extender_1_out;  // XOR_Gate xor_1, 8 bits wide
  byte_adder byte_adder_1 (.carry_in(op_code[0]), .b(xor_1_out), .a(a), .sum(byte_adder_1_sum));  // open: carry
  logic_engine logic_engine_1 (.in_1(op_code[0]), .in_2(op_code[1]), .a(a), .b(b), .o(logic_engine_1_o));
  Multiplexer #(.width(8)) multiplexer_1 (
    .in0(logic_engine_1_o), .in1(byte_adder_1_sum), .out(out_4), .sel(op_code[2]));
endmodule

module bit_mem (
  input  save,
  input  value,
  output out_3
);

  wire nand_1_out, nand_2_out, nand_3_out, not_1_out;

  nand nand_1 (nand_1_out, save, not_1_out);
  not not_1 (not_1_out, value);
  nand nand_2 (nand_2_out, save, value);
  nand nand_3 (nand_3_out, nand_1_out, out_3);
  nand nand_4 (out_3, nand_3_out, nand_2_out);
endmodule

module bit_mem_two (
  input  save,
  input  value,
  input  cl,
  output out_4
);

  wire nand_1_out, nand_2_out, not_1_out;

  nand nand_1 (nand_1_out, save, not_1_out);
  not not_1 (not_1_out, value);
  nand nand_2 (nand_2_out, save, value);
  S_R_Flip_Flop s_r_ff_1 (.S(nand_1_out), .R(nand_2_out), .clk(cl), .Q(out_4));  // open: reset, Qn, preset
endmodule

module bit_mem_cl (
  input  savee,
  input  cl,
  input  valuee,
  output out_4
);

  wire and_1_out, and_2_out, nand_1_out, nand_2_out, nand_3_out;

  and and_1 (and_1_out, savee, ~valuee);  // AND_Gate
  and and_2 (and_2_out, savee, valuee);
  nand nand_1 (nand_1_out, and_1_out, cl);
  nand nand_2 (nand_2_out, cl, and_2_out);
  nand nand_3 (nand_3_out, nand_1_out, out_4);
  nand nand_4 (out_4, nand_3_out, nand_2_out);
endmodule

module byte_adder (
  input  carry_in,
  input  [7:0] a,
  input  [7:0] b,
  output [7:0] sum,
  output carry
);

  wire full_adder_1_carry, full_adder_2_carry, full_adder_3_carry, full_adder_4_carry, full_adder_5_carry,
       full_adder_6_carry, full_adder_7_carry;

  Full_adder full_adder_1 (.carry_in(carry_in), .a(a[0]), .b(b[0]), .sum(sum[0]), .carry(full_adder_1_carry));
  Full_adder full_adder_2 (.carry_in(full_adder_1_carry), .a(a[1]), .b(b[1]), .sum(sum[1]), .carry(full_adder_2_carry));
  Full_adder full_adder_3 (.carry_in(full_adder_2_carry), .a(a[2]), .b(b[2]), .sum(sum[2]), .carry(full_adder_3_carry));
  Full_adder full_adder_4 (.carry_in(full_adder_3_carry), .a(a[3]), .b(b[3]), .sum(sum[3]), .carry(full_adder_4_carry));
  Full_adder full_adder_5 (.carry_in(full_adder_4_carry), .a(a[4]), .b(b[4]), .sum(sum[4]), .carry(full_adder_5_carry));
  Full_adder full_adder_6 (.carry_in(full_adder_5_carry), .a(a[5]), .b(b[5]), .sum(sum[5]), .carry(full_adder_6_carry));
  Full_adder full_adder_7 (.carry_in(full_adder_6_carry), .a(a[6]), .b(b[6]), .sum(sum[6]), .carry(full_adder_7_carry));
  Full_adder full_adder_8 (.carry_in(full_adder_7_carry), .a(a[7]), .b(b[7]), .sum(sum[7]), .carry(carry));
endmodule

module byte_mem (
  input  cl,
  input  load,
  input  save,
  input  [7:0] value,
  output [7:0] enabled_when_load,
  output [7:0] always_enabled
);

  bit_mem_two bit_mem_two_1 (.value(value[0]), .cl(cl), .save(save), .out_4(always_enabled[0]));
  bit_mem_two bit_mem_two_2 (.value(value[1]), .cl(cl), .save(save), .out_4(always_enabled[1]));
  bit_mem_two bit_mem_two_3 (.value(value[2]), .cl(cl), .save(save), .out_4(always_enabled[2]));
  bit_mem_two bit_mem_two_4 (.value(value[3]), .cl(cl), .save(save), .out_4(always_enabled[3]));
  bit_mem_two bit_mem_two_5 (.value(value[4]), .cl(cl), .save(save), .out_4(always_enabled[4]));
  bit_mem_two bit_mem_two_6 (.value(value[5]), .cl(cl), .save(save), .out_4(always_enabled[5]));
  bit_mem_two bit_mem_two_7 (.value(value[6]), .cl(cl), .save(save), .out_4(always_enabled[6]));
  bit_mem_two bit_mem_two_8 (.value(value[7]), .cl(cl), .save(save), .out_4(always_enabled[7]));
  on_off on_off_1 (.off_on(load), .value(always_enabled), .o(enabled_when_load));
endmodule

module byte_to_duo_fourbit (
  input  [7:0] in_1,
  output [3:0] high,
  output [3:0] low
);


  assign high = in_1[7:4];
  assign low = in_1[3:0];
endmodule

module count (
  input  clock,
  input  overwrite,
  input  [7:0] value,
  output [7:0] out_4
);

  wire [7:0] incrementer_1_o, selector_1_o;

  selector selector_1 (.s(overwrite), .input_1(incrementer_1_o), .input_2(value), .o(selector_1_o));
  Register register_1 (.D(selector_1_o), .en(1'b1), .Q(out_4), .clk(clock));  // open: clr
  incrementer incrementer_1 (.value(out_4), .o(incrementer_1_o));  // open: carry
endmodule

module demux (
  input  [2:0] in_1,
  output out_2,
  output out_3,
  output out_4,
  output out_5,
  output out_6,
  output out_7,
  output out_8,
  output out_9
);

  and and_1 (out_2, ~in_1[0], ~in_1[1], ~in_1[2]);  // AND_Gate
  and and_2 (out_3, in_1[0], ~in_1[1], ~in_1[2]);  // AND_Gate
  and and_3 (out_4, ~in_1[0], in_1[1], ~in_1[2]);  // AND_Gate
  and and_4 (out_5, in_1[0], in_1[1], ~in_1[2]);  // AND_Gate
  and and_5 (out_6, ~in_1[0], ~in_1[1], in_1[2]);  // AND_Gate
  and and_6 (out_7, in_1[0], ~in_1[1], in_1[2]);  // AND_Gate
  and and_7 (out_8, ~in_1[0], in_1[1], in_1[2]);  // AND_Gate
  and and_8 (out_9, in_1[0], in_1[1], in_1[2]);
endmodule

module Full_adder (
  input  carry_in,
  input  a,
  input  b,
  output sum,
  output carry
);

  wire and_1_out, and_2_out, or_1_out, xor_1_out;

  xor xor_1 (xor_1_out, a, b);
  or or_1 (or_1_out, a, b);
  xor xor_2 (sum, carry_in, xor_1_out);
  and and_1 (and_1_out, carry_in, or_1_out);
  and and_2 (and_2_out, b, a);
  or or_2 (carry, and_1_out, and_2_out);
endmodule

module half_adder (
  input  a,
  input  b,
  output sum,
  output carry
);

  xor xor_1 (sum, a, b);
  and and_1 (carry, a, b);
endmodule

module incrementer (
  input  [7:0] value,
  output [7:0] o,
  output carry
);

  byte_adder byte_adder_1 (.carry_in(1'b1), .b({8{1'b0}}), .a(value), .carry(carry), .sum(o));
endmodule

module logic_engine (
  input  in_1,
  input  in_2,
  input  [7:0] a,
  input  [7:0] b,
  output [7:0] o
);

  wire [7:0] nand_1_out, not_1_out, or_1_out, selector_1_o;

  assign or_1_out = a | b;  // OR_Gate or_1, 8 bits wide
  assign nand_1_out = ~(a & b);  // NAND_Gate nand_1, 8 bits wide
  selector selector_1 (.s(in_1), .input_1(or_1_out), .input_2(nand_1_out), .o(selector_1_o));
  assign not_1_out = ~selector_1_o;  // NOT_Gate not_1, 8 bits wide
  selector selector_2 (.s(in_2), .input_1(selector_1_o), .input_2(not_1_out), .o(o));
endmodule

module on_off (
  input  off_on,
  input  [7:0] value,
  output [7:0] o
);

  and and_1 (o[0], off_on, value[0]);
  and and_2 (o[1], off_on, value[1]);
  and and_3 (o[2], off_on, value[2]);
  and and_4 (o[3], off_on, value[3]);
  and and_5 (o[4], off_on, value[4]);
  and and_6 (o[5], off_on, value[5]);
  and and_7 (o[6], off_on, value[6]);
  and and_8 (o[7], off_on, value[7]);
endmodule

module signed_not (
  input  [7:0] in_1,
  output [7:0] out_2
);

  wire [7:0] not_1_out;

  assign not_1_out = ~in_1;  // NOT_Gate not_1, 8 bits wide
  incrementer incrementer_1 (.value(not_1_out), .o(out_2));  // open: carry
endmodule

module SRFlipflop (
  input  set,
  input  reset,
  output out_3
);

  wire nand_2_out;

  nand nand_1 (out_3, ~set, nand_2_out);  // NAND_Gate
  nand nand_2 (nand_2_out, out_3, ~reset);  // NAND_Gate
endmodule

module SRfliflop_cl (
  input  set,
  input  cl,
  input  reset,
  output out_4
);

  wire nand_1_out, nand_2_out, nand_4_out;

  nand nand_1 (nand_1_out, set, cl);
  nand nand_2 (nand_2_out, cl, reset);
  nand nand_3 (out_4, nand_1_out, nand_4_out);
  nand nand_4 (nand_4_out, out_4, nand_2_out);
endmodule

module selector (
  input  s,
  input  [7:0] input_1,
  input  [7:0] input_2,
  output [7:0] o
);

  wire not_1_out;
  wire [7:0] on_off_1_o, on_off_2_o;

  not not_1 (not_1_out, s);
  on_off on_off_1 (.off_on(s), .value(input_2), .o(on_off_1_o));
  on_off on_off_2 (.off_on(not_1_out), .value(input_1), .o(on_off_2_o));
  assign o = on_off_2_o | on_off_1_o;  // OR_Gate or_1, 8 bits wide
endmodule

module overture_mem (
  input  cl,
  input  [2:0] destination,
  input  save_Y_N,
  input  [2:0] source,
  input  [7:0] counter,
  input  [7:0] input_i,
  input  [7:0] value,
  output [7:0] reg0,
  output [7:0] reg1,
  output [7:0] reg2,
  output [7:0] reg3,
  output [7:0] reg4,
  output [7:0] reg5,
  output counter_flag,
  output output_flag,
  output [7:0] selected_value
);

  wire and_1_out, and_2_out, and_3_out, and_4_out, and_5_out, and_6_out, demux_1_out_2, demux_1_out_3,
       demux_1_out_4, demux_1_out_5, demux_1_out_6, demux_1_out_7, demux_1_out_8, demux_1_out_9,
       demux_2_out_2, demux_2_out_3, demux_2_out_4, demux_2_out_5, demux_2_out_6, demux_2_out_7,
       demux_2_out_8, demux_2_out_9;
  wire [3:0] byte_to_duo_fourbit_1_high, byte_to_duo_fourbit_1_low, byte_to_duo_fourbit_2_high,
       byte_to_duo_fourbit_2_low, byte_to_duo_fourbit_3_high, byte_to_duo_fourbit_3_low,
       byte_to_duo_fourbit_4_high, byte_to_duo_fourbit_4_low, byte_to_duo_fourbit_5_high,
       byte_to_duo_fourbit_5_low, byte_to_duo_fourbit_6_high, byte_to_duo_fourbit_6_low;
  wire [7:0] byte_mem_1_enabled_when_load, byte_mem_2_enabled_when_load, byte_mem_3_enabled_when_load,
       byte_mem_4_enabled_when_load, byte_mem_5_enabled_when_load, byte_mem_6_enabled_when_load,
       multiplexer_1_out, multiplexer_2_out, or_1_out, or_2_out, or_3_out, or_4_out, or_5_out, or_6_out;

  demux demux_1 (
    .in_1(destination), .out_2(demux_1_out_2), .out_3(demux_1_out_3), .out_4(demux_1_out_4),
    .out_5(demux_1_out_5), .out_6(demux_1_out_6), .out_7(demux_1_out_7), .out_8(demux_1_out_8),
    .out_9(demux_1_out_9));
  demux demux_2 (
    .in_1(source), .out_2(demux_2_out_2), .out_3(demux_2_out_3), .out_4(demux_2_out_4),
    .out_5(demux_2_out_5), .out_6(demux_2_out_6), .out_7(demux_2_out_7), .out_8(demux_2_out_8),
    .out_9(demux_2_out_9));
  and and_1 (and_1_out, demux_1_out_2, save_Y_N);
  and and_2 (and_2_out, demux_1_out_3, save_Y_N);
  and and_3 (and_3_out, demux_1_out_4, save_Y_N);
  and and_4 (and_4_out, demux_1_out_5, save_Y_N);
  and and_5 (and_5_out, demux_1_out_6, save_Y_N);
  and and_6 (and_6_out, demux_1_out_7, save_Y_N);
  and and_7 (counter_flag, demux_1_out_8, save_Y_N);
  and and_8 (output_flag, demux_1_out_9, save_Y_N);
  Multiplexer #(.width(8)) multiplexer_1 (.in0({8{1'b0}}), .in1(counter), .out(multiplexer_1_out), .sel(demux_2_out_8));
  Multiplexer #(.width(8)) multiplexer_2 (.in0({8{1'b0}}), .in1(input_i), .out(multiplexer_2_out), .sel(demux_2_out_9));
  byte_mem byte_mem_1 (
    .save(and_1_out), .value(value), .cl(cl), .load(demux_2_out_2),
    .enabled_when_load(byte_mem_1_enabled_when_load), .always_enabled(reg0));
  byte_mem byte_mem_2 (
    .save(and_2_out), .value(value), .cl(cl), .load(demux_2_out_3),
    .enabled_when_load(byte_mem_2_enabled_when_load), .always_enabled(reg1));
  byte_mem byte_mem_3 (
    .save(and_3_out), .value(value), .cl(cl), .load(demux_2_out_4),
    .enabled_when_load(byte_mem_3_enabled_when_load), .always_enabled(reg2));
  byte_mem byte_mem_4 (
    .save(and_4_out), .value(value), .cl(cl), .load(demux_2_out_5),
    .enabled_when_load(byte_mem_4_enabled_when_load), .always_enabled(reg3));
  byte_mem byte_mem_5 (
    .save(and_5_out), .value(value), .cl(cl), .load(demux_2_out_6),
    .enabled_when_load(byte_mem_5_enabled_when_load), .always_enabled(reg4));
  byte_mem byte_mem_6 (
    .save(and_6_out), .cl(cl), .load(demux_2_out_7), .enabled_when_load(byte_mem_6_enabled_when_load),
    .always_enabled(reg5));  // open: value
  assign or_1_out = byte_mem_1_enabled_when_load | byte_mem_2_enabled_when_load;  // OR_Gate or_1, 8 bits wide
  assign or_2_out = or_1_out | byte_mem_3_enabled_when_load;  // OR_Gate or_2, 8 bits wide
  assign or_3_out = or_2_out | byte_mem_4_enabled_when_load;  // OR_Gate or_3, 8 bits wide
  assign or_4_out = or_3_out | byte_mem_5_enabled_when_load;  // OR_Gate or_4, 8 bits wide
  assign or_5_out = or_4_out | byte_mem_6_enabled_when_load;  // OR_Gate or_5, 8 bits wide
  assign or_6_out = or_5_out | multiplexer_1_out;  // OR_Gate or_6, 8 bits wide
  assign selected_value = or_6_out | multiplexer_2_out;  // OR_Gate or_7, 8 bits wide
  Hex_Digit_Display hex_digit_display_1 (.value(byte_to_duo_fourbit_1_high));  // open: dp
  Hex_Digit_Display hex_digit_display_2 (.value(byte_to_duo_fourbit_1_low));  // open: dp
  Hex_Digit_Display hex_digit_display_3 (.value(byte_to_duo_fourbit_2_high));  // open: dp
  byte_to_duo_fourbit byte_to_duo_fourbit_1 (
    .in_1(reg0), .high(byte_to_duo_fourbit_1_high), .low(byte_to_duo_fourbit_1_low));
  Hex_Digit_Display hex_digit_display_4 (.value(byte_to_duo_fourbit_2_low));  // open: dp
  byte_to_duo_fourbit byte_to_duo_fourbit_2 (
    .in_1(reg1), .high(byte_to_duo_fourbit_2_high), .low(byte_to_duo_fourbit_2_low));
  Hex_Digit_Display hex_digit_display_5 (.value(byte_to_duo_fourbit_3_high));  // open: dp
  Hex_Digit_Display hex_digit_display_6 (.value(byte_to_duo_fourbit_3_low));  // open: dp
  byte_to_duo_fourbit byte_to_duo_fourbit_3 (
    .in_1(reg2), .high(byte_to_duo_fourbit_3_high), .low(byte_to_duo_fourbit_3_low));
  Hex_Digit_Display hex_digit_display_7 (.value(byte_to_duo_fourbit_4_high));  // open: dp
  Hex_Digit_Display hex_digit_display_8 (.value(byte_to_duo_fourbit_4_low));  // open: dp
  byte_to_duo_fourbit byte_to_duo_fourbit_4 (
    .in_1(reg3), .high(byte_to_duo_fourbit_4_high), .low(byte_to_duo_fourbit_4_low));
  Hex_Digit_Display hex_digit_display_9 (.value(byte_to_duo_fourbit_5_high));  // open: dp
  Hex_Digit_Display hex_digit_display_10 (.value(byte_to_duo_fourbit_5_low));  // open: dp
  byte_to_duo_fourbit byte_to_duo_fourbit_5 (
    .in_1(reg4), .high(byte_to_duo_fourbit_5_high), .low(byte_to_duo_fourbit_5_low));
  Hex_Digit_Display hex_digit_display_11 (.value(byte_to_duo_fourbit_6_high));  // open: dp
  Hex_Digit_Display hex_digit_display_12 (.value(byte_to_duo_fourbit_6_low));  // open: dp
  byte_to_duo_fourbit byte_to_duo_fourbit_6 (
    .in_1(reg5), .high(byte_to_duo_fourbit_6_high), .low(byte_to_duo_fourbit_6_low));
endmodule

module overture_condition (
  input  [2:0] condition,
  input  [7:0] value_reg0,
  output out_3
);

  wire and_1_out, and_2_out, and_3_out, comparator_1_eq, comparator_1_gt, comparator_1_lt;

  Comparator comparator_1 (
    .a(value_reg0), .b({8{1'b0}}), .gt(comparator_1_gt), .eq(comparator_1_eq), .lt(comparator_1_lt));
  and and_1 (and_1_out, condition[0], comparator_1_gt);
  and and_2 (and_2_out, condition[1], comparator_1_eq);
  and and_3 (and_3_out, condition[2], comparator_1_lt);
  or or_1 (out_3, and_1_out, and_2_out, and_3_out);
endmodule

module twobitadd (
  input  in_1,
  input  a0,
  input  b0,
  input  a1,
  input  b1,
  output S0,
  output S1,
  output carry
);

  wire and_1_out, and_2_out, and_3_out, and_4_out, or_1_out, or_2_out, or_3_out, xor_1_out, xor_2_out;

  xor xor_1 (xor_1_out, a0, b0);
  or or_1 (or_1_out, a0, b0);
  xor xor_2 (xor_2_out, a1, b1);
  or or_2 (or_2_out, a1, b1);
  and and_1 (and_1_out, in_1, or_1_out);
  and and_2 (and_2_out, b0, a0);
  xor xor_3 (S1, or_3_out, xor_2_out);
  and and_3 (and_3_out, or_3_out, or_2_out);
  and and_4 (and_4_out, b1, a1);
  xor xor_4 (S0, in_1, xor_1_out);
  or or_3 (or_3_out, and_1_out, and_2_out);
  or or_4 (carry, and_3_out, and_4_out);
endmodule

module twobitaddb (
  input  a0,
  input  b0,
  input  a,
  input  b,
  output S0,
  output S1,
  output Carry
);

  wire full_adder_1_carry;

  Full_adder full_adder_1 (.a(a0), .b(b0), .sum(S0), .carry(full_adder_1_carry));  // open: carry_in
  Full_adder full_adder_2 (.carry_in(full_adder_1_carry), .a(a), .b(b), .sum(S1), .carry(Carry));
endmodule

module S (
  input  set,
  input  reset,
  output Q
);

  wire nand_1_out;

  nand nand_1 (nand_1_out, set, Q);
  nand nand_2 (Q, nand_1_out, reset);
endmodule

module h (
  input  save,
  input  clk,
  input  [3:0] value,
  output [3:0] out_4
);

  // bit_mem_two bit_mem: pin names not known; wires that end beside it: save, value[0], clk, save, out_4[0]
  // bit_mem_two bit_mem_two_1: pin names not known; wires that end beside it: save, value[1], clk, save, out_4[1]
  // bit_mem_two bit_mem_two_2: pin names not known; wires that end beside it: save, value[2], clk, save, out_4[2]
  // bit_mem_two bit_mem_two_3: pin names not known; wires that end beside it: save, value[3], clk, out_4[3]
endmodule

module instruction_decoder (
  input  [1:0] in_1,
  output immediate,
  output copy,
  output operation,
  output condition
);

  and and_1 (immediate, ~in_1[0], ~in_1[1]);  // AND_Gate
  and and_2 (copy, in_1[0], ~in_1[1]);  // AND_Gate
  and and_3 (operation, ~in_1[0], in_1[1]);  // AND_Gate
  and and_4 (condition, in_1[0], in_1[1]);
endmodule

module indtruction_value (
  input  [7:0] immediate_value,
  input  [7:0] register_value,
  input  [7:0] ALU_value,
  input  immediate,
  input  copy,
  input  operation,
  input  condition,
  output [7:0] out_8
);

  wire [7:0] multiplexer_1_out;

  Multiplexer #(.width(8)) multiplexer_1 (.in0(ALU_value), .in1(register_value), .out(multiplexer_1_out), .sel(copy));
  Multiplexer #(.width(8)) multiplexer_2 (.in0(multiplexer_1_out), .in1(immediate_value), .out(out_8), .sel(immediate));
endmodule

module overture_destination (
  input  [2:0] arg1,
  input  immediate,
  input  copy,
  input  operation,
  input  condition,
  output [2:0] destination,
  output save_N_Y
);

  wire [2:0] multiplexer_1_out, multiplexer_2_out;

  not not_1 (save_N_Y, condition);
  Multiplexer #(.width(3)) multiplexer_1 (.in0(3'b110), .in1(3'b011), .out(multiplexer_1_out), .sel(operation));
  Multiplexer #(.width(3)) multiplexer_2 (.in0(multiplexer_1_out), .in1(arg1), .out(multiplexer_2_out), .sel(copy));
  Multiplexer #(.width(3)) multiplexer_3 (.in0(multiplexer_2_out), .in1(3'b000), .out(destination), .sel(immediate));
endmodule

module decoded (
  input  [7:0] instruction,
  input  [7:0] register_value,
  input  [7:0] ALU_value,
  output [2:0] destination,
  output save,
  output [7:0] value
);

  wire instruction_decoder_1_condition, instruction_decoder_1_copy, instruction_decoder_1_immediate,
       instruction_decoder_1_operation;

  instruction_decoder instruction_decoder_1 (
    .in_1(instruction[7:6]), .immediate(instruction_decoder_1_immediate), .copy(instruction_decoder_1_copy),
    .operation(instruction_decoder_1_operation), .condition(instruction_decoder_1_condition));
  overture_destination overture_destination_1 (
    .immediate(instruction_decoder_1_immediate), .copy(instruction_decoder_1_copy),
    .operation(instruction_decoder_1_operation), .condition(instruction_decoder_1_condition),
    .save_N_Y(save), .destination(destination));  // open: arg1
  indtruction_value indtruction_value_1 (
    .ALU_value(ALU_value), .immediate(instruction_decoder_1_immediate), .copy(instruction_decoder_1_copy),
    .operation(instruction_decoder_1_operation), .condition(instruction_decoder_1_condition),
    .immediate_value(instruction), .register_value(register_value), .out_8(value));
endmodule
