// Logisim project V232bitfloatstack - Copy - Copy.circ as structural Verilog: 18 circuits, main circuit box
module box (
  input  [31:0] in_1,
  input  interrupt,
  input  [31:0] in_3,
  output [31:0] cycles,
  output outputflag3,
  output [31:0] output3,
  output [31:0] out_7
);

  wire main_1_outputflag0, main_1_outputflag1, main_1_outputflag2;
  wire [1:0] joystick_1_y;
  wire [2:0] main_1_output1_2;
  wire [3:0] main_1_output0, main_1_output2, main_1_output2_2, main_1_output2_3, main_1_output2_4,
       main_1_output2_5, main_1_output2_6, main_1_output2_7, main_1_output2_8, register_2_q, register_3_q;
  wire [23:0] main_1_address;
  wire [31:0] rgb_video_1_p6;
  wire [31:3] main_1_output1;
  wire [31:4] main_1_output0_2;
  wire [63:0] rom_1_data;

  ROM #(.addrWidth(24), .dataWidth(64)) rom_1 (.addr(main_1_address), .data(rom_1_data));
  main main_1 (
    .instruction(rom_1_data), .input0(in_3), .input1(out_7), .input2(in_1), .interrupt(interrupt),
    .cycles(cycles), .Address(main_1_address), .outputflag0(main_1_outputflag0),
    .output0({main_1_output0_2, main_1_output0}), .outputflag1(main_1_outputflag1),
    .output1({main_1_output1, main_1_output1_2}), .outputflag2(main_1_outputflag2),
    .output2({main_1_output2_8, main_1_output2_7, main_1_output2_6, main_1_output2_5, main_1_output2_4, main_1_output2_3, main_1_output2_2, main_1_output2}),
    .outputflag3(outputflag3), .output3(output3));
  Register #(.width(32)) register_1 (
    .D({main_1_output0_2, main_1_output0}), .en(main_1_outputflag0), .clk(main_1_outputflag0));  // open: Q, clr
  Register #(.trigger("high"), .width(4)) register_2 (
    .D(main_1_output0), .en(1'b1), .Q(register_2_q), .clk(main_1_outputflag0));  // open: clr
  Register #(.trigger("high"), .width(4)) register_3 (
    .D(main_1_output2), .en(1'b1), .Q(register_3_q), .clk(main_1_outputflag2));  // open: clr
  Joystick #(.bits(2)) joystick_1 (.y(joystick_1_y));  // open: x
  // RGB_Video #(.cursor("No Cursor"), .height(8), .width(16)) rgb_video_1: pin names not known; wires that end beside it: main_1_outputflag1, main_1_outputflag1, register_2_q, main_1_output1_2, register_3_q, rgb_video_1_p6, out_7
  assign rgb_video_1_p6 = {{30{1'b0}}, joystick_1_y};  // Bit_Extender bit_extender_1
  assign out_7 = {{30{1'b0}}, joystick_1_y};  // Bit_Extender bit_extender_2

  // Notes on the sheet:
  //   contents of rom_1 (hex, n*v repeats v):
  //   f2000000010007 f0000700000000 f0000300000009 70000700000004 6500200003000b f0000000000022
  //   f0000000000020 72000800010021 70000800010008 f0000f00000022 70000800000021 65002000010012
  //   f0000000000022 f0000000000020 70000800000021 72000800010008 f0000f00000022 72000800010021
  //   65002100030019 f0000000000022 f0000f00000020 72000300010021 70000300010003 f0000f00000022
  //   70000300000021 65002100010020 f0000000000022 f0000f00000020 70000300000021 72000300010003
  //   f0000f00000022 72000300010021 70000000000002 70000900000006 30000000040000 680000000f0000
  //   30000900050009 63000900000028 b2000000090009 b2000000050005 6600090007002c 72000900070001
  //   b2000700010009 b2000000050005 65000000000046 f0000000000001 68000800070008 25000900080037
  //   f0000100000004 32000900050009 61000500000034 70000500010005 30000900050009 70000000020000
  //   f0000100000001 7200080001000a 68000a0007000a 250009000a0041 f0000100000004 32000900050009
  //   6400050000003e 72000500010005 30000900050009 70000000020000 f0000100000001 65000100000046
  //   f0000100000004 f0000000000005 f0000800000000 f0000400000009 650000000f0060 f0000000000001
  //   68000300070003 25000900030051 70000700000004 32000900050009 6100050000004e 70000500010005
  //   30000900050009 72000000020000 f0000100000001 7200030001000a 68000a0007000a 250009000a005b
  //   70000700000004 32000900050009 64000500000058 72000500010005 30000900050009 72000000020000
  //   f0000100000001 65000100000060 70000700000004 f0000000000005 f0000700000000 f0000300000009
  //   f0000000000022 70000200000020 70000600000021 f0000f00000022 70000000000020 70000900000021
  //   27000400000004
endmodule

module main (
  input  [63:0] instruction,
  input  [31:0] input0,
  input  [31:0] input1,
  input  [31:0] input2,
  input  interrupt,
  output [31:0] cycles,
  output [23:0] Address,
  output outputflag0,
  output [31:0] output0,
  output outputflag1,
  output [31:0] output1,
  output outputflag2,
  output [31:0] output2,
  output outputflag3,
  output [31:0] output3
);

  wire and_1_out, and_2_out, and_3_out, and_4_out, and_5_out, and_6_out, buffer_1_out, clock_1_out,
       comparison_1_y_n, d_ff_1_q, d_ff_2_q, decoder2_1_save_carry, decoder2_1_save_y_n, multiplexer_1_out,
       multiplexer_2_out, multiplexer_3_out, register_1_q;
  wire [7:0] mem_block_1_counter;
  wire [31:0] aluv2_1_carry0, aluv2_1_outputt, aluv2_1_stackeeh, decoder2_1_dst, decoder2_1_value,
       mem_block_1_carryo, mem_block_1_input0, mem_block_1_input1, mem_block_1_selected_dst,
       multiplexer_4_out;

  buf buffer_1 (buffer_1_out, instruction[48]);
  and and_1 (and_1_out, buffer_1_out, and_2_out);
  and and_2 (and_2_out, ~instruction[56], instruction[57], instruction[58]);  // AND_Gate
  and and_3 (and_3_out, instruction[56], instruction[57], instruction[58]);
  and and_4 (and_4_out, instruction[56], ~instruction[57], instruction[58]);  // AND_Gate
  and and_5 (and_5_out, ~instruction[56], ~instruction[57], instruction[58]);  // AND_Gate
  Clock #(.highDuration(2), .lowDuration(2)) clock_1 (.out(clock_1_out));
  D_Flip_Flop #(.trigger("high")) d_ff_1 (
    .clk(multiplexer_2_out), .D(and_6_out), .Q(d_ff_1_q));  // open: Qn, preset, reset
  and and_6 (and_6_out, ~and_2_out, ~instruction[56], instruction[57], instruction[58]);  // AND_Gate
  Multiplexer multiplexer_1 (.in0(clock_1_out), .in1(1'b0), .out(multiplexer_1_out), .sel(d_ff_1_q));
  D_Flip_Flop #(.trigger("high")) d_ff_2 (
    .clk(and_1_out), .D(and_1_out), .Q(d_ff_2_q), .reset(interrupt));  // open: Qn, preset
  Multiplexer multiplexer_2 (.in0(multiplexer_1_out), .in1(1'b0), .out(multiplexer_2_out), .sel(d_ff_2_q));
  Multiplexer multiplexer_3 (.in0(interrupt), .in1(1'b0), .out(multiplexer_3_out), .sel(instruction[59]));
  Counter #(.max('hffffffff), .width(32)) counter_1 (
    .count(multiplexer_2_out), .Q(cycles), .up(multiplexer_2_out), .clk(multiplexer_2_out));  // open: load, D, carry, clr
  Register #(.trigger("falling"), .width(1)) register_1 (
    .D(multiplexer_3_out), .en(1'b1), .Q(register_1_q), .clk(multiplexer_2_out));  // open: clr
  decoder2 decoder2_1 (
    .instruction(instruction[55:48]), .comparison_out(comparison_1_y_n), .ALUout(aluv2_1_outputt),
    .selectdst(mem_block_1_selected_dst), .subroutineregister(aluv2_1_stackeeh),
    .counter({mem_block_1_counter, Address}), .ret_yn(and_4_out), .counter_yn(and_2_out),
    .dst(decoder2_1_dst), .save_y_n(decoder2_1_save_y_n), .value(decoder2_1_value),
    .save_carry(decoder2_1_save_carry));
  mem_block mem_block_1 (
    .cl(multiplexer_2_out), .dst(decoder2_1_dst), .save_yn(decoder2_1_save_y_n), .value(decoder2_1_value),
    .save_carry(decoder2_1_save_carry), .carry(aluv2_1_carry0), .instruction(instruction[55:48]),
    .doublepoint_y(and_3_out), .source0({{16{1'b0}}, instruction[47:32]}),
    .source1({{16{1'b0}}, instruction[31:16]}), .dstaddrress({{16{1'b0}}, instruction[15:0]}),
    .input_0(input0), .input_1(input1), .input_2(input2), .input0(mem_block_1_input0),
    .input1(mem_block_1_input1), .selected_dst(mem_block_1_selected_dst), .carryo(mem_block_1_carryo),
    .outputflag_0(outputflag0), .output_0(output0), .outputflag_1(outputflag1), .output_1(output1),
    .outputflag_2(outputflag2), .output_2(output2), .outputflag_3(outputflag3), .output_3(output3),
    .counter({mem_block_1_counter, Address}));
  Multiplexer #(.width(32)) multiplexer_4 (
    .in0(mem_block_1_input0), .in1({mem_block_1_counter, Address}), .out(multiplexer_4_out), .sel(and_5_out));
  ALUv2 aluv2_1 (
    .cl(multiplexer_2_out), .in0(multiplexer_4_out), .in1(mem_block_1_input1), .carry(mem_block_1_carryo),
    .instruction(instruction[55:48]), .innstructionbit9(instruction[57]), .pushoverwrite(and_5_out),
    .popoverwrite(and_4_out), .outputt(aluv2_1_outputt), .carry0(aluv2_1_carry0), .stackeeh(aluv2_1_stackeeh));
  comparison comparison_1 (
    .instruction(instruction[55:48]), .in0(mem_block_1_input0), .in1(mem_block_1_input1),
    .instructionbit8(instruction[56]), .instructionbit9(instruction[57]), .instructionbit11(instruction[59]),
    .interrrupt(register_1_q), .y_n(comparison_1_y_n));
endmodule

module mem_block (
  input  cl,
  input  [31:0] dst,
  input  save_yn,
  input  [31:0] value,
  input  save_carry,
  input  [31:0] carry,
  input  [7:0] instruction,
  input  doublepoint_y,
  input  [31:0] source0,
  input  [31:0] source1,
  input  [31:0] dstaddrress,
  input  [31:0] input_0,
  input  [31:0] input_1,
  input  [31:0] input_2,
  output [31:0] input0,
  output [31:0] input1,
  output [31:0] selected_dst,
  output [31:0] carryo,
  output outputflag_0,
  output [31:0] output_0,
  output outputflag_1,
  output [31:0] output_1,
  output outputflag_2,
  output [31:0] output_2,
  output outputflag_3,
  output [31:0] output_3,
  output [31:0] counter
);

  wire comparator_1_eq;
  wire [31:0] ramv2_1_out_8, ramv2_1_out_9, ramv2_1_out_10, ramv2_1_out_11, ramv2_1_out_12, ramv2_1_out_13,
       ramv2_1_out_14, ramv2_1_out_15, ramv2_1_out_16, ramv2_1_out_17, ramv2_1_out_18, ramv2_1_out_19,
       ramv2_1_out_20, ramv2_1_out_21, ramv2_1_out_22, ramv2_1_out_23, ramv2_1_out_24, ramv2_1_out_25,
       ramv2_1_out_26, ramv2_1_out_27, ramv2_1_out_28, ramv2_1_out_29, ramv2_1_out_30, ramv2_1_out_31,
       ramv2_1_out_32, ramv2_1_out_33, ramv2_1_out_34, ramv2_1_out_35, ramv2_1_out_36, ramv2_1_out_37,
       ramv2_1_out_38, ramv2_1_out_39, ramv2_1_out_50, selectdst_1_out_42, selectinput_2_inputt;

  RamV2 ramv2_1 (
    .output_flag(outputflag_0), .output1(output_0), .outflag2(outputflag_1), .output2(output_1),
    .outflag3(outputflag_2), .output3(output_2), .outflag4(outputflag_3), .output4(output_3),
    .counterr(counter), .carryo(carryo), .out_10(ramv2_1_out_10), .out_11(ramv2_1_out_11),
    .out_12(ramv2_1_out_12), .out_50(ramv2_1_out_50), .out_13(ramv2_1_out_13), .out_14(ramv2_1_out_14),
    .out_15(ramv2_1_out_15), .out_16(ramv2_1_out_16), .out_17(ramv2_1_out_17), .out_18(ramv2_1_out_18),
    .out_19(ramv2_1_out_19), .out_20(ramv2_1_out_20), .out_21(ramv2_1_out_21), .out_22(ramv2_1_out_22),
    .out_23(ramv2_1_out_23), .out_24(ramv2_1_out_24), .out_25(ramv2_1_out_25), .out_26(ramv2_1_out_26),
    .out_27(ramv2_1_out_27), .out_28(ramv2_1_out_28), .out_29(ramv2_1_out_29), .out_30(ramv2_1_out_30),
    .out_31(ramv2_1_out_31), .out_32(ramv2_1_out_32), .out_33(ramv2_1_out_33), .out_34(ramv2_1_out_34),
    .out_8(ramv2_1_out_8), .out_35(ramv2_1_out_35), .out_36(ramv2_1_out_36), .out_37(ramv2_1_out_37),
    .out_38(ramv2_1_out_38), .out_39(ramv2_1_out_39), .out_9(ramv2_1_out_9), .save_yn(save_yn),
    .value(value), .saveclock(cl), .save_carry(save_carry), .carry(carry), .dst(dst),
    .in_7(selectdst_1_out_42));
  selectdst selectdst_1 (
    .inputt(input0), .out_42(selectdst_1_out_42), .in_40(ramv2_1_out_50), .in_30(ramv2_1_out_34),
    .in_31(ramv2_1_out_35), .in_32(ramv2_1_out_36), .in_33(ramv2_1_out_37), .in_34(ramv2_1_out_38),
    .in_35(ramv2_1_out_39), .in_36(input_0), .in_37(input_1), .in_38(input_2), .in_39(carryo),
    .in_4(ramv2_1_out_8), .in_5(ramv2_1_out_9), .in_6(ramv2_1_out_10), .in_7(ramv2_1_out_11),
    .in_8(ramv2_1_out_12), .in_9(ramv2_1_out_13), .in_10(ramv2_1_out_14), .in_11(ramv2_1_out_15),
    .in_12(ramv2_1_out_16), .in_13(ramv2_1_out_17), .in_14(ramv2_1_out_18), .in_15(ramv2_1_out_19),
    .in_16(ramv2_1_out_20), .in_17(ramv2_1_out_21), .in_18(ramv2_1_out_22), .in_19(ramv2_1_out_23),
    .in_20(ramv2_1_out_24), .in_21(ramv2_1_out_25), .in_22(ramv2_1_out_26), .in_23(ramv2_1_out_27),
    .in_24(ramv2_1_out_28), .in_25(ramv2_1_out_29), .in_26(ramv2_1_out_30), .in_27(ramv2_1_out_31),
    .in_28(ramv2_1_out_32), .in_29(ramv2_1_out_33), .doublepointer(doublepoint_y),
    .immediate_y(instruction[7]), .immediate_select(source0));
  selectInput selectinput_1 (
    .inputt(input1), .in_29(ramv2_1_out_34), .in_30(ramv2_1_out_35), .in_31(ramv2_1_out_36),
    .in_32(ramv2_1_out_37), .in_33(ramv2_1_out_38), .in_34(ramv2_1_out_39), .input0(input_0),
    .input1(input_1), .input2(input_2), .carry(carryo), .in_3(ramv2_1_out_8), .in_4(ramv2_1_out_9),
    .in_5(ramv2_1_out_10), .in_6(ramv2_1_out_11), .in_7(ramv2_1_out_12), .in_8(ramv2_1_out_13),
    .in_9(ramv2_1_out_14), .in_10(ramv2_1_out_15), .in_11(ramv2_1_out_16), .in_12(ramv2_1_out_17),
    .in_13(ramv2_1_out_18), .in_14(ramv2_1_out_19), .in_15(ramv2_1_out_20), .in_16(ramv2_1_out_21),
    .in_17(ramv2_1_out_22), .in_18(ramv2_1_out_23), .in_19(ramv2_1_out_24), .in_20(ramv2_1_out_25),
    .in_21(ramv2_1_out_26), .in_22(ramv2_1_out_27), .in_23(ramv2_1_out_28), .in_24(ramv2_1_out_29),
    .in_25(ramv2_1_out_30), .in_26(ramv2_1_out_31), .in_27(ramv2_1_out_32), .in_28(ramv2_1_out_33),
    .immediate_y(instruction[6]), .immediate_select(source1), .extraregs(ramv2_1_out_50));
  selectInput selectinput_2 (
    .inputt(selectinput_2_inputt), .in_29(ramv2_1_out_34), .in_30(ramv2_1_out_35), .in_31(ramv2_1_out_36),
    .in_32(ramv2_1_out_37), .in_33(ramv2_1_out_38), .in_34(ramv2_1_out_39), .input0(input_0),
    .input1(input_1), .input2(input_2), .carry(carryo), .in_3(ramv2_1_out_8), .in_4(ramv2_1_out_9),
    .in_5(ramv2_1_out_10), .in_6(ramv2_1_out_11), .in_7(ramv2_1_out_12), .in_8(ramv2_1_out_13),
    .in_9(ramv2_1_out_14), .in_10(ramv2_1_out_15), .in_11(ramv2_1_out_16), .in_12(ramv2_1_out_17),
    .in_13(ramv2_1_out_18), .in_14(ramv2_1_out_19), .in_15(ramv2_1_out_20), .in_16(ramv2_1_out_21),
    .in_17(ramv2_1_out_22), .in_18(ramv2_1_out_23), .in_19(ramv2_1_out_24), .in_20(ramv2_1_out_25),
    .in_21(ramv2_1_out_26), .in_22(ramv2_1_out_27), .in_23(ramv2_1_out_28), .in_24(ramv2_1_out_29),
    .in_25(ramv2_1_out_30), .in_26(ramv2_1_out_31), .in_27(ramv2_1_out_32), .in_28(ramv2_1_out_33),
    .immediate_y(instruction[5]), .immediate_select(dstaddrress), .extraregs(ramv2_1_out_50));
  Comparator #(.width(7)) comparator_1 (.a(instruction[6:0]), .b(7'b0111111), .eq(comparator_1_eq));  // open: gt, lt
  Multiplexer #(.width(32)) multiplexer_1 (
    .in0(selectinput_2_inputt), .in1(input0), .out(selected_dst), .sel(comparator_1_eq));
endmodule

module decoder2 (
  input  [7:0] instruction,
  input  comparison_out,
  input  [31:0] ALUout,
  input  [31:0] selectdst,
  input  [31:0] subroutineregister,
  input  [31:0] counter,
  input  ret_yn,
  input  counter_yn,
  output [31:0] dst,
  output save_y_n,
  output [31:0] value,
  output save_carry
);

  wire and_1_out, and_2_out, nor_1_out;
  wire [31:0] multiplexer_1_out, multiplexer_2_out;

  Multiplexer #(.width(32)) multiplexer_1 (.in0(selectdst), .in1(counter), .out(multiplexer_1_out), .sel(counter_yn));
  Multiplexer #(.width(32)) multiplexer_2 (
    .in0(multiplexer_1_out), .in1(subroutineregister), .out(multiplexer_2_out), .sel(ret_yn));
  nor nor_1 (nor_1_out, instruction[3], instruction[4]);
  Multiplexer #(.width(32)) multiplexer_3 (.in0(selectdst), .in1(32'h24), .out(dst), .sel(nor_1_out));
  Multiplexer multiplexer_4 (.in0(1'b1), .in1(comparison_out), .out(save_y_n), .sel(nor_1_out));
  Multiplexer #(.width(32)) multiplexer_5 (.in0(ALUout), .in1(multiplexer_2_out), .out(value), .sel(nor_1_out));
  and and_1 (and_1_out, instruction[4], ~instruction[3]);  // AND_Gate
  and and_2 (and_2_out, ~instruction[2], instruction[3], instruction[4]);  // AND_Gate
  or or_1 (save_carry, and_1_out, and_2_out);
endmodule

module ALUv2 (
  input  cl,
  input  [31:0] in0,
  input  [31:0] in1,
  input  [31:0] carry,
  input  [7:0] instruction,
  input  innstructionbit9,
  input  pushoverwrite,
  input  popoverwrite,
  output [31:0] outputt,
  output [31:0] carry0,
  output [31:0] stackeeh
);

  wire [31:0] arithmaticengine_1_carryo, arithmaticengine_1_output_0, logicengine_1_out_4, shift_1_carryo,
       shift_1_outputt;

  logicengine logicengine_1 (.in1(in0), .in2(in1), .instruction(instruction), .out_4(logicengine_1_out_4));
  arithmaticengine arithmaticengine_1 (
    .in1(in0), .in2(in1), .carry(carry), .instruction(instruction), .instructionbit9(innstructionbit9),
    .output_0(arithmaticengine_1_output_0), .carryo(arithmaticengine_1_carryo));
  shift shift_1 (
    .cl(cl), .in0(in0), .in1(in1), .carry(carry), .instruction(instruction), .pushoverwrite(pushoverwrite),
    .popoverwrite(popoverwrite), .outputt(shift_1_outputt), .carryo(shift_1_carryo), .stackeeh(stackeeh));
  Multiplexer #(.width(32)) multiplexer_1 (
    .in0(arithmaticengine_1_carryo), .in1(shift_1_carryo), .out(carry0), .sel(instruction[3]));
  Multiplexer #(.select(2), .width(32)) multiplexer_2 (
    .in0({32{1'b0}}), .in1(logicengine_1_out_4), .in2(arithmaticengine_1_output_0), .in3(shift_1_outputt),
    .out(outputt), .sel(instruction[4:3]));
endmodule

module RamV2 (
  input  saveclock,
  input  [31:0] dst,
  input  save_yn,
  input  [31:0] value,
  input  save_carry,
  input  [31:0] carry,
  input  [31:0] in_7,
  output [31:0] out_8,
  output [31:0] out_9,
  output [31:0] out_10,
  output [31:0] out_11,
  output [31:0] out_12,
  output [31:0] out_13,
  output [31:0] out_14,
  output [31:0] out_15,
  output [31:0] out_16,
  output [31:0] out_17,
  output [31:0] out_18,
  output [31:0] out_19,
  output [31:0] out_20,
  output [31:0] out_21,
  output [31:0] out_22,
  output [31:0] out_23,
  output [31:0] out_24,
  output [31:0] out_25,
  output [31:0] out_26,
  output [31:0] out_27,
  output [31:0] out_28,
  output [31:0] out_29,
  output [31:0] out_30,
  output [31:0] out_31,
  output [31:0] out_32,
  output [31:0] out_33,
  output [31:0] out_34,
  output [31:0] out_35,
  output [31:0] out_36,
  output [31:0] out_37,
  output [31:0] out_38,
  output [31:0] out_39,
  output [31:0] carryo,
  output output_flag,
  output [31:0] output1,
  output outflag2,
  output [31:0] output2,
  output outflag3,
  output [31:0] output3,
  output outflag4,
  output [31:0] output4,
  output [31:0] counterr,
  output [31:0] out_50
);

  wire and_1_out, and_2_out, and_3_out, and_4_out, and_5_out, clock_1_out, comparator_1_gt, comparator_2_eq,
       not_1_out;
  wire [23:0] multiplexer_1_out, subtractor_1_out;

  not not_1 (not_1_out, saveclock);
  and and_1 (and_1_out, dst[5], ~comparator_1_gt);  // AND_Gate
  Multiplexer #(.width(24)) multiplexer_1 (.in0(dst[23:0]), .in1(in_7[23:0]), .out(multiplexer_1_out), .sel(not_1_out));
  Comparator #(.mode("unsigned"), .width(32)) comparator_1 (.a(dst), .b(32'h24), .gt(comparator_1_gt));  // open: eq, lt
  Clock clock_1 (.out(clock_1_out));
  Comparator #(.mode("unsigned"), .width(32)) comparator_2 (.a(dst), .b(32'h24), .eq(comparator_2_eq));  // open: gt, lt
  Subtractor #(.width(24)) subtractor_1 (.a(multiplexer_1_out), .b(24'h25), .out(subtractor_1_out));  // open: bin, bout
  RAM #(.addrWidth(24), .dataWidth(32)) ram_1 (
    .addr(subtractor_1_out), .we(and_2_out), .oe(1'b1), .clk(clock_1_out), .din(value), .dout(out_50));
  and and_2 (and_2_out, saveclock, save_yn, comparator_1_gt);
  and and_3 (and_3_out, ~dst[5], ~comparator_1_gt, save_yn);  // AND_Gate
  Register #(.width(32)) register_1 (.D(carry), .en(save_carry), .clk(saveclock), .Q(carryo));  // open: clr
  Demultiplexer #(.select(2), .width(32)) demultiplexer_1 (
    .out0(output1), .out1(output2), .out2(output3), .out3(output4), .in(value), .sel(dst[1:0]));
  and and_4 (and_4_out, and_1_out, save_yn, saveclock);
  and and_5 (and_5_out, save_yn, comparator_2_eq);
  Decoder #(.select(2)) decoder_1 (
    .out0(output_flag), .out1(outflag2), .out2(outflag3), .out3(outflag4), .sel(dst[1:0]), .en(and_4_out));
  Counter #(.max('hffffffff), .trigger("falling"), .width(32)) counter_1 (
    .load(and_5_out), .D(value), .count(1'b1), .Q(counterr), .up(1'b1), .clk(saveclock));  // open: carry, clr
  thirtytworeg thirtytworeg_1 (
    .cl(saveclock), .select16(dst), .save_yn(and_3_out), .value(value), .out_5(out_8), .out_6(out_9),
    .out_7(out_10), .out_8(out_11), .out_9(out_12), .out_10(out_13), .out_11(out_14), .out_12(out_15),
    .out_13(out_16), .out_14(out_17), .out_15(out_18), .out_16(out_19), .out_17(out_20), .out_18(out_21),
    .out_19(out_22), .out_20(out_23), .out_21(out_24), .out_22(out_25), .out_23(out_26), .out_24(out_27),
    .out_25(out_28), .out_26(out_29), .out_27(out_30), .out_28(out_31), .out_29(out_32), .out_30(out_33),
    .out_31(out_34), .out_32(out_35), .out_33(out_36), .out_34(out_37), .out_35(out_38), .out_36(out_39));

  // Notes on the sheet:
  //   setting counter is done through setting dst to the counter address
endmodule

module fourreg (
  input  [31:0] value,
  input  cl,
  input  in_3,
  input  [1:0] select2,
  output [31:0] out_5,
  output [31:0] out_6,
  output [31:0] out_7,
  output [31:0] out_8
);

  wire decoder_1_out0, decoder_1_out1, decoder_1_out2, decoder_1_out3;

  Decoder #(.select(2)) decoder_1 (
    .out0(decoder_1_out0), .out1(decoder_1_out1), .out2(decoder_1_out2), .out3(decoder_1_out3),
    .sel(select2), .en(in_3));
  Register #(.width(32)) register_1 (.D(value), .en(decoder_1_out0), .clk(cl), .Q(out_5));  // open: clr
  Register #(.width(32)) register_2 (.D(value), .en(decoder_1_out1), .clk(cl), .Q(out_6));  // open: clr
  Register #(.width(32)) register_3 (.D(value), .en(decoder_1_out2), .clk(cl), .Q(out_7));  // open: clr
  Register #(.width(32)) register_4 (.D(value), .en(decoder_1_out3), .clk(cl), .Q(out_8));  // open: clr
endmodule

module sixteenreg (
  input  cl,
  input  [31:0] value,
  input  [3:0] select4,
  input  in_4,
  output [31:0] out_5,
  output [31:0] out_6,
  output [31:0] out_7,
  output [31:0] out_8,
  output [31:0] out_9,
  output [31:0] out_10,
  output [31:0] out_11,
  output [31:0] out_12,
  output [31:0] out_13,
  output [31:0] out_14,
  output [31:0] out_15,
  output [31:0] out_16,
  output [31:0] out_17,
  output [31:0] out_18,
  output [31:0] out_19,
  output [31:0] out_20
);

  wire decoder_1_out0, decoder_1_out1, decoder_1_out2, decoder_1_out3;

  Decoder #(.select(2)) decoder_1 (
    .out0(decoder_1_out0), .out1(decoder_1_out1), .out2(decoder_1_out2), .out3(decoder_1_out3),
    .sel(select4[3:2]), .en(in_4));
  fourreg fourreg_1 (
    .value(value), .cl(cl), .in_3(decoder_1_out0), .select2(select4[1:0]), .out_5(out_5), .out_6(out_6),
    .out_7(out_7), .out_8(out_8));
  fourreg fourreg_2 (
    .value(value), .cl(cl), .in_3(decoder_1_out1), .select2(select4[1:0]), .out_5(out_9), .out_6(out_10),
    .out_7(out_11), .out_8(out_12));
  fourreg fourreg_3 (
    .value(value), .cl(cl), .in_3(decoder_1_out2), .select2(select4[1:0]), .out_5(out_13), .out_6(out_14),
    .out_7(out_15), .out_8(out_16));
  fourreg fourreg_4 (
    .value(value), .cl(cl), .in_3(decoder_1_out3), .select2(select4[1:0]), .out_5(out_17), .out_6(out_18),
    .out_7(out_19), .out_8(out_20));
endmodule

module thirtytworeg (
  input  cl,
  input  [31:0] select16,
  input  save_yn,
  input  [31:0] value,
  output [31:0] out_5,
  output [31:0] out_6,
  output [31:0] out_7,
  output [31:0] out_8,
  output [31:0] out_9,
  output [31:0] out_10,
  output [31:0] out_11,
  output [31:0] out_12,
  output [31:0] out_13,
  output [31:0] out_14,
  output [31:0] out_15,
  output [31:0] out_16,
  output [31:0] out_17,
  output [31:0] out_18,
  output [31:0] out_19,
  output [31:0] out_20,
  output [31:0] out_21,
  output [31:0] out_22,
  output [31:0] out_23,
  output [31:0] out_24,
  output [31:0] out_25,
  output [31:0] out_26,
  output [31:0] out_27,
  output [31:0] out_28,
  output [31:0] out_29,
  output [31:0] out_30,
  output [31:0] out_31,
  output [31:0] out_32,
  output [31:0] out_33,
  output [31:0] out_34,
  output [31:0] out_35,
  output [31:0] out_36
);

  wire decoder_1_out0, decoder_1_out1;

  Decoder decoder_1 (.out0(decoder_1_out0), .out1(decoder_1_out1), .sel(select16[4]), .en(save_yn));
  sixteenreg sixteenreg_1 (
    .cl(cl), .value(value), .select4(select16[3:0]), .in_4(decoder_1_out0), .out_5(out_5), .out_6(out_6),
    .out_7(out_7), .out_8(out_8), .out_9(out_9), .out_10(out_10), .out_11(out_11), .out_12(out_12),
    .out_13(out_13), .out_14(out_14), .out_15(out_15), .out_16(out_16), .out_17(out_17), .out_18(out_18),
    .out_19(out_19), .out_20(out_20));
  sixteenreg sixteenreg_2 (
    .cl(cl), .value(value), .select4(select16[3:0]), .in_4(decoder_1_out1), .out_5(out_21), .out_6(out_22),
    .out_7(out_23), .out_8(out_24), .out_9(out_25), .out_10(out_26), .out_11(out_27), .out_12(out_28),
    .out_13(out_29), .out_14(out_30), .out_15(out_31), .out_16(out_32), .out_17(out_33), .out_18(out_34),
    .out_19(out_35), .out_20(out_36));
endmodule

module selectInput (
  input  immediate_y,
  input  [31:0] immediate_select,
  input  [31:0] in_3,
  input  [31:0] in_4,
  input  [31:0] in_5,
  input  [31:0] in_6,
  input  [31:0] in_7,
  input  [31:0] in_8,
  input  [31:0] in_9,
  input  [31:0] in_10,
  input  [31:0] in_11,
  input  [31:0] in_12,
  input  [31:0] in_13,
  input  [31:0] in_14,
  input  [31:0] in_15,
  input  [31:0] in_16,
  input  [31:0] in_17,
  input  [31:0] in_18,
  input  [31:0] in_19,
  input  [31:0] in_20,
  input  [31:0] in_21,
  input  [31:0] in_22,
  input  [31:0] in_23,
  input  [31:0] in_24,
  input  [31:0] in_25,
  input  [31:0] in_26,
  input  [31:0] in_27,
  input  [31:0] in_28,
  input  [31:0] in_29,
  input  [31:0] in_30,
  input  [31:0] in_31,
  input  [31:0] in_32,
  input  [31:0] in_33,
  input  [31:0] in_34,
  input  [31:0] input0,
  input  [31:0] input1,
  input  [31:0] input2,
  input  [31:0] carry,
  input  [31:0] extraregs,
  output [31:0] inputt
);

  wire comparator_1_gt;
  wire [31:0] multiplexer_1_out, multiplexer_2_out, multiplexer_3_out, multiplexer_5_out;

  Multiplexer #(.select(2), .width(32)) multiplexer_1 (
    .in0(input0), .in1(input1), .in2(input2), .in3(carry), .out(multiplexer_1_out),
    .sel(immediate_select[1:0]));
  Comparator #(.mode("unsigned"), .width(32)) comparator_1 (
    .a(immediate_select), .b(32'h24), .gt(comparator_1_gt));  // open: eq, lt
  Multiplexer #(.width(32)) multiplexer_2 (
    .in0(multiplexer_5_out), .in1(multiplexer_1_out), .out(multiplexer_2_out), .sel(immediate_select[5]));
  Multiplexer #(.width(32)) multiplexer_3 (
    .in0(multiplexer_2_out), .in1(extraregs), .out(multiplexer_3_out), .sel(comparator_1_gt));
  Multiplexer #(.width(32)) multiplexer_4 (
    .in0(multiplexer_3_out), .in1(immediate_select), .out(inputt), .sel(immediate_y));
  Multiplexer #(.select(5), .width(32)) multiplexer_5 (
    .in0(in_3), .in1(in_4), .in2(in_5), .in3(in_6), .in4(in_7), .in5(in_8), .in6(in_9), .in7(in_10),
    .in8(in_11), .in9(in_12), .in10(in_13), .in11(in_14), .in12(in_15), .in13(in_16), .in14(in_17),
    .in15(in_18), .in16(in_19), .in17(in_20), .in18(in_21), .in19(in_22), .in20(in_23), .in21(in_24),
    .in22(in_25), .in23(in_26), .in24(in_27), .in25(in_28), .in26(in_29), .in27(in_30), .in28(in_31),
    .in29(in_32), .in30(in_33), .in31(in_34), .out(multiplexer_5_out), .sel(immediate_select[4:0]));
endmodule

module selectdst (
  input  doublepointer,
  input  immediate_y,
  input  [31:0] immediate_select,
  input  [31:0] in_4,
  input  [31:0] in_5,
  input  [31:0] in_6,
  input  [31:0] in_7,
  input  [31:0] in_8,
  input  [31:0] in_9,
  input  [31:0] in_10,
  input  [31:0] in_11,
  input  [31:0] in_12,
  input  [31:0] in_13,
  input  [31:0] in_14,
  input  [31:0] in_15,
  input  [31:0] in_16,
  input  [31:0] in_17,
  input  [31:0] in_18,
  input  [31:0] in_19,
  input  [31:0] in_20,
  input  [31:0] in_21,
  input  [31:0] in_22,
  input  [31:0] in_23,
  input  [31:0] in_24,
  input  [31:0] in_25,
  input  [31:0] in_26,
  input  [31:0] in_27,
  input  [31:0] in_28,
  input  [31:0] in_29,
  input  [31:0] in_30,
  input  [31:0] in_31,
  input  [31:0] in_32,
  input  [31:0] in_33,
  input  [31:0] in_34,
  input  [31:0] in_35,
  input  [31:0] in_36,
  input  [31:0] in_37,
  input  [31:0] in_38,
  input  [31:0] in_39,
  input  [31:0] in_40,
  output [31:0] inputt,
  output [31:0] out_42
);

  wire and_1_out, and_2_out, comparator_1_gt, comparator_2_gt;
  wire [31:0] multiplexer_1_out, multiplexer_2_out, multiplexer_3_out, multiplexer_4_out, multiplexer_5_out,
       multiplexer_6_out, multiplexer_7_out;

  Comparator #(.mode("unsigned"), .width(32)) comparator_1 (
    .a(immediate_select), .b(32'h24), .gt(comparator_1_gt));  // open: eq, lt
  Multiplexer #(.select(2), .width(32)) multiplexer_1 (
    .in0(multiplexer_3_out), .in1(immediate_select), .in2(multiplexer_6_out), .in3(immediate_select),
    .out(multiplexer_1_out), .sel({immediate_select[5], immediate_y}));
  and and_1 (and_1_out, ~immediate_y, comparator_1_gt);  // AND_Gate
  Multiplexer #(.width(32)) multiplexer_2 (
    .in0(multiplexer_1_out), .in1(in_40), .out(multiplexer_2_out), .sel(and_1_out));
  Comparator #(.mode("unsigned"), .width(32)) comparator_2 (
    .a(multiplexer_2_out), .b(32'h24), .gt(comparator_2_gt));  // open: eq, lt
  Multiplexer #(.select(5), .width(32)) multiplexer_3 (
    .in0(in_4), .in1(in_5), .in2(in_6), .in3(in_7), .in4(in_8), .in5(in_9), .in6(in_10), .in7(in_11),
    .in8(in_12), .in9(in_13), .in10(in_14), .in11(in_15), .in12(in_16), .in13(in_17), .in14(in_18),
    .in15(in_19), .in16(in_20), .in17(in_21), .in18(in_22), .in19(in_23), .in20(in_24), .in21(in_25),
    .in22(in_26), .in23(in_27), .in24(in_28), .in25(in_29), .in26(in_30), .in27(in_31), .in28(in_32),
    .in29(in_33), .in30(in_34), .in31(in_35), .out(multiplexer_3_out), .sel(immediate_select[4:0]));
  Multiplexer #(.select(5), .width(32)) multiplexer_4 (
    .in0(in_4), .in1(in_5), .in2(in_6), .in3(in_7), .in4(in_8), .in5(in_9), .in6(in_10), .in7(in_11),
    .in8(in_12), .in9(in_13), .in10(in_14), .in11(in_15), .in12(in_16), .in13(in_17), .in14(in_18),
    .in15(in_19), .in16(in_20), .in17(in_21), .in18(in_22), .in19(in_23), .in20(in_24), .in21(in_25),
    .in22(in_26), .in23(in_27), .in24(in_28), .in25(in_29), .in26(in_30), .in27(in_31), .in28(in_32),
    .in29(in_33), .in30(in_34), .in31(in_35), .out(multiplexer_4_out), .sel(multiplexer_2_out[4:0]));
  Multiplexer #(.select(2), .width(32)) multiplexer_5 (
    .in0(multiplexer_2_out), .in1(multiplexer_4_out), .in2(multiplexer_2_out), .in3(multiplexer_7_out),
    .out(multiplexer_5_out), .sel({multiplexer_2_out[5], doublepointer}));
  Multiplexer #(.select(2), .width(32)) multiplexer_6 (
    .in0(in_36), .in1(in_37), .in2(in_38), .in3(in_39), .out(multiplexer_6_out), .sel(immediate_select[1:0]));
  Multiplexer #(.select(2), .width(32)) multiplexer_7 (
    .in0(in_36), .in1(in_37), .in2(in_38), .in3(in_39), .out(multiplexer_7_out), .sel(multiplexer_2_out[1:0]));
  and and_2 (and_2_out, doublepointer, ~immediate_y, comparator_2_gt);  // AND_Gate
  Multiplexer #(.width(32)) multiplexer_8 (.in0(multiplexer_5_out), .in1(in_40), .out(inputt), .sel(and_2_out));
  Multiplexer #(.width(32)) multiplexer_9 (
    .in0(immediate_select), .in1(multiplexer_2_out), .out(out_42), .sel(doublepointer));
endmodule

module logicengine (
  input  [31:0] in1,
  input  [31:0] in2,
  input  [7:0] instruction,
  output [31:0] out_4
);

  wire [0:0] bitselector_1_out;
  wire [3:0] undriven_4, undriven_5, undriven_6;
  wire [4:0] priority_encoder_1_out, undriven, undriven_2, undriven_3;
  wire [31:0] and_1_out, multiplexer_1_out, not_1_out, not_2_out, not_3_out, not_4_out, or_1_out, xor_1_out;

  assign not_1_out = ~in1;  // NOT_Gate not_1, 32 bits wide
  assign and_1_out = in1 & in2;  // AND_Gate and_1, 32 bits wide
  assign or_1_out = in1 | in2;  // OR_Gate or_1, 32 bits wide
  assign xor_1_out = in1 ^ in2;  // XOR_Gate xor_1, 32 bits wide
  Priority_Encoder #(.select(5)) priority_encoder_1 (
    .in0(in1[0]), .in1(in1[1]), .in2(in1[2]), .in3(in1[3]), .in4(in1[4]), .in5(in1[5]), .in6(in1[6]),
    .in7(in1[7]), .in8(in1[8]), .in9(in1[9]), .in10(in1[10]), .in11(in1[11]), .in12(in1[12]), .in13(in1[13]),
    .in14(in1[14]), .in15(in1[15]), .in16(in1[16]), .in17(in1[17]), .in18(in1[18]), .in19(in1[19]),
    .in20(in1[20]), .in21(in1[21]), .in22(in1[22]), .in23(in1[23]), .in24(in1[24]), .in25(in1[25]),
    .in26(in1[26]), .in27(in1[27]), .in28(in1[28]), .in29(in1[29]), .in30(in1[30]), .in31(in1[31]),
    .out(priority_encoder_1_out));  // open: gs, en_out, en_in
  BitSelector #(.width(32)) bitselector_1 (.in(in1), .out(bitselector_1_out[0]), .sel(in2[4:0]));
  Multiplexer #(.width(32)) multiplexer_1 (
    .in0(not_1_out),
    .in1({undriven_6, undriven_5, undriven_4, undriven_3, undriven_2, undriven, priority_encoder_1_out}),
    .out(multiplexer_1_out), .sel(instruction[6]));
  assign not_2_out = ~and_1_out;  // NOT_Gate not_2, 32 bits wide
  assign not_3_out = ~or_1_out;  // NOT_Gate not_3, 32 bits wide
  assign not_4_out = ~xor_1_out;  // NOT_Gate not_4, 32 bits wide
  Multiplexer #(.select(3), .width(32)) multiplexer_2 (
    .in0(and_1_out), .in1(or_1_out), .in2(not_2_out), .in3(not_3_out), .in4(xor_1_out), .in5(not_4_out),
    .in6({{31{1'b0}}, bitselector_1_out[0]}), .in7(multiplexer_1_out), .out(out_4), .sel(instruction[2:0]));
endmodule

module arithmaticengine (
  input  [31:0] in1,
  input  [31:0] in2,
  input  [31:0] carry,
  input  [7:0] instruction,
  input  instructionbit9,
  output [31:0] output_0,
  output [31:0] carryo
);

  wire and_1_out;
  wire [0:0] adder_1_cout, adder_2_cout, subtractor_1_bout, subtractor_2_bout;
  wire [7:0] fptoint_1_p2, fptoint_2_p2, fptoint_3_p2;
  wire [31:0] adder_1_out, adder_2_out, divider_1_out, divider_1_rem, fpadder_1_out, fpdivider_1_out,
       fpmultiplier_1_out, fpsubtractor_1_out, inttofp_1_p2, multiplexer_1_out, multiplexer_2_out,
       multiplexer_3_out, multiplier_1_cout, multiplier_1_out, subtractor_1_out, subtractor_2_out;

  and and_1 (and_1_out, carry[0], instruction[0]);
  Adder #(.width(32)) adder_1 (.a(in1), .b(in2), .out(adder_1_out), .cin(and_1_out), .cout(adder_1_cout[0]));
  Subtractor #(.width(32)) subtractor_1 (
    .a(in1), .b(in2), .out(subtractor_1_out), .bin(and_1_out), .bout(subtractor_1_bout[0]));
  Multiplier #(.mode("twosComplement"), .width(32)) multiplier_1 (
    .a(in1), .b(in2), .out(multiplier_1_out), .cin(carry), .cout(multiplier_1_cout));
  Divider #(.mode("twosComplement"), .width(32)) divider_1 (
    .a(in1), .b(in2), .out(divider_1_out), .upper(carry), .rem(divider_1_rem));
  Adder #(.width(32)) adder_2 (.a(in1), .b({32{1'b0}}), .out(adder_2_out), .cin(1'b1), .cout(adder_2_cout[0]));
  Subtractor #(.width(32)) subtractor_2 (
    .a(in1), .b({32{1'b0}}), .out(subtractor_2_out), .bin(1'b1), .bout(subtractor_2_bout[0]));
  FPAdder fpadder_1 (.a(in1), .b(in2), .out(fpadder_1_out));
  FPSubtractor fpsubtractor_1 (.a(in1), .b(in2), .out(fpsubtractor_1_out));
  FPMultiplier fpmultiplier_1 (.a(in1), .b(in2), .out(fpmultiplier_1_out));
  FPDivider fpdivider_1 (.a(in1), .b(in2), .out(fpdivider_1_out));
  // FPToInt #(.mode("truncate")) fptoint_1: pin names not known; wires that end beside it: in1, fptoint_1_p2
  // IntToFP #(.width(32)) inttofp_1: pin names not known; wires that end beside it: in1, inttofp_1_p2
  // FPToInt #(.mode("ceil")) fptoint_2: pin names not known; wires that end beside it: in1, fptoint_2_p2
  // FPToInt fptoint_3: pin names not known; wires that end beside it: in1, fptoint_3_p2
  Multiplexer #(.select(3), .width(32)) multiplexer_1 (
    .in0(fpadder_1_out), .in1(fpsubtractor_1_out), .in2(fpmultiplier_1_out), .in3(fpdivider_1_out),
    .in4({{24{1'b0}}, fptoint_1_p2}), .in5(inttofp_1_p2), .in6({{24{1'b0}}, fptoint_2_p2}),
    .in7({{24{1'b0}}, fptoint_3_p2}), .out(multiplexer_1_out), .sel(instruction[2:0]));
  Multiplexer #(.select(3), .width(32)) multiplexer_2 (
    .in0(adder_1_out), .in1(adder_1_out), .in2(subtractor_1_out), .in3(subtractor_1_out),
    .in4(multiplier_1_out), .in5(divider_1_out), .in6(adder_2_out), .in7(subtractor_2_out),
    .out(multiplexer_2_out), .sel(instruction[2:0]));
  Multiplexer #(.select(3), .width(32)) multiplexer_3 (
    .in0({{31{1'b0}}, adder_1_cout[0]}), .in1({{31{1'b0}}, adder_1_cout[0]}),
    .in2({{31{1'b0}}, subtractor_1_bout[0]}), .in3({{31{1'b0}}, subtractor_1_bout[0]}),
    .in4(multiplier_1_cout), .in5(divider_1_rem), .in6({{31{1'b0}}, adder_2_cout[0]}),
    .in7({{31{1'b0}}, subtractor_2_bout[0]}), .out(multiplexer_3_out), .sel(instruction[2:0]));
  Multiplexer #(.width(32)) multiplexer_4 (
    .in0(multiplexer_2_out), .in1(multiplexer_1_out), .out(output_0), .sel(instructionbit9));
  Multiplexer #(.width(32)) multiplexer_5 (
    .in0(multiplexer_3_out), .in1({32{1'b0}}), .out(carryo), .sel(instructionbit9));
endmodule

module shift (
  input  cl,
  input  [31:0] in0,
  input  [31:0] in1,
  input  [31:0] carry,
  input  [7:0] instruction,
  input  pushoverwrite,
  input  popoverwrite,
  output [31:0] outputt,
  output [31:0] carryo,
  output [31:0] stackeeh
);

  wire and_1_out, comparator_1_eq, comparator_2_eq, comparator_3_eq, or_1_out, or_2_out;
  wire [5:0] adder_1_out, adder_2_out, not_1_out, not_2_out;
  wire [31:0] adder_3_out, multiplexer_1_out, multiplexer_2_out, multiplexer_3_out, multiplexer_4_out,
       pull_resistor_1_node, shifter_5_out, shifter_6_out;
  wire [63:0] shifter_1_out, shifter_2_out, shifter_3_out, shifter_4_out;

  Pull_Resistor pull_resistor_1 (.node(pull_resistor_1_node));
  assign pull_resistor_1_node = instruction[0] ? carry : 32'bz;  // Controlled_Buffer controlled_buffer_1
  and and_1 (and_1_out, ~instruction[0], instruction[1], instruction[2]);  // AND_Gate
  Comparator #(.width(4)) comparator_1 (.a(instruction[3:0]), .b(4'b1111), .eq(comparator_1_eq));  // open: gt, lt
  Comparator #(.width(7)) comparator_2 (.a(instruction[6:0]), .b(7'b0111111), .eq(comparator_2_eq));  // open: gt, lt
  Comparator #(.width(7)) comparator_3 (.a(instruction[6:0]), .b(7'b0011111), .eq(comparator_3_eq));  // open: gt, lt
  Shifter #(.width(64)) shifter_1 (.in({in0, pull_resistor_1_node}), .\dist (in1[5:0]), .out(shifter_1_out));
  assign not_1_out = ~in1[5:0];  // NOT_Gate not_1, 6 bits wide
  Adder #(.width(6)) adder_1 (.a(not_1_out), .b(6'b000001), .out(adder_1_out));  // open: cin, cout
  Shifter #(.shift("lr"), .width(64)) shifter_2 (
    .in({pull_resistor_1_node, in0}), .\dist (in1[5:0]), .out(shifter_2_out));
  assign not_2_out = ~in1[5:0];  // NOT_Gate not_2, 6 bits wide
  Adder #(.width(6)) adder_2 (.a(not_2_out), .b(6'b001000), .out(adder_2_out));  // open: cin, cout
  or or_1 (or_1_out, comparator_2_eq, popoverwrite);
  or or_2 (or_2_out, comparator_3_eq, pushoverwrite);
  Shifter #(.shift("lr"), .width(64)) shifter_3 (.in({in0, {32{1'b0}}}), .\dist (adder_1_out), .out(shifter_3_out));
  Shifter #(.width(64)) shifter_4 (.in({in0, {32{1'b0}}}), .\dist (adder_2_out), .out(shifter_4_out));
  Shifter #(.shift("rl"), .width(32)) shifter_5 (.in(in0), .\dist (in1[4:0]), .out(shifter_5_out));
  Shifter #(.shift("rr"), .width(32)) shifter_6 (.in(in0), .\dist (in1[4:0]), .out(shifter_6_out));
  Adder #(.width(32)) adder_3 (.a({32{1'b0}}), .b(in0), .out(adder_3_out), .cin(pushoverwrite));  // open: cout
  Multiplexer #(.width(32)) multiplexer_1 (
    .in0(shifter_5_out), .in1(shifter_6_out), .out(multiplexer_1_out), .sel(instruction[0]));
  stack stack_1 (.cl(cl), .in_2(adder_3_out), .pop(or_1_out), .push(or_2_out), .out_6(stackeeh));  // open: in_3
  Multiplexer #(.width(32)) multiplexer_2 (
    .in0(shifter_1_out[63:32]), .in1(shifter_2_out[31:0]), .out(multiplexer_2_out), .sel(instruction[1]));
  Multiplexer #(.width(32)) multiplexer_3 (
    .in0(multiplexer_2_out), .in1(multiplexer_1_out), .out(multiplexer_3_out), .sel(instruction[2]));
  Multiplexer #(.width(32)) multiplexer_4 (
    .in0(multiplexer_3_out), .in1(stackeeh), .out(multiplexer_4_out), .sel(comparator_1_eq));
  Multiplexer #(.width(32)) multiplexer_5 (
    .in0(multiplexer_4_out), .in1({in1[15:0], in0[15:0]}), .out(outputt), .sel(and_1_out));
  Multiplexer #(.width(32)) multiplexer_6 (
    .in0(shifter_3_out[31:0]), .in1(shifter_4_out[31:0]), .out(carryo), .sel(instruction[1]));
endmodule

module comparison (
  input  [7:0] instruction,
  input  [31:0] in0,
  input  [31:0] in1,
  input  instructionbit8,
  input  instructionbit9,
  input  instructionbit11,
  input  interrrupt,
  output y_n
);

  wire and_1_out, and_2_out, and_3_out, and_4_out, and_5_out, and_6_out, and_7_out, and_8_out, and_9_out,
       and_10_out, comparator_1_eq, comparator_1_gt, comparator_1_lt, comparator_2_eq, comparator_2_gt,
       comparator_2_lt, fpcomparator_1_p3, fpcomparator_1_p4, fpcomparator_1_p5, multiplexer_1_out,
       multiplexer_2_out, or_1_out, or_2_out, or_3_out;

  Comparator #(.width(32)) comparator_1 (
    .a(in0), .b(in1), .gt(comparator_1_gt), .eq(comparator_1_eq), .lt(comparator_1_lt));
  Comparator #(.mode("unsigned"), .width(32)) comparator_2 (
    .a(in0), .b(in1), .gt(comparator_2_gt), .eq(comparator_2_eq), .lt(comparator_2_lt));
  // FPComparator fpcomparator_1: pin names not known; wires that end beside it: in0, in1, fpcomparator_1_p3, fpcomparator_1_p4, fpcomparator_1_p5
  and and_1 (and_1_out, instruction[0], comparator_1_gt);
  and and_2 (and_2_out, instruction[1], comparator_1_eq);
  and and_3 (and_3_out, instruction[2], comparator_1_lt);
  and and_4 (and_4_out, instruction[0], comparator_2_gt);
  and and_5 (and_5_out, instruction[1], comparator_2_eq);
  and and_6 (and_6_out, instruction[2], comparator_2_lt);
  and and_7 (and_7_out, instruction[0], fpcomparator_1_p3);
  and and_8 (and_8_out, instruction[1], fpcomparator_1_p4);
  and and_9 (and_9_out, instruction[2], fpcomparator_1_p5);
  or or_1 (or_1_out, and_1_out, and_2_out, and_3_out);
  or or_2 (or_2_out, and_4_out, and_5_out, and_6_out);
  or or_3 (or_3_out, and_7_out, and_8_out, and_9_out);
  Multiplexer multiplexer_1 (.in0(or_1_out), .in1(or_2_out), .out(multiplexer_1_out), .sel(instructionbit8));
  Multiplexer multiplexer_2 (.in0(multiplexer_1_out), .in1(or_3_out), .out(multiplexer_2_out), .sel(instructionbit9));
  and and_10 (and_10_out, multiplexer_2_out, interrrupt);
  Multiplexer multiplexer_3 (.in0(multiplexer_2_out), .in1(and_10_out), .out(y_n), .sel(instructionbit11));
endmodule

module beeldscherm (
  input  [3:0] in_1,
  input  [3:0] in_2
);

  wire rgb_video_1_p1, rgb_video_1_p3, rgb_video_2_p1, undriven_2;
  wire [5:0] register_1_q;
  wire [7:0] register_2_q, rgb_video_2_p4, undriven;
  wire [15:0] rgb_video_1_p2, rgb_video_1_p4;

  Register #(.trigger("high"), .width(6)) register_1 (
    .D(rgb_video_1_p2[5:0]), .en(1'b1), .Q(register_1_q), .clk(rgb_video_1_p1));  // open: clr
  // RGB_Video #(.cursor("No Cursor"), .height(64), .width(64)) rgb_video_1: pin names not known; wires that end beside it: rgb_video_1_p1, rgb_video_1_p2, rgb_video_1_p3, rgb_video_1_p4, 1'b1, rgb_video_1_p3, rgb_video_1_p3, register_1_q, rgb_video_1_p4[5:0], in_1
  Register #(.trigger("high")) register_2 (.D(undriven), .en(1'b1), .Q(register_2_q), .clk(undriven_2));  // open: clr
  // RGB_Video #(.height(256), .width(256)) rgb_video_2: pin names not known; wires that end beside it: rgb_video_2_p1, rgb_video_2_p1, register_2_q, rgb_video_2_p4, in_2
endmodule

module test (
  output [31:0] out_1,
  output [31:0] out_2
);

  wire clock_1_out;
  wire [31:0] counter_1_q;

  Clock clock_1 (.out(clock_1_out));
  Counter #(.max('hffffffff), .width(32)) counter_1 (
    .count(clock_1_out), .Q(counter_1_q), .up(clock_1_out), .clk(clock_1_out));  // open: load, D, carry, clr
  ALUv2 aluv2_1 (
    .in0(counter_1_q), .in1(counter_1_q), .carry(counter_1_q), .instruction(counter_1_q[7:0]),
    .innstructionbit9(counter_1_q[0]), .outputt(out_1), .carry0(out_2));  // open: cl, pushoverwrite, popoverwrite, stackeeh
endmodule

module addsub (
  input  subtract,
  input  carry_in,
  input  [7:0] a,
  input  [7:0] b,
  output [7:0] sum,
  output carry
);

  wire full_adder_1_carry, full_adder_2_carry, full_adder_3_carry, full_adder_4_carry, full_adder_5_carry,
       full_adder_6_carry, full_adder_7_carry, xor_1_out, xor_2_out, xor_3_out, xor_4_out, xor_5_out,
       xor_6_out, xor_7_out, xor_8_out;

  xor xor_1 (xor_1_out, subtract, a[1]);
  xor xor_2 (xor_2_out, subtract, a[2]);
  xor xor_3 (xor_3_out, subtract, a[3]);
  xor xor_4 (xor_4_out, a[4], subtract);
  xor xor_5 (xor_5_out, a[5], subtract);
  xor xor_6 (xor_6_out, a[6], subtract);
  xor xor_7 (xor_7_out, a[7], subtract);
  xor xor_8 (xor_8_out, subtract, carry_in);
  Full_adder full_adder_1 (.carry_in(xor_8_out), .a(a[0]), .b(b[0]), .sum(sum[0]), .carry(full_adder_1_carry));
  Full_adder full_adder_2 (
    .carry_in(full_adder_1_carry), .a(xor_1_out), .b(b[1]), .sum(sum[1]), .carry(full_adder_2_carry));
  Full_adder full_adder_3 (
    .carry_in(full_adder_2_carry), .a(xor_2_out), .b(b[2]), .sum(sum[2]), .carry(full_adder_3_carry));
  Full_adder full_adder_4 (
    .carry_in(full_adder_3_carry), .a(xor_3_out), .b(b[3]), .sum(sum[3]), .carry(full_adder_4_carry));
  Full_adder full_adder_5 (
    .carry_in(full_adder_4_carry), .a(xor_4_out), .b(b[4]), .sum(sum[4]), .carry(full_adder_5_carry));
  Full_adder full_adder_6 (
    .carry_in(full_adder_5_carry), .a(xor_5_out), .b(b[5]), .sum(sum[5]), .carry(full_adder_6_carry));
  Full_adder full_adder_7 (
    .carry_in(full_adder_6_carry), .a(xor_6_out), .b(b[6]), .sum(sum[6]), .carry(full_adder_7_carry));
  Full_adder full_adder_8 (.carry_in(full_adder_7_carry), .a(xor_7_out), .b(b[7]), .sum(sum[7]), .carry(carry));
endmodule
