// Logisim project Voorbeelden.circ as structural Verilog
module LogicGates (
  input  in_1,
  input  in_2,
  output out_3,
  output out_4,
  output out_5,
  output out_6,
  output out_7,
  output out_8,
  output out_9,
  output out_10
);

  assign out_10 = in_2 ? in_1 : 1'bz;  // Controlled_Buffer controlled_buffer_1
  and and_1 (out_3, in_1, in_2);
  nand nand_1 (out_4, in_1, in_2);
  or or_1 (out_5, in_1, in_2);
  nor nor_1 (out_6, in_1, in_2);
  xor xor_1 (out_7, in_1, in_2);
  xnor xnor_1 (out_8, in_1, in_2);
  not not_1 (out_9, in_1);
endmodule

module multiplex (
  input  a,
  input  b,
  input  selector,
  input  in_4,
  input  in_5,
  input  in_6,
  output out_7,
  output out_8
);

  wire and_1_out, and_2_out, not_1_out;

  not not_1 (not_1_out, selector);
  and and_1 (and_1_out, a, not_1_out);
  and and_2 (and_2_out, b, selector);
  Multiplexer multiplexer_1 (.in0(in_4), .in1(in_5), .out(out_8), .sel(in_6));
  or or_1 (out_7, and_1_out, and_2_out);
endmodule

module demultiplex (
  input  a,
  input  selector,
  input  in_3,
  input  in_4,
  output out_5,
  output out_6,
  output out_7,
  output out_8
);

  wire not_1_out;

  not not_1 (not_1_out, selector);
  Demultiplexer demultiplexer_1 (.out0(out_7), .out1(out_8), .in(in_3), .sel(in_4));
  and and_1 (out_5, a, not_1_out);
  and and_2 (out_6, a, selector);
endmodule

// add
module half_adder (
  input  a,
  input  b,
  output sum,
  output carry
);

  xor xor_1 (sum, a, b);
  and and_1 (carry, a, b);
endmodule

// add
module Full_adder (
  input  carry_in,
  input  a,
  input  b,
  output sum,
  output carry
);

  wire and_1_out, and_2_out, or_1_out, xor_1_out;

  xor xor_1 (xor_1_out, a, b);
  or or_1 (or_1_out, b, a);
  xor xor_2 (sum, carry_in, xor_1_out);
  and and_1 (and_1_out, carry_in, or_1_out);
  and and_2 (and_2_out, b, a);
  or or_2 (carry, and_1_out, and_2_out);
endmodule

// +
module byte_adder (
  input  carry_in,
  input  [7:0] a,
  input  [7:0] b,
  output [7:0] out_4,
  output carry
);

  wire full_adder_1_carry, full_adder_2_carry, full_adder_3_carry, full_adder_4_carry, full_adder_5_carry,
       full_adder_6_carry, full_adder_7_carry;

  Full_adder full_adder_1 (.carry_in(carry_in), .a(a[0]), .b(b[0]), .sum(out_4[0]), .carry(full_adder_1_carry));
  Full_adder full_adder_2 (
    .carry_in(full_adder_1_carry), .a(a[1]), .b(b[1]), .sum(out_4[1]), .carry(full_adder_2_carry));
  Full_adder full_adder_3 (
    .carry_in(full_adder_2_carry), .a(a[2]), .b(b[2]), .sum(out_4[2]), .carry(full_adder_3_carry));
  Full_adder full_adder_4 (
    .carry_in(full_adder_3_carry), .a(a[3]), .b(b[3]), .sum(out_4[3]), .carry(full_adder_4_carry));
  Full_adder full_adder_5 (
    .carry_in(full_adder_4_carry), .a(a[4]), .b(b[4]), .sum(out_4[4]), .carry(full_adder_5_carry));
  Full_adder full_adder_6 (
    .carry_in(full_adder_5_carry), .a(a[5]), .b(b[5]), .sum(out_4[5]), .carry(full_adder_6_carry));
  Full_adder full_adder_7 (
    .carry_in(full_adder_6_carry), .a(a[6]), .b(b[6]), .sum(out_4[6]), .carry(full_adder_7_carry));
  Full_adder full_adder_8 (.carry_in(full_adder_7_carry), .a(a[7]), .b(b[7]), .sum(out_4[7]), .carry(carry));
endmodule

// +
module add_sub (
  input  subtract,
  input  carry_in,
  input  [7:0] a,
  input  [7:0] b,
  output [7:0] out_5,
  output carry
);

  wire full_adder_1_carry, full_adder_2_carry, full_adder_3_carry, full_adder_4_carry, full_adder_5_carry,
       full_adder_6_carry, full_adder_7_carry, xor_1_out, xor_2_out, xor_3_out, xor_4_out, xor_5_out,
       xor_6_out, xor_7_out, xor_8_out;

  xor xor_1 (xor_1_out, subtract, a[4]);
  xor xor_2 (xor_2_out, subtract, a[5]);
  xor xor_3 (xor_3_out, subtract, a[6]);
  xor xor_4 (xor_4_out, subtract, a[7]);
  xor xor_5 (xor_5_out, subtract, a[0]);
  xor xor_6 (xor_6_out, subtract, a[1]);
  xor xor_7 (xor_7_out, subtract, a[2]);
  xor xor_8 (xor_8_out, subtract, a[3]);
  Full_adder full_adder_1 (.carry_in(carry_in), .a(xor_5_out), .b(b[0]), .sum(out_5[0]), .carry(full_adder_1_carry));
  Full_adder full_adder_2 (
    .carry_in(full_adder_1_carry), .a(xor_6_out), .b(b[1]), .sum(out_5[1]), .carry(full_adder_2_carry));
  Full_adder full_adder_3 (
    .carry_in(full_adder_2_carry), .a(xor_7_out), .b(b[2]), .sum(out_5[2]), .carry(full_adder_3_carry));
  Full_adder full_adder_4 (
    .carry_in(full_adder_3_carry), .a(xor_8_out), .b(b[3]), .sum(out_5[3]), .carry(full_adder_4_carry));
  Full_adder full_adder_5 (
    .carry_in(full_adder_4_carry), .a(xor_1_out), .b(b[4]), .sum(out_5[4]), .carry(full_adder_5_carry));
  Full_adder full_adder_6 (
    .carry_in(full_adder_5_carry), .a(xor_2_out), .b(b[5]), .sum(out_5[5]), .carry(full_adder_6_carry));
  Full_adder full_adder_7 (
    .carry_in(full_adder_6_carry), .a(xor_3_out), .b(b[6]), .sum(out_5[6]), .carry(full_adder_7_carry));
  Full_adder full_adder_8 (.carry_in(full_adder_7_carry), .a(xor_4_out), .b(b[7]), .sum(out_5[7]), .carry(carry));
endmodule

module mult (
  input  [3:0] in_1,
  input  [3:0] in_2,
  output out_3,
  output out_4,
  output out_5,
  output out_6,
  output out_7,
  output out_8,
  output out_9,
  output out_10
);

  wire and_2_out, and_3_out, and_4_out, and_5_out, and_6_out, and_7_out, and_8_out, and_9_out, and_10_out,
       and_11_out, and_12_out, and_13_out, and_14_out, and_15_out, and_16_out, fourbit_add_1_out_11,
       fourbit_add_1_out_12, fourbit_add_1_out_13, fourbit_add_1_out_14, fourbit_add_2_out_11,
       fourbit_add_2_out_12, fourbit_add_2_out_13, fourbit_add_2_out_14;

  and and_1 (out_3, in_1[0], in_2[0]);
  and and_2 (and_2_out, in_1[1], in_2[0]);
  and and_3 (and_3_out, in_1[2], in_2[0]);
  and and_4 (and_4_out, in_1[3], in_2[0]);
  and and_5 (and_5_out, in_1[0], in_2[1]);
  and and_6 (and_6_out, in_1[1], in_2[1]);
  and and_7 (and_7_out, in_1[2], in_2[1]);
  and and_8 (and_8_out, in_1[3], in_2[1]);
  and and_9 (and_9_out, in_1[0], in_2[2]);
  and and_10 (and_10_out, in_1[1], in_2[2]);
  and and_11 (and_11_out, in_1[2], in_2[2]);
  and and_12 (and_12_out, in_1[3], in_2[2]);
  and and_13 (and_13_out, in_1[0], in_2[3]);
  and and_14 (and_14_out, in_1[1], in_2[3]);
  and and_15 (and_15_out, in_1[2], in_2[3]);
  and and_16 (and_16_out, in_1[3], in_2[3]);
  fourbit_add fourbit_add_1 (
    .in_1(and_2_out), .in_3(and_3_out), .in_4(and_4_out), .in_5(1'b0), .in_6(and_5_out), .in_7(and_6_out),
    .in_8(and_7_out), .in_9(and_8_out), .out_14(fourbit_add_1_out_14), .out_10(out_4),
    .out_11(fourbit_add_1_out_11), .out_12(fourbit_add_1_out_12), .out_13(fourbit_add_1_out_13));  // open: in_2
  fourbit_add fourbit_add_2 (
    .in_1(fourbit_add_1_out_11), .in_3(fourbit_add_1_out_12), .in_4(fourbit_add_1_out_13),
    .in_5(fourbit_add_1_out_14), .in_6(and_9_out), .in_7(and_10_out), .in_8(and_11_out), .in_9(and_12_out),
    .out_14(fourbit_add_2_out_14), .out_10(out_5), .out_11(fourbit_add_2_out_11),
    .out_12(fourbit_add_2_out_12), .out_13(fourbit_add_2_out_13));  // open: in_2
  fourbit_add fourbit_add_3 (
    .in_1(fourbit_add_2_out_11), .in_3(fourbit_add_2_out_12), .in_4(fourbit_add_2_out_13),
    .in_5(fourbit_add_2_out_14), .in_6(and_13_out), .in_7(and_14_out), .in_8(and_15_out), .in_9(and_16_out),
    .out_14(out_10), .out_10(out_6), .out_11(out_7), .out_12(out_8), .out_13(out_9));  // open: in_2
endmodule

module vergelijken (
  input  [3:0] a,
  input  [3:0] b,
  output bigger,
  output equal,
  output smaller
);

  wire bitfinder_1_found, bitselector_1_out;
  wire [1:0] bitfinder_1_index;
  wire [3:0] xor_1_out;

  xor xor_1 (xor_1_out[0], a[0], b[0]);
  xor xor_2 (xor_1_out[1], a[1], b[1]);
  xor xor_3 (xor_1_out[2], a[2], b[2]);
  xor xor_4 (xor_1_out[3], a[3], b[3]);
  BitFinder #(.\type ("high1"), .width(4)) bitfinder_1 (
    .in(xor_1_out), .index(bitfinder_1_index), .found(bitfinder_1_found));
  BitSelector #(.width(4)) bitselector_1 (.in(a), .out(bitselector_1_out), .sel(bitfinder_1_index));
  and and_1 (bigger, bitselector_1_out, bitfinder_1_found);
  not not_1 (equal, bitfinder_1_found);
  nor nor_1 (smaller, bigger, equal);
endmodule

module SR_flipflop (
  input  set,
  input  reset,
  output Q
);

  wire nand_1_out;

  nand nand_1 (nand_1_out, set, Q);
  nand nand_2 (Q, nand_1_out, reset);
endmodule

module gated_SR_flipflop (
  input  reset,
  input  clk,
  input  set,
  output Q
);

  wire nand_1_out, nand_2_out;

  nand nand_1 (nand_1_out, reset, clk);
  nand nand_2 (nand_2_out, clk, set);
  SR_flipflop SR (.set(nand_1_out), .reset(nand_2_out), .Q(Q));
endmodule

module bit_mem (
  input  save,
  input  clk,
  input  value,
  output out_4
);

  wire and_1_out, and_2_out;

  and and_1 (and_1_out, save, ~value);  // AND_Gate
  and and_2 (and_2_out, save, value);
  gated_SR_flipflop Gated_SR (.reset(and_1_out), .clk(clk), .set(and_2_out), .Q(out_4));
endmodule

module Four_bit_register (
  input  save,
  input  clk,
  input  [3:0] value,
  output [3:0] out_4
);

  bit_mem bit_mem_1 (.save(save), .clk(clk), .value(value[0]), .out_4(out_4[0]));
  bit_mem bit_mem_2 (.save(save), .clk(clk), .value(value[1]), .out_4(out_4[1]));
  bit_mem bit_mem_3 (.save(save), .clk(clk), .value(value[2]), .out_4(out_4[2]));
  bit_mem bit_mem_4 (.save(save), .clk(clk), .value(value[3]), .out_4(out_4[3]));
endmodule

module Four_BYTE_RAM (
  input  [7:0] value,
  input  clk,
  input  enable,
  input  [1:0] select2,
  output [7:0] out_5,
  output [7:0] out_6,
  output [7:0] out_7,
  output [7:0] out_8
);

  wire decoder_1_out0, decoder_1_out1, decoder_1_out2, decoder_1_out3;

  Decoder #(.select(2)) decoder_1 (
    .out0(decoder_1_out0), .out1(decoder_1_out1), .out2(decoder_1_out2), .out3(decoder_1_out3),
    .sel(select2), .en(enable));
  Register register_1 (.D(value), .en(decoder_1_out0), .clk(clk), .Q(out_5));  // open: clr
  Register register_2 (.D(value), .en(decoder_1_out1), .clk(clk), .Q(out_6));  // open: clr
  Register register_3 (.D(value), .en(decoder_1_out2), .clk(clk), .Q(out_7));  // open: clr
  Register register_4 (.D(value), .en(decoder_1_out3), .clk(clk), .Q(out_8));  // open: clr
endmodule

// inc
module increment (
  input  [7:0] value,
  output [7:0] o,
  output carry
);

  byte_adder byte_adder_1 (.carry_in(1'b1), .a(value), .b({8{1'b0}}), .out_4(o), .carry(carry));
endmodule

module count (
  input  clk,
  input  overwrite,
  input  [7:0] value,
  output [7:0] out_4
);

  wire [7:0] increment_1_o, multiplexer_1_out;

  Multiplexer #(.width(8)) multiplexer_1 (.in0(increment_1_o), .in1(value), .out(multiplexer_1_out), .sel(overwrite));
  Register register_1 (.D(multiplexer_1_out), .en(1'b1), .Q(out_4), .clk(clk));  // open: clr
  increment increment_1 (.value(out_4), .o(increment_1_o));  // open: carry
endmodule

module stack (
  input  in_1,
  input  pop,
  input  push,
  input  clk,
  input  [7:0] value,
  output [7:0] out_6
);

  wire and_1_out, or_1_out;
  wire [7:0] counter_1_q;

  or or_1 (or_1_out, pop, push);
  Counter counter_1 (.count(or_1_out), .Q(counter_1_q), .up(push), .clk(clk), .clr(in_1));  // open: load, D, carry
  and and_1 (and_1_out, clk, push);
  RAM #(.clearpin("true"), .enables("line")) ram_1 (
    .addr(counter_1_q), .we(and_1_out), .clk(and_1_out), .din(value), .dout(out_6), .clr(in_1));
endmodule

module fourbit_add (
  input  in_1,
  input  in_2,
  input  in_3,
  input  in_4,
  input  in_5,
  input  in_6,
  input  in_7,
  input  in_8,
  input  in_9,
  output out_10,
  output out_11,
  output out_12,
  output out_13,
  output out_14
);

  wire full_adder_1_carry, full_adder_2_carry, full_adder_3_carry;

  Full_adder full_adder_1 (.carry_in(in_2), .a(in_1), .b(in_6), .sum(out_10), .carry(full_adder_1_carry));
  Full_adder full_adder_2 (.carry_in(full_adder_1_carry), .a(in_3), .b(in_7), .sum(out_11), .carry(full_adder_2_carry));
  Full_adder full_adder_3 (.carry_in(full_adder_2_carry), .a(in_4), .b(in_8), .sum(out_12), .carry(full_adder_3_carry));
  Full_adder full_adder_4 (.carry_in(full_adder_3_carry), .a(in_5), .b(in_9), .sum(out_13), .carry(out_14));
endmodule
