// Logisim project stack.circ as structural Verilog: 1 circuit, main circuit stack
module stack (
  input  cl,
  input  [31:0] in_2,
  input  in_3,
  input  pop,
  input  push,
  output [31:0] out_6
);

  wire and_1_out, not_1_out, or_1_out;
  wire [7:0] counter_1_q;

  or or_1 (or_1_out, pop, push);
  Counter counter_1 (.count(or_1_out), .Q(counter_1_q), .up(push), .clk(cl), .clr(in_3));  // open: load, D, carry
  and and_1 (and_1_out, cl, push);
  RAM #(.clearpin("true"), .dataWidth(32), .enables("line"), .trigger("falling")) ram_1 (
    .addr(counter_1_q), .we(and_1_out), .clk(not_1_out), .din(in_2), .dout(out_6), .clr(in_3));
  not not_1 (not_1_out, and_1_out);
endmodule
